// Logisim project 5-stage-cpu-redirect.circ as structural Verilog: 9 circuits, main circuit main
module main (
  input  Rst
);

  wire alu_1_equal, and_1_out, and_2_out, branch_1_pcsrc, Clk, ComClk, comparator_1_eq, control_1_aluysrc2,
       control_1_dmwe, control_1_load, control_1_pcaddsrc, control_1_rfr1src, control_1_rfwe,
       control_1_syscall, datahzd_1_nop, datahzd_1_stop, ex_mem_1_dispdout, ex_mem_1_dmwedout,
       ex_mem_1_haltdout, ex_mem_1_rfwedout, Halt, id_ex_1_aluysrc2dout, id_ex_1_dmwedout, id_ex_1_loaddout,
       id_ex_1_pcaddsrcdout, id_ex_1_rfwedout, id_ex_1_syscalldout, main_1_p5, mem_wb_1_dispdout, not_1_out,
       not_2_out, or_1_out;
  wire [1:0] branch_1_brpcsrc, control_1_aluysrc, control_1_rfdinsrc, control_1_rfrwsrc, datahzd_1_rdtr1src,
       datahzd_1_rdtr2src, ex_mem_1_rfdinsrcdout, id_ex_1_aluysrcdout, id_ex_1_rdtr1srcdout,
       id_ex_1_rdtr2srcdout, id_ex_1_rfdinsrcdout, mem_wb_1_rfdinsrcdout;
  wire [3:0] control_1_aluop, Disp_q, Disp_q_2, Disp_q_3, Disp_q_4, Disp_q_5, Disp_q_6, Disp_q_7, Disp_q_8,
       id_ex_1_aluopdout;
  wire [4:0] ex_mem_1_wregdout, id_ex_1_wregdout, insanalyse_1_rd, insanalyse_1_rs, insanalyse_1_rt,
       insanalyse_1_shamt, main_1_p3, multiplexer_3_out, multiplexer_4_out, multiplexer_5_out;
  wire [5:0] control_1_brins, id_ex_1_brinsdout, insanalyse_1_funct, insanalyse_1_op;
  wire [15:0] insanalyse_1_immediate16;
  wire [25:0] insanalyse_1_immediate26;
  wire [31:0] adder_1_out, adder_2_out, adder_3_out, adder_4_out, adder_5_out, alu_1_result,
       bit_extender_1_out, bit_extender_2_out, bit_extender_3_out, bit_extender_4_out, bit_extender_5_out,
       control_1_allins, counter_1_q, ex_mem_1_a0dout, ex_mem_1_aludout, ex_mem_1_irdout, ex_mem_1_pcadddout,
       ex_mem_1_pcdout, ex_mem_1_rfr2dout, id_ex_1_a0dout, id_ex_1_ext5to32dout, id_ex_1_ext16to32dout,
       id_ex_1_irdout, id_ex_1_pc_1dout, id_ex_1_pcdout, id_ex_1_rfr1dout, id_ex_1_rfr2dout,
       id_ex_1_sext16to32dout, id_ex_1_sext26to32dout, id_ex_1_v0dout, if_id_1_irdout, if_id_1_pc_1dout,
       if_id_1_pcdout, main_1_p4, main_1_p6, main_1_p7, main_1_p9, main_1_p10, mem_wb_1_a0dout,
       mem_wb_1_aludout, mem_wb_1_dmdout, mem_wb_1_irdout, mem_wb_1_pcadddout, mem_wb_1_sext16to32dout,
       multiplexer_1_out, multiplexer_2_out, multiplexer_6_out, multiplexer_7_out, multiplexer_8_out,
       multiplexer_9_out, multiplexer_10_out, multiplexer_11_out, multiplexer_12_out, multiplexer_13_out,
       multiplexer_14_out, multiplexer_15_out, multiplexer_16_out, PC_q, ram_1_data, register_1_q,
       register_2_q, rom_1_data;

  Multiplexer #(.width(32), .enable("false")) multiplexer_1 (
    .in0(adder_1_out), .in1(multiplexer_14_out), .out(multiplexer_1_out), .sel(branch_1_pcsrc));
  Hex_Digit_Display hex_digit_display_1 (.value(Disp_q_8), .dp(1'b0));
  Register #(.width(32)) PC (.D(multiplexer_1_out), .en(datahzd_1_stop), .Q(PC_q), .clk(Clk));  // open: clr
  Hex_Digit_Display hex_digit_display_2 (.value(Disp_q_6), .dp(1'b0));
  Hex_Digit_Display hex_digit_display_3 (.value(Disp_q_7), .dp(1'b0));
  Multiplexer #(.width(32), .enable("false")) multiplexer_2 (
    .in0(adder_2_out), .in1(register_1_q), .out(multiplexer_2_out), .sel(datahzd_1_stop));
  Adder #(.width(32)) adder_1 (.a(32'h1), .b(PC_q), .out(adder_1_out));  // open: cin, cout
  Hex_Digit_Display hex_digit_display_4 (.value(Disp_q_5), .dp(1'b0));
  Hex_Digit_Display hex_digit_display_5 (.value(Disp_q_4), .dp(1'b0));
  Register #(.width(32), .trigger("high")) Disp (
    .D(mem_wb_1_a0dout), .en(1'b1),
    .Q({Disp_q_8, Disp_q_7, Disp_q_6, Disp_q_5, Disp_q_4, Disp_q_3, Disp_q_2, Disp_q}),
    .clk(mem_wb_1_dispdout), .clr(1'b0));
  Clock clock_1 (.out(ComClk));
  // Probe on register_1_q
  Register #(.width(32)) register_1 (.D(multiplexer_2_out), .Q(register_1_q), .clk(Clk));  // open: en, clr
  Hex_Digit_Display hex_digit_display_6 (.value(Disp_q_3), .dp(1'b0));
  Hex_Digit_Display hex_digit_display_7 (.value(Disp_q_2), .dp(1'b0));
  Adder #(.width(32)) adder_2 (.a(32'h1), .b(register_1_q), .out(adder_2_out));  // open: cin, cout
  ROM #(.addrWidth(10), .dataWidth(32)) rom_1 (.addr(PC_q[9:0]), .data(rom_1_data), .sel(1'b1));
  Hex_Digit_Display hex_digit_display_8 (.value(Disp_q), .dp(1'b0));
  IF_ID if_id_1 (
    .PCDin(PC_q), .IRDin(rom_1_data), .PCDout(if_id_1_pcdout), .IRDout(if_id_1_irdout), .WE(datahzd_1_stop),
    .Clk(Clk), .Rst(branch_1_pcsrc), .PC_1Din(adder_1_out), .PC_1Dout(if_id_1_pc_1dout));
  DataHzd datahzd_1 (
    .EX_WReg(id_ex_1_wregdout), .MEM_WReg(ex_mem_1_wregdout), .AllIns(control_1_allins),
    .EX_WE(id_ex_1_rfwedout), .Rs(insanalyse_1_rs), .Rt(insanalyse_1_rt), .Stop(datahzd_1_stop),
    .Nop(datahzd_1_nop), .MEM_WE(ex_mem_1_rfwedout), .RDTR1Src(datahzd_1_rdtr1src),
    .RDTR2Src(datahzd_1_rdtr2src), .load(id_ex_1_loaddout));
  InsAnalyse insanalyse_1 (
    .Ins(if_id_1_irdout), .OP(insanalyse_1_op), .Rs(insanalyse_1_rs), .Rt(insanalyse_1_rt),
    .Rd(insanalyse_1_rd), .Shamt(insanalyse_1_shamt), .funct(insanalyse_1_funct),
    .Immediate16(insanalyse_1_immediate16), .Immediate26(insanalyse_1_immediate26));
  not not_1 (not_1_out, control_1_rfr1src);
  // Probe on if_id_1_irdout
  Control control_1 (
    .OP(insanalyse_1_op), .funct(insanalyse_1_funct), .PCAddSrc(control_1_pcaddsrc),
    .RFR1Src(control_1_rfr1src), .RFRWSrc(control_1_rfrwsrc), .RFDinSrc(control_1_rfdinsrc),
    .RFWE(control_1_rfwe), .ALUYSrc(control_1_aluysrc), .ALUOP(control_1_aluop), .DMWE(control_1_dmwe),
    .Syscall(control_1_syscall), .ALUYSrc2(control_1_aluysrc2), .BrIns(control_1_brins),
    .AllIns(control_1_allins), .load(control_1_load));
  Multiplexer #(.width(5), .enable("false")) multiplexer_3 (
    .in0(insanalyse_1_rs), .in1(insanalyse_1_rt), .out(multiplexer_3_out), .sel(control_1_rfr1src));
  Multiplexer #(.width(5), .enable("false")) multiplexer_4 (
    .in0(insanalyse_1_rs), .in1(insanalyse_1_rt), .out(multiplexer_4_out), .sel(not_1_out));
  Multiplexer #(.select(2), .width(5), .enable("false")) multiplexer_5 (
    .in0(insanalyse_1_rt), .in1(insanalyse_1_rd), .in2({5{1'b1}}), .out(multiplexer_5_out),
    .sel(control_1_rfrwsrc));  // open: in3
  Counter #(.width(32), .max('hffffffff)) counter_1 (.Q(counter_1_q), .clk(Clk));  // open: load, D, count, carry, clr
  Multiplexer #(.width(32), .enable("false")) multiplexer_6 (
    .in0({32{1'b0}}), .in1(32'h1), .out(multiplexer_6_out), .sel(Halt));
  // regfile_5_stage_cpu_main main_1: pin names not known; wires that end beside it: multiplexer_3_out, multiplexer_4_out, main_1_p3, main_1_p4, main_1_p5, main_1_p6, main_1_p7, Clk, main_1_p9, main_1_p10
  assign bit_extender_1_out = {{27{1'b0}}, insanalyse_1_shamt};  // Bit_Extender bit_extender_1
  assign bit_extender_2_out = {{16{insanalyse_1_immediate16[15]}}, insanalyse_1_immediate16};  // Bit_Extender bit_extender_2
  assign bit_extender_3_out = {{16{1'b0}}, insanalyse_1_immediate16};  // Bit_Extender bit_extender_3
  assign bit_extender_4_out = {{6{insanalyse_1_immediate26[25]}}, insanalyse_1_immediate26};  // Bit_Extender bit_extender_4
  // Probe on adder_3_out
  Adder #(.width(32)) adder_3 (.a(multiplexer_6_out), .b(counter_1_q), .out(adder_3_out));  // open: cin, cout
  or or_1 (or_1_out, datahzd_1_nop, branch_1_pcsrc);
  ID_EX id_ex_1 (
    .PCDin(if_id_1_pcdout), .IRDin(if_id_1_irdout), .ALUOPDin(control_1_aluop), .PCDout(id_ex_1_pcdout),
    .IRDout(id_ex_1_irdout), .ALUOPDout(id_ex_1_aluopdout), .ALUYSrcDin(control_1_aluysrc),
    .ALUYSrcDout(id_ex_1_aluysrcdout), .ALUYSrc2Din(control_1_aluysrc2), .ALUYSrc2Dout(id_ex_1_aluysrc2dout),
    .Ext5to32Din(bit_extender_1_out), .Ext5to32Dout(id_ex_1_ext5to32dout),
    .SExt16to32Din(bit_extender_2_out), .SExt16to32Dout(id_ex_1_sext16to32dout),
    .Ext16to32Din(bit_extender_3_out), .Ext16to32Dout(id_ex_1_ext16to32dout), .RFR1Din(main_1_p9),
    .RFR1Dout(id_ex_1_rfr1dout), .RFR2Din(main_1_p10), .RFR2Dout(id_ex_1_rfr2dout),
    .PC_1Din(if_id_1_pc_1dout), .PC_1Dout(id_ex_1_pc_1dout), .DMWEDin(control_1_dmwe),
    .DMWEDout(id_ex_1_dmwedout), .PCAddSrcDin(control_1_pcaddsrc), .PCAddSrcDout(id_ex_1_pcaddsrcdout),
    .RFWEDin(control_1_rfwe), .RFWEDout(id_ex_1_rfwedout), .RFDinSrcDin(control_1_rfdinsrc),
    .RFDinSrcDout(id_ex_1_rfdinsrcdout), .SExt26to32Din(bit_extender_4_out),
    .SExt26to32Dout(id_ex_1_sext26to32dout), .BrInsDin(control_1_brins), .BrInsDout(id_ex_1_brinsdout),
    .WRegDin(multiplexer_5_out), .WRegDout(id_ex_1_wregdout), .SyscallDin(control_1_syscall),
    .SyscallDout(id_ex_1_syscalldout), .WE(1'b1), .Clk(Clk), .Rst(or_1_out), .a0Din(main_1_p7),
    .a0Dout(id_ex_1_a0dout), .RDTR1SrcDin(datahzd_1_rdtr1src), .RDTR1SrcDout(id_ex_1_rdtr1srcdout),
    .RDTR2SrcDin(datahzd_1_rdtr2src), .RDTR2SrcDout(id_ex_1_rdtr2srcdout), .loadDin(control_1_load),
    .loadDout(id_ex_1_loaddout), .v0Din(main_1_p6), .v0Dout(id_ex_1_v0dout));
  Multiplexer #(.select(2), .width(32), .enable("false")) multiplexer_7 (
    .in0(id_ex_1_v0dout), .in1(main_1_p4), .in2(multiplexer_16_out), .in3(multiplexer_16_out),
    .out(multiplexer_7_out), .sel(id_ex_1_rdtr1srcdout));
  Multiplexer #(.select(2), .width(32), .enable("false")) multiplexer_8 (
    .in0(id_ex_1_a0dout), .in1(main_1_p4), .in2(multiplexer_16_out), .in3(multiplexer_16_out),
    .out(multiplexer_8_out), .sel(id_ex_1_rdtr2srcdout));
  Multiplexer #(.select(2), .width(32), .enable("false")) multiplexer_9 (
    .in0(id_ex_1_rfr1dout), .in1(main_1_p4), .in2(multiplexer_16_out), .in3(multiplexer_16_out),
    .out(multiplexer_9_out), .sel(id_ex_1_rdtr1srcdout));
  Multiplexer #(.select(2), .width(32), .enable("false")) multiplexer_10 (
    .in0(id_ex_1_rfr2dout), .in1(main_1_p4), .in2(multiplexer_16_out), .in3(multiplexer_16_out),
    .out(multiplexer_10_out), .sel(id_ex_1_rdtr2srcdout));
  // Probe on id_ex_1_irdout
  Comparator #(.width(32), .mode("unsigned")) comparator_1 (
    .a(multiplexer_7_out), .b(32'ha), .eq(comparator_1_eq));  // open: gt, lt
  Multiplexer #(.select(2), .width(32), .enable("false")) multiplexer_11 (
    .in0(multiplexer_10_out), .in1(id_ex_1_ext5to32dout), .in2(id_ex_1_sext16to32dout),
    .in3(id_ex_1_ext16to32dout), .out(multiplexer_11_out), .sel(id_ex_1_aluysrcdout));
  Multiplexer #(.width(32), .disabled(0), .enable("false")) multiplexer_12 (
    .in0(multiplexer_11_out), .in1({32{1'b0}}), .out(multiplexer_12_out), .sel(id_ex_1_aluysrc2dout));
  Multiplexer #(.width(32), .enable("false")) multiplexer_13 (
    .in0({32{1'b0}}), .in1(id_ex_1_sext16to32dout), .out(multiplexer_13_out), .sel(id_ex_1_pcaddsrcdout));
  and and_1 (and_1_out, id_ex_1_syscalldout, comparator_1_eq);
  and and_2 (and_2_out, id_ex_1_syscalldout, ~comparator_1_eq);  // AND_Gate
  Branch branch_1 (
    .Equal(alu_1_equal), .Judge(alu_1_result[0]), .BrIns(id_ex_1_brinsdout), .BrPCSrc(branch_1_brpcsrc),
    .PCSrc(branch_1_pcsrc));
  ALU alu_1 (
    .AluOP(id_ex_1_aluopdout), .X(multiplexer_9_out), .Equal(alu_1_equal), .Result(alu_1_result),
    .Y(multiplexer_12_out));  // open: Signed_Overflow, Result_2, UnSigned_Overflow
  Adder #(.width(32)) adder_4 (
    .a(multiplexer_13_out), .b(id_ex_1_pc_1dout), .out(adder_4_out), .cin(1'b0));  // open: cout
  Multiplexer #(.select(2), .width(32), .enable("false")) multiplexer_14 (
    .in0(multiplexer_9_out), .in1(id_ex_1_pc_1dout), .in2(adder_4_out), .in3(id_ex_1_sext26to32dout),
    .out(multiplexer_14_out), .sel(branch_1_brpcsrc));
  not not_2 (not_2_out, branch_1_pcsrc);
  EX_MEM ex_mem_1 (
    .PCDin(id_ex_1_pcdout), .IRDin(id_ex_1_irdout), .DMWEDin(id_ex_1_dmwedout), .RFWEDin(id_ex_1_rfwedout),
    .RFDinSrcDin(id_ex_1_rfdinsrcdout), .PCDout(ex_mem_1_pcdout), .IRDout(ex_mem_1_irdout),
    .DMWEDout(ex_mem_1_dmwedout), .RFWEDout(ex_mem_1_rfwedout), .RFDinSrcDout(ex_mem_1_rfdinsrcdout),
    .ALUDin(alu_1_result), .ALUDout(ex_mem_1_aludout), .RFR2Din(multiplexer_10_out),
    .RFR2Dout(ex_mem_1_rfr2dout), .PCAddDin(adder_4_out), .PCAddDout(ex_mem_1_pcadddout),
    .WRegDin(id_ex_1_wregdout), .WRegDout(ex_mem_1_wregdout), .HaltDin(and_1_out),
    .HaltDout(ex_mem_1_haltdout), .DispDin(and_2_out), .DispDout(ex_mem_1_dispdout), .WE(1'b1), .Clk(Clk),
    .Rst(Rst), .a0Din(multiplexer_8_out), .a0Dout(ex_mem_1_a0dout));
  Multiplexer #(.width(32), .enable("false")) multiplexer_15 (
    .in0(adder_5_out), .in1(register_2_q), .out(multiplexer_15_out), .sel(not_2_out));
  Multiplexer #(.select(2), .width(32), .enable("false")) multiplexer_16 (
    .in0(ex_mem_1_pcadddout), .in2(ex_mem_1_aludout), .out(multiplexer_16_out), .sel(ex_mem_1_rfdinsrcdout));  // open: in1, in3
  Register #(.width(32)) register_2 (.D(multiplexer_15_out), .Q(register_2_q), .clk(Clk));  // open: en, clr
  Adder #(.width(32)) adder_5 (.a(32'h1), .b(register_2_q), .out(adder_5_out));  // open: cin, cout
  // Probe on register_2_q
  RAM #(.addrWidth(10), .dataWidth(32), .bus("separate")) ram_1 (
    .addr(ex_mem_1_aludout[9:0]), .din(ex_mem_1_rfr2dout), .data(ram_1_data), .str(ex_mem_1_dmwedout),
    .sel(1'b1), .clk(Clk), .ld(1'b1), .clr(1'b0));
  // Probe on ex_mem_1_irdout
  assign bit_extender_5_out = {{16{ram_1_data[15]}}, ram_1_data[15:0]};  // Bit_Extender bit_extender_5
  // Probe on mem_wb_1_irdout
  MEM_WB mem_wb_1 (
    .PCDin(ex_mem_1_pcdout), .IRDin(ex_mem_1_irdout), .RFWEDin(ex_mem_1_rfwedout),
    .RFDinSrcDin(ex_mem_1_rfdinsrcdout), .IRDout(mem_wb_1_irdout), .RFWEDout(main_1_p5),
    .RFDinSrcDout(mem_wb_1_rfdinsrcdout), .ALUDin(ex_mem_1_aludout), .ALUDout(mem_wb_1_aludout),
    .DMDin(ram_1_data), .DMDout(mem_wb_1_dmdout), .PCAddDin(ex_mem_1_pcadddout),
    .PCAddDout(mem_wb_1_pcadddout), .SExt16to32Din(bit_extender_5_out),
    .SExt16to32Dout(mem_wb_1_sext16to32dout), .WRegDin(ex_mem_1_wregdout), .WRegDout(main_1_p3),
    .HaltDin(ex_mem_1_haltdout), .HaltDout(Halt), .DispDin(ex_mem_1_dispdout), .DispDout(mem_wb_1_dispdout),
    .WE(1'b1), .Clk(Clk), .Rst(Rst), .a0Din(ex_mem_1_a0dout), .a0Dout(mem_wb_1_a0dout));  // open: PCDout
  and and_3 (Clk, ~Halt, ComClk);  // AND_Gate
  Multiplexer #(.select(2), .width(32), .enable("false")) multiplexer_17 (
    .in0(mem_wb_1_pcadddout), .in1(mem_wb_1_dmdout), .in2(mem_wb_1_aludout), .in3(mem_wb_1_sext16to32dout),
    .out(main_1_p4), .sel(mem_wb_1_rfdinsrcdout));

  // Notes on the sheet:
  //   contents of rom_1 (hex, n*v repeats v):
  //   20110001 8000c05 20110001 20120002 20130003 8000c09 20110001 20120002 20130003 8000c0d 20110001
  //   20120002 20130003 8000c11 20110001 20120002 20130003 c000cb8 20100001 20110001 118fc0 112020
  //   20020022 c 118882 12200001 8000c15 112020 20020022 c 20110001 118880 112020 20020022 c 12200001
  //   8000c1f 20110001 118fc0 112020 20020022 c 1188c3 112020 20020022 c 118903 112020 20020022 c 118903
  //   112020 20020022 c 118903 112020 20020022 c 118903 112020 20020022 c 118903 112020 20020022 c 118903
  //   112020 20020022 c 118903 112020 20020022 c 20100001 109fc0 139fc3 8021 2012000c 24160003 26100001
  //   3210000f 20080008 20090001 139900 2709825 132020 20020022 c 1094022 1500fff9 22100001 2018000f
  //   2188024 108700 20080008 20090001 139902 2709825 132021 20020022 c 1094022 1500fff9 108702 2c9b022
  //   12c00001 8000c50 4020 1084027 84400 3508ffff 82021 20020022 c 2010ffff 20110000 ae300000 22100001
  //   22310004 ae300000 22100001 22310004 ae300000 22100001 22310004 ae300000 22100001 22310004 ae300000
  //   22100001 22310004 ae300000 22100001 22310004 ae300000 22100001 22310004 ae300000 22100001 22310004
  //   ae300000 22100001 22310004 ae300000 22100001 22310004 ae300000 22100001 22310004 ae300000 22100001
  //   22310004 ae300000 22100001 22310004 ae300000 22100001 22310004 ae300000 22100001 22310004 ae300000
  //   22100001 22310004 22100001 8020 2011003c 8e130000 8e340000 274402a 11000002 ae330000 ae140000
  //   2231fffc 1611fff8 102020 20020022 c 22100004 2011003c 1611fff2 2002000a c 20100000 22100001 102020
  //   20020022 c 22100002 102020 20020022 c 22100003 102020 20020022 c 22100004 102020 20020022 c 22100005
  //   102020 20020022 c 22100006 102020 20020022 c 22100007 102020 20020022 c 22100008 102020 20020022
  //   20020022 c 3e00008
endmodule

module InsAnalyse (
  input  [31:0] Ins,
  output [5:0] OP,
  output [4:0] Rs,
  output [4:0] Rt,
  output [4:0] Rd,
  output [4:0] Shamt,
  output [5:0] funct,
  output [15:0] Immediate16,
  output [25:0] Immediate26
);


  assign funct = Ins[5:0];
  assign Immediate16 = Ins[15:0];
  assign Immediate26 = Ins[25:0];
  assign OP = Ins[31:26];
  assign Rd = Ins[15:11];
  assign Rs = Ins[25:21];
  assign Rt = Ins[20:16];
  assign Shamt = Ins[10:6];
endmodule

module Control (
  input  [5:0] OP,
  input  [5:0] funct,
  output [31:0] AllIns,
  output [5:0] BrIns,
  output load,
  output PCAddSrc,
  output RFR1Src,
  output [1:0] RFRWSrc,
  output [1:0] RFDinSrc,
  output RFWE,
  output [1:0] ALUYSrc,
  output ALUYSrc2,
  output [3:0] ALUOP,
  output DMWE,
  output Syscall
);

  wire decoder_1_out0, decoder_2_out0, decoder_2_out1, decoder_4_out0, decoder_4_out1;

  Decoder #(.select(5), .disabled(0)) decoder_1 (
    .out0(decoder_1_out0), .out1(AllIns[9]), .out2(AllIns[8]), .out3(AllIns[7]), .out4(AllIns[6]),
    .out5(AllIns[5]), .out8(AllIns[4]), .out9(AllIns[3]), .out10(AllIns[2]), .out12(AllIns[1]),
    .out13(AllIns[0]), .sel(OP[4:0]), .en(decoder_2_out0));  // open: out6, out7, out11, out14, out15, out16, out17, out18, out19, out20, out21, out22, out23, out24, out25, out26, out27, out28, out29, out30, out31
  Decoder #(.enable("false")) decoder_2 (.out0(decoder_2_out0), .out1(decoder_2_out1), .sel(OP[5]));
  Decoder #(.select(5), .disabled(0)) decoder_3 (
    .out1(AllIns[10]), .out3(AllIns[11]), .out11(AllIns[12]), .sel(OP[4:0]), .en(decoder_2_out1));  // open: out0, out2, out4, out5, out6, out7, out8, out9, out10, out12, out13, out14, out15, out16, out17, out18, out19, out20, out21, out22, out23, out24, out25, out26, out27, out28, out29, out30, out31
  or or_1 (PCAddSrc, AllIns[6], AllIns[5], AllIns[9]);
  nor nor_1 (RFDinSrc[1], AllIns[11], AllIns[7]);
  or or_2 (RFDinSrc[0], AllIns[11], AllIns[10]);
  or or_3 (RFR1Src, AllIns[19], AllIns[17], AllIns[18], AllIns[16], AllIns[15]);
  or or_4 (ALUYSrc[1], AllIns[4], AllIns[3], AllIns[1], AllIns[0], AllIns[11], AllIns[12], AllIns[2], AllIns[10]);
  or or_5 (ALUYSrc[0], AllIns[1], AllIns[19], AllIns[17], AllIns[18], AllIns[0]);
  or or_6 (ALUOP[3], AllIns[24], AllIns[0], AllIns[25], AllIns[26], AllIns[2], AllIns[27], AllIns[9]);
  nor nor_2 (RFWE, AllIns[12], AllIns[6], AllIns[5], AllIns[8], AllIns[14], AllIns[13], AllIns[9]);
  or or_7 (ALUOP[1], AllIns[23], AllIns[1], AllIns[18], AllIns[22], AllIns[25], AllIns[6], AllIns[5], AllIns[26], AllIns[2], AllIns[15], AllIns[9]);
  or or_8 (RFRWSrc[0], AllIns[20], AllIns[21], AllIns[23], AllIns[19], AllIns[17], AllIns[18], AllIns[22], AllIns[24], AllIns[25], AllIns[26], AllIns[27], AllIns[16], AllIns[15]);
  or or_9 (ALUOP[2], AllIns[20], AllIns[4], AllIns[3], AllIns[21], AllIns[23], AllIns[1], AllIns[22], AllIns[11], AllIns[12], AllIns[6], AllIns[5], AllIns[27], AllIns[10]);
  or or_10 (ALUOP[0], AllIns[20], AllIns[4], AllIns[3], AllIns[21], AllIns[23], AllIns[1], AllIns[17], AllIns[11], AllIns[12], AllIns[26], AllIns[2], AllIns[10], AllIns[9]);
  Decoder #(.disabled(0)) decoder_4 (.out0(decoder_4_out0), .out1(decoder_4_out1), .sel(funct[5]), .en(decoder_1_out0));
  Decoder #(.select(5), .disabled(0)) decoder_5 (
    .out0(AllIns[19]), .out2(AllIns[18]), .out3(AllIns[17]), .out4(AllIns[16]), .out6(AllIns[15]),
    .out8(AllIns[14]), .out12(AllIns[13]), .sel(funct[4:0]), .en(decoder_4_out0));  // open: out1, out5, out7, out9, out10, out11, out13, out14, out15, out16, out17, out18, out19, out20, out21, out22, out23, out24, out25, out26, out27, out28, out29, out30, out31
  Decoder #(.select(5), .disabled(0)) decoder_6 (
    .out0(AllIns[20]), .out1(AllIns[21]), .out2(AllIns[22]), .out4(AllIns[23]), .out5(AllIns[24]),
    .out7(AllIns[25]), .out10(AllIns[26]), .out11(AllIns[27]), .sel(funct[4:0]), .en(decoder_4_out1));  // open: out3, out6, out8, out9, out12, out13, out14, out15, out16, out17, out18, out19, out20, out21, out22, out23, out24, out25, out26, out27, out28, out29, out30, out31
  or or_11 (load, AllIns[10], AllIns[11]);

  assign AllIns[31:28] = 4'b0000;
  assign ALUYSrc2 = AllIns[9];
  assign BrIns = {AllIns[6:5], AllIns[9:7], AllIns[14]};
  assign DMWE = AllIns[12];
  assign RFRWSrc[1] = AllIns[7];
  assign Syscall = AllIns[13];

  // Other names for the same wires on the sheet: ori = AllIns[0]; andi = AllIns[1]; slti = AllIns[2];
  //   addiu = AllIns[3]; addi = AllIns[4]; bne = AllIns[5]; beq = AllIns[6]; jal = AllIns[7]; j = AllIns[8];
  //   bgez = AllIns[9]; lh = AllIns[10]; lw = AllIns[11]; sw = AllIns[12]; jr = AllIns[14]; srlv = AllIns[15];
  //   sllv = AllIns[16]; sra = AllIns[17]; srl = AllIns[18]; sll = AllIns[19]; add = AllIns[20]; addu = AllIns[21];
  //   sub = AllIns[22]; and = AllIns[23]; or = AllIns[24]; nor = AllIns[25]; slt = AllIns[26]; sltu = AllIns[27]
endmodule

module Branch (
  input  Equal,
  input  Judge,
  input  [5:0] BrIns,
  output [1:0] BrPCSrc,
  output PCSrc
);

  wire and_1_out, and_2_out, and_3_out, and_4_out, and_5_out, and_6_out, and_7_out, and_8_out, and_9_out,
       not_1_out, not_2_out, not_3_out;

  not not_1 (not_1_out, Judge);
  not not_2 (not_2_out, Equal);
  and and_1 (and_1_out, BrIns[5], Equal);
  and and_2 (and_2_out, BrIns[4], not_3_out);
  not not_3 (not_3_out, Equal);
  and and_3 (and_3_out, BrIns[5], Equal);
  and and_4 (and_4_out, BrIns[4], not_2_out);
  and and_5 (and_5_out, BrIns[3], not_1_out);
  and and_6 (and_6_out, BrIns[3], not_1_out);
  or or_1 (BrPCSrc[1], and_3_out, and_4_out, BrIns[2], BrIns[1], and_5_out);
  nor nor_1 (BrPCSrc[0], and_6_out, and_1_out, and_2_out, BrIns[0]);
  and and_7 (and_7_out, BrIns[5], Equal);
  and and_8 (and_8_out, BrIns[4], ~Equal);  // AND_Gate
  and and_9 (and_9_out, BrIns[3], ~Equal);  // AND_Gate
  or or_2 (PCSrc, and_7_out, and_8_out, and_9_out, BrIns[2], BrIns[1], BrIns[0]);

  // Other names for the same wires on the sheet: jr = BrIns[0]; jal = BrIns[1]; j = BrIns[2]; bgez = BrIns[3];
  //   bne = BrIns[4]; beq = BrIns[5]
endmodule

module IF_ID (
  input  [31:0] PC_1Din,
  input  [31:0] PCDin,
  input  [31:0] IRDin,
  input  WE,
  input  Clk,
  input  Rst,
  output [31:0] PC_1Dout,
  output [31:0] PCDout,
  output [31:0] IRDout
);

  wire d_ff_1_q;

  Register #(.width(32)) PC_1 (.D(PC_1Din), .en(WE), .Q(PC_1Dout), .clk(Clk), .clr(d_ff_1_q));
  Register #(.width(32)) PC (.D(PCDin), .en(WE), .Q(PCDout), .clk(Clk), .clr(d_ff_1_q));
  Register #(.width(32)) IR (.D(IRDin), .en(WE), .Q(IRDout), .clk(Clk), .clr(d_ff_1_q));
  D_Flip_Flop d_ff_1 (.clk(Clk), .D(Rst), .Q(d_ff_1_q), .reset(d_ff_1_q));  // open: Qn, preset, en
endmodule

module ID_EX (
  input  loadDin,
  input  [1:0] RDTR1SrcDin,
  input  [1:0] RDTR2SrcDin,
  input  [31:0] a0Din,
  input  [31:0] v0Din,
  input  SyscallDin,
  input  [31:0] PC_1Din,
  input  [31:0] PCDin,
  input  [31:0] IRDin,
  input  [3:0] ALUOPDin,
  input  [1:0] ALUYSrcDin,
  input  ALUYSrc2Din,
  input  [31:0] RFR1Din,
  input  [31:0] RFR2Din,
  input  [31:0] Ext5to32Din,
  input  [31:0] SExt16to32Din,
  input  [31:0] Ext16to32Din,
  input  [31:0] SExt26to32Din,
  input  DMWEDin,
  input  PCAddSrcDin,
  input  RFWEDin,
  input  [1:0] RFDinSrcDin,
  input  [5:0] BrInsDin,
  input  [4:0] WRegDin,
  input  WE,
  input  Clk,
  input  Rst,
  output loadDout,
  output [1:0] RDTR1SrcDout,
  output [1:0] RDTR2SrcDout,
  output [31:0] a0Dout,
  output [31:0] v0Dout,
  output SyscallDout,
  output [31:0] PC_1Dout,
  output [31:0] PCDout,
  output [31:0] IRDout,
  output [3:0] ALUOPDout,
  output [1:0] ALUYSrcDout,
  output ALUYSrc2Dout,
  output [31:0] RFR1Dout,
  output [31:0] RFR2Dout,
  output [31:0] Ext5to32Dout,
  output [31:0] SExt16to32Dout,
  output [31:0] Ext16to32Dout,
  output [31:0] SExt26to32Dout,
  output DMWEDout,
  output PCAddSrcDout,
  output RFWEDout,
  output [1:0] RFDinSrcDout,
  output [5:0] BrInsDout,
  output [4:0] WRegDout
);

  wire d_ff_1_q;

  Register #(.width(1)) load (.D(loadDin), .en(WE), .Q(loadDout), .clk(Clk), .clr(d_ff_1_q));
  Register #(.width(2)) RDTR1Src (.D(RDTR1SrcDin), .en(WE), .Q(RDTR1SrcDout), .clk(Clk), .clr(d_ff_1_q));
  Register #(.width(2)) RDTR2Src (.D(RDTR2SrcDin), .en(WE), .Q(RDTR2SrcDout), .clk(Clk), .clr(d_ff_1_q));
  Register #(.width(32)) a0 (.D(a0Din), .en(WE), .Q(a0Dout), .clk(Clk), .clr(d_ff_1_q));
  Register #(.width(32)) v0 (.D(v0Din), .en(WE), .Q(v0Dout), .clk(Clk), .clr(d_ff_1_q));
  Register #(.width(1)) Syscall (.D(SyscallDin), .en(WE), .Q(SyscallDout), .clk(Clk), .clr(d_ff_1_q));
  Register #(.width(32)) PC_1 (.D(PC_1Din), .en(WE), .Q(PC_1Dout), .clk(Clk), .clr(d_ff_1_q));
  Register #(.width(32)) PC (.D(PCDin), .en(WE), .Q(PCDout), .clk(Clk), .clr(d_ff_1_q));
  Register #(.width(32)) IR (.D(IRDin), .en(WE), .Q(IRDout), .clk(Clk), .clr(d_ff_1_q));
  Register #(.width(4)) ALUOP (.D(ALUOPDin), .en(WE), .Q(ALUOPDout), .clk(Clk), .clr(d_ff_1_q));
  Register #(.width(2)) ALUYSrc (.D(ALUYSrcDin), .en(WE), .Q(ALUYSrcDout), .clk(Clk), .clr(d_ff_1_q));
  Register #(.width(1)) ALUYSrc2 (.D(ALUYSrc2Din), .en(WE), .Q(ALUYSrc2Dout), .clk(Clk), .clr(d_ff_1_q));
  Register #(.width(32)) RFR1 (.D(RFR1Din), .en(WE), .Q(RFR1Dout), .clk(Clk), .clr(d_ff_1_q));
  Register #(.width(32)) RFR2 (.D(RFR2Din), .en(WE), .Q(RFR2Dout), .clk(Clk), .clr(d_ff_1_q));
  Register #(.width(32)) Ext5to32 (.D(Ext5to32Din), .en(WE), .Q(Ext5to32Dout), .clk(Clk), .clr(d_ff_1_q));
  Register #(.width(32)) SExt16to32 (.D(SExt16to32Din), .en(WE), .Q(SExt16to32Dout), .clk(Clk), .clr(d_ff_1_q));
  Register #(.width(32)) Ext16to32 (.D(Ext16to32Din), .en(WE), .Q(Ext16to32Dout), .clk(Clk), .clr(d_ff_1_q));
  Register #(.width(32)) SExt26to32 (.D(SExt26to32Din), .en(WE), .Q(SExt26to32Dout), .clk(Clk), .clr(d_ff_1_q));
  Register #(.width(1)) DMWE (.D(DMWEDin), .en(WE), .Q(DMWEDout), .clk(Clk), .clr(d_ff_1_q));
  Register #(.width(1)) PCAddSrc (.D(PCAddSrcDin), .en(WE), .Q(PCAddSrcDout), .clk(Clk), .clr(d_ff_1_q));
  Register #(.width(1)) RFWE (.D(RFWEDin), .en(WE), .Q(RFWEDout), .clk(Clk), .clr(d_ff_1_q));
  Register #(.width(2)) RFDinSrc (.D(RFDinSrcDin), .en(WE), .Q(RFDinSrcDout), .clk(Clk), .clr(d_ff_1_q));
  Register #(.width(6)) BrIns (.D(BrInsDin), .en(WE), .Q(BrInsDout), .clk(Clk), .clr(d_ff_1_q));
  Register #(.width(5)) WReg (.D(WRegDin), .en(WE), .Q(WRegDout), .clk(Clk), .clr(d_ff_1_q));
  D_Flip_Flop d_ff_1 (.clk(Clk), .D(Rst), .Q(d_ff_1_q), .reset(d_ff_1_q));  // open: Qn, preset, en
endmodule

module EX_MEM (
  input  [31:0] a0Din,
  input  DispDin,
  input  HaltDin,
  input  [31:0] PCDin,
  input  [31:0] IRDin,
  input  DMWEDin,
  input  RFWEDin,
  input  [1:0] RFDinSrcDin,
  input  [31:0] ALUDin,
  input  [31:0] RFR2Din,
  input  [31:0] PCAddDin,
  input  [4:0] WRegDin,
  input  WE,
  input  Clk,
  input  Rst,
  output [31:0] a0Dout,
  output DispDout,
  output HaltDout,
  output [31:0] PCDout,
  output [31:0] IRDout,
  output DMWEDout,
  output RFWEDout,
  output [1:0] RFDinSrcDout,
  output [31:0] ALUDout,
  output [31:0] RFR2Dout,
  output [31:0] PCAddDout,
  output [4:0] WRegDout
);

  wire d_ff_1_q;

  Register #(.width(32)) a0 (.D(a0Din), .en(WE), .Q(a0Dout), .clk(Clk), .clr(d_ff_1_q));
  Register #(.width(1)) Disp (.D(DispDin), .en(WE), .Q(DispDout), .clk(Clk), .clr(d_ff_1_q));
  Register #(.width(1)) Halt (.D(HaltDin), .en(WE), .Q(HaltDout), .clk(Clk), .clr(d_ff_1_q));
  Register #(.width(32)) PC (.D(PCDin), .en(WE), .Q(PCDout), .clk(Clk), .clr(d_ff_1_q));
  Register #(.width(32)) IR (.D(IRDin), .en(WE), .Q(IRDout), .clk(Clk), .clr(d_ff_1_q));
  Register #(.width(1)) DMWE (.D(DMWEDin), .en(WE), .Q(DMWEDout), .clk(Clk), .clr(d_ff_1_q));
  Register #(.width(1)) RFWE (.D(RFWEDin), .en(WE), .Q(RFWEDout), .clk(Clk), .clr(d_ff_1_q));
  Register #(.width(2)) RFDinSrc (.D(RFDinSrcDin), .en(WE), .Q(RFDinSrcDout), .clk(Clk), .clr(d_ff_1_q));
  Register #(.width(32)) ALU (.D(ALUDin), .en(WE), .Q(ALUDout), .clk(Clk), .clr(d_ff_1_q));
  Register #(.width(32)) RFR2 (.D(RFR2Din), .en(WE), .Q(RFR2Dout), .clk(Clk), .clr(d_ff_1_q));
  Register #(.width(32)) PCAdd (.D(PCAddDin), .en(WE), .Q(PCAddDout), .clk(Clk), .clr(d_ff_1_q));
  Register #(.width(5)) WReg (.D(WRegDin), .en(WE), .Q(WRegDout), .clk(Clk), .clr(d_ff_1_q));
  D_Flip_Flop d_ff_1 (.clk(Clk), .D(Rst), .Q(d_ff_1_q), .reset(d_ff_1_q));  // open: Qn, preset, en
endmodule

module MEM_WB (
  input  [31:0] a0Din,
  input  DispDin,
  input  HaltDin,
  input  [31:0] PCDin,
  input  [31:0] IRDin,
  input  RFWEDin,
  input  [1:0] RFDinSrcDin,
  input  [31:0] ALUDin,
  input  [31:0] DMDin,
  input  [31:0] SExt16to32Din,
  input  [31:0] PCAddDin,
  input  [4:0] WRegDin,
  input  WE,
  input  Clk,
  input  Rst,
  output [31:0] a0Dout,
  output DispDout,
  output HaltDout,
  output [31:0] PCDout,
  output [31:0] IRDout,
  output RFWEDout,
  output [1:0] RFDinSrcDout,
  output [31:0] ALUDout,
  output [31:0] DMDout,
  output [31:0] SExt16to32Dout,
  output [31:0] PCAddDout,
  output [4:0] WRegDout
);

  wire d_ff_1_q;

  Register #(.width(32)) a0 (.D(a0Din), .en(WE), .Q(a0Dout), .clk(Clk), .clr(d_ff_1_q));
  Register #(.width(1)) Disp (.D(DispDin), .en(WE), .Q(DispDout), .clk(Clk), .clr(d_ff_1_q));
  Register #(.width(1)) Halt (.D(HaltDin), .en(WE), .Q(HaltDout), .clk(Clk), .clr(d_ff_1_q));
  Register #(.width(32)) PC (.D(PCDin), .en(WE), .Q(PCDout), .clk(Clk), .clr(d_ff_1_q));
  Register #(.width(32)) IR (.D(IRDin), .en(WE), .Q(IRDout), .clk(Clk), .clr(d_ff_1_q));
  Register #(.width(1)) RFWE (.D(RFWEDin), .en(WE), .Q(RFWEDout), .clk(Clk), .clr(d_ff_1_q));
  Register #(.width(2)) RFDinSrc (.D(RFDinSrcDin), .en(WE), .Q(RFDinSrcDout), .clk(Clk), .clr(d_ff_1_q));
  Register #(.width(32)) ALU (.D(ALUDin), .en(WE), .Q(ALUDout), .clk(Clk), .clr(d_ff_1_q));
  Register #(.width(32)) DM (.D(DMDin), .en(WE), .Q(DMDout), .clk(Clk), .clr(d_ff_1_q));
  Register #(.width(32)) SExt16to32 (.D(SExt16to32Din), .en(WE), .Q(SExt16to32Dout), .clk(Clk), .clr(d_ff_1_q));
  Register #(.width(32)) PCAdd (.D(PCAddDin), .en(WE), .Q(PCAddDout), .clk(Clk), .clr(d_ff_1_q));
  Register #(.width(5)) WReg (.D(WRegDin), .en(WE), .Q(WRegDout), .clk(Clk), .clr(d_ff_1_q));
  D_Flip_Flop d_ff_1 (.clk(Clk), .D(Rst), .Q(d_ff_1_q), .reset(d_ff_1_q));  // open: Qn, preset, en
endmodule

module DataHzd (
  input  [4:0] Rs,
  input  [4:0] EX_WReg,
  input  EX_WE,
  input  [4:0] MEM_WReg,
  input  [4:0] Rt,
  input  MEM_WE,
  input  [31:0] AllIns,
  input  load,
  output Nop,
  output Stop,
  output [1:0] RDTR1Src,
  output [1:0] RDTR2Src
);

  wire and_1_out, and_6_out, and_7_out, and_8_out, and_9_out, and_10_out, and_11_out, and_12_out, and_13_out,
       and_14_out, and_15_out, and_16_out, and_18_out, and_19_out, and_20_out, and_21_out, and_22_out,
       and_23_out, and_24_out, and_25_out, comparator_1_eq, comparator_2_eq, comparator_3_eq,
       comparator_4_eq, EXRsEqu, EXRtEqu, MEMRsEqu, MEMRtEqu, or_1_out, or_2_out, or_3_out, or_4_out,
       or_5_out, or_6_out, or_7_out, or_8_out, or_9_out, or_10_out, or_11_out, or_12_out, or_13_out,
       or_14_out, or_17_out, or_20_out, or_21_out, or_22_out, or_23_out, or_24_out, or_25_out, or_26_out,
       or_27_out, RsZero, RtZero;
  wire [4:0] EX_WReg_t, MEM_WReg_t, Rs_t, Rt_t;

  Multiplexer #(.width(5), .enable("false")) multiplexer_1 (
    .in0({5{1'b0}}), .in1(EX_WReg), .out(EX_WReg_t), .sel(EX_WE));
  Multiplexer #(.width(5), .enable("false")) multiplexer_2 (
    .in0({5{1'b0}}), .in1(MEM_WReg), .out(MEM_WReg_t), .sel(MEM_WE));
  Comparator #(.width(5), .mode("unsigned")) comparator_1 (
    .a(EX_WReg_t), .b(Rs_t), .eq(comparator_1_eq));  // open: gt, lt
  Comparator #(.width(5), .mode("unsigned")) comparator_2 (
    .a(EX_WReg_t), .b(Rt_t), .eq(comparator_2_eq));  // open: gt, lt
  Comparator #(.width(5), .mode("unsigned")) comparator_3 (
    .a(MEM_WReg_t), .b(Rs_t), .eq(comparator_3_eq));  // open: gt, lt
  Comparator #(.width(5), .mode("unsigned")) comparator_4 (
    .a(MEM_WReg_t), .b(Rt_t), .eq(comparator_4_eq));  // open: gt, lt
  or or_1 (or_1_out, AllIns[5], AllIns[6], AllIns[12]);
  or or_2 (or_2_out, AllIns[17], AllIns[18], AllIns[19]);
  or or_3 (or_3_out, AllIns[17], AllIns[18], AllIns[19]);
  or or_4 (or_4_out, AllIns[0], AllIns[1], AllIns[2], AllIns[3], AllIns[4], AllIns[14], AllIns[9], AllIns[10], AllIns[11]);
  or or_5 (or_5_out, AllIns[15], AllIns[16]);
  or or_6 (or_6_out, AllIns[5], AllIns[6], AllIns[12]);
  or or_7 (or_7_out, AllIns[15], AllIns[16]);
  or or_8 (or_8_out, AllIns[5], AllIns[6], AllIns[12]);
  or or_9 (or_9_out, AllIns[15], AllIns[16], AllIns[20], AllIns[21], AllIns[22], AllIns[23], AllIns[24], AllIns[25], AllIns[26], AllIns[27], AllIns[13]);
  or or_10 (or_10_out, EXRsEqu, EXRtEqu);
  or or_11 (or_11_out, AllIns[0], AllIns[1], AllIns[2], AllIns[3], AllIns[4], AllIns[14], AllIns[9], AllIns[10], AllIns[11]);
  and and_1 (and_1_out, or_3_out, EXRtEqu);
  or or_12 (or_12_out, AllIns[20], AllIns[21], AllIns[22], AllIns[23], AllIns[24], AllIns[25], AllIns[26], AllIns[27], AllIns[13]);
  or or_13 (or_13_out, AllIns[20], AllIns[21], AllIns[22], AllIns[23], AllIns[24], AllIns[25], AllIns[26], AllIns[27], AllIns[13]);
  and and_2 (EXRsEqu, RsZero, comparator_1_eq);
  and and_3 (EXRtEqu, RtZero, comparator_2_eq);
  and and_4 (MEMRsEqu, RsZero, comparator_3_eq);
  and and_5 (MEMRtEqu, RtZero, comparator_4_eq);
  or or_14 (or_14_out, EXRsEqu, EXRtEqu);
  and and_6 (and_6_out, or_2_out, EXRtEqu);
  and and_7 (and_7_out, or_11_out, EXRsEqu);
  and and_8 (and_8_out, or_4_out, EXRsEqu);
  and and_9 (and_9_out, or_5_out, EXRtEqu);
  and and_10 (and_10_out, or_6_out, EXRsEqu);
  and and_11 (and_11_out, or_7_out, EXRsEqu);
  and and_12 (and_12_out, or_8_out, EXRtEqu);
  and and_13 (and_13_out, or_9_out, or_14_out);
  and and_14 (and_14_out, or_1_out, or_10_out);
  and and_15 (and_15_out, or_12_out, EXRsEqu);
  and and_16 (and_16_out, or_13_out, EXRtEqu);
  Multiplexer #(.width(5), .enable("false")) multiplexer_3 (.in0(Rs), .in1(5'b00010), .out(Rs_t), .sel(AllIns[13]));
  Multiplexer #(.width(5), .enable("false")) multiplexer_4 (.in0(Rt), .in1(5'b00100), .out(Rt_t), .sel(AllIns[13]));
  or or_15 (RsZero, Rs_t[0], Rs_t[1], Rs_t[2], Rs_t[3], Rs_t[4]);
  or or_16 (RtZero, Rt_t[0], Rt_t[1], Rt_t[2], Rt_t[3], Rt_t[4]);
  or or_17 (or_17_out, and_13_out, and_14_out, and_6_out, and_7_out);
  or or_18 (RDTR1Src[1], and_1_out, and_8_out, and_15_out, and_9_out, and_10_out);
  or or_19 (RDTR2Src[1], and_16_out, and_11_out, and_12_out);
  and and_17 (Nop, or_17_out, load);
  not not_1 (Stop, Nop);
  or or_20 (or_20_out, AllIns[17], AllIns[18], AllIns[19]);
  or or_21 (or_21_out, AllIns[0], AllIns[1], AllIns[2], AllIns[3], AllIns[4], AllIns[14], AllIns[9], AllIns[10], AllIns[11]);
  or or_22 (or_22_out, AllIns[15], AllIns[16]);
  or or_23 (or_23_out, AllIns[5], AllIns[6], AllIns[12]);
  or or_24 (or_24_out, AllIns[15], AllIns[16]);
  or or_25 (or_25_out, AllIns[5], AllIns[6], AllIns[12]);
  and and_18 (and_18_out, or_20_out, MEMRtEqu);
  or or_26 (or_26_out, AllIns[20], AllIns[21], AllIns[22], AllIns[23], AllIns[24], AllIns[25], AllIns[26], AllIns[27], AllIns[13]);
  and and_19 (and_19_out, or_22_out, MEMRtEqu);
  and and_20 (and_20_out, or_23_out, MEMRsEqu);
  or or_27 (or_27_out, AllIns[20], AllIns[21], AllIns[22], AllIns[23], AllIns[24], AllIns[25], AllIns[26], AllIns[27], AllIns[13]);
  and and_21 (and_21_out, or_24_out, MEMRsEqu);
  and and_22 (and_22_out, or_25_out, MEMRtEqu);
  and and_23 (and_23_out, or_21_out, MEMRsEqu);
  and and_24 (and_24_out, or_26_out, MEMRsEqu);
  and and_25 (and_25_out, or_27_out, MEMRtEqu);
  or or_28 (RDTR2Src[0], and_25_out, and_21_out, and_22_out);
  or or_29 (RDTR1Src[0], and_18_out, and_23_out, and_24_out, and_19_out, and_20_out);
  // also tied to GND on the sheet: {AllIns[28], AllIns[29], AllIns[30], AllIns[31]}

  // Other names for the same wires on the sheet: ori = AllIns[0]; andi = AllIns[1]; slti = AllIns[2];
  //   addiu = AllIns[3]; addi = AllIns[4]; bne = AllIns[5]; beq = AllIns[6]; jal = AllIns[7]; j = AllIns[8];
  //   bgez = AllIns[9]; lh = AllIns[10]; lw = AllIns[11]; sw = AllIns[12]; syscall = AllIns[13]; jr = AllIns[14];
  //   srlv = AllIns[15]; sllv = AllIns[16]; sra = AllIns[17]; srl = AllIns[18]; sll = AllIns[19]; add = AllIns[20];
  //   addu = AllIns[21]; sub = AllIns[22]; and = AllIns[23]; or = AllIns[24]; nor = AllIns[25]; slt = AllIns[26];
  //   sltu = AllIns[27]; MEMR1Equ = RDTR1Src[0]; EXR1Equ = RDTR1Src[1]; MEMR2Equ = RDTR2Src[0]; EXR2Equ = RDTR2Src[1]
endmodule
