// Logisim project 5-stage-cpu.circ as structural Verilog: 11 circuits, main circuit main
module main (
  input  Rst
);

  wire alu_1_equal, and_1_out, and_2_out, and_3_out, and_4_out, branch_1_pcsrc, branch_1_postclr, Clk,
       ComClk, comparator_1_eq, comparator_2_eq, control_1_aluysrc2, control_1_dmwe, control_1_load,
       control_1_pcaddsrc, control_1_rfr1src, control_1_rfwe, control_1_syscall, datahzd_1_nop,
       datahzd_1_stop, ex_mem_1_dispdout, ex_mem_1_dmwedout, ex_mem_1_haltdout, ex_mem_1_rfwedout, Halt,
       id_ex_1_aluysrc2dout, id_ex_1_dmwedout, id_ex_1_loaddout, id_ex_1_pcaddsrcdout, id_ex_1_rfwedout,
       id_ex_1_syscalldout, intr_1_intr, intr_1_res, main_1_p5, mem_wb_1_dispdout, not_1_out, not_2_out,
       or_1_out, or_2_out;
  wire [0:0] bht_1_hit;
  wire [1:0] bht_1_predict, branch_1_brpcsrc, branch_1_repcsrc2, branch_1_tobht_2, control_1_aluysrc,
       control_1_rfdinsrc, control_1_rfrwsrc, datahzd_1_rdtr1src, datahzd_1_rdtr2src, ex_mem_1_rfdinsrcdout,
       id_ex_1_aluysrcdout, id_ex_1_rdtr1srcdout, id_ex_1_rdtr2srcdout, id_ex_1_rfdinsrcdout,
       mem_wb_1_rfdinsrcdout;
  wire [2:0] bht_1_hitnum, bht_1_insertnum, branch_1_tobht_3;
  wire [3:0] control_1_aluop, Disp_q_2, Disp_q_3, Disp_q_4, Disp_q_5, Disp_q_6, id_ex_1_aluopdout,
       Interupt0_out, intr_1_irwt;
  wire [4:0] ex_mem_1_wregdout, id_ex_1_wregdout, insanalyse_1_rd, insanalyse_1_rs, insanalyse_1_rt,
       insanalyse_1_shamt, main_1_p3, multiplexer_5_out, multiplexer_6_out, multiplexer_7_out;
  wire [5:0] insanalyse_1_funct, insanalyse_1_op;
  wire [6:0] control_1_brins, control_1_intctl, ex_mem_1_intctldout, id_ex_1_brinsdout, id_ex_1_intctldout,
       mem_wb_1_intctldout;
  wire [7:0] branch_1_tobht;
  wire [8:0] id_ex_1_bhtitemdout, if_id_1_bhtitemdout;
  wire [11:0] Disp_q;
  wire [15:0] insanalyse_1_immediate16;
  wire [25:0] insanalyse_1_immediate26;
  wire [31:0] adder_1_out, adder_2_out, adder_3_out, adder_4_out, adder_5_out, adder_6_out, alu_1_result,
       bht_1_branchaddr, bit_extender_1_out, bit_extender_2_out, bit_extender_3_out, bit_extender_4_out,
       bit_extender_5_out, control_1_allins, counter_1_q, EPC_q, ex_mem_1_a0dout, ex_mem_1_aludout,
       ex_mem_1_cp00dout, ex_mem_1_cp01dout, ex_mem_1_irdout, ex_mem_1_pcadddout, ex_mem_1_pcdout,
       ex_mem_1_rfr2dout, id_ex_1_a0dout, id_ex_1_cp00dout, id_ex_1_cp01dout, id_ex_1_ext5to32dout,
       id_ex_1_ext16to32dout, id_ex_1_irdout, id_ex_1_pc_1dout, id_ex_1_pcdout, id_ex_1_rfr1dout,
       id_ex_1_rfr2dout, id_ex_1_sext16to32dout, id_ex_1_sext26to32dout, id_ex_1_v0dout, if_id_1_irdout,
       if_id_1_pc_1dout, if_id_1_pcdout, intr_1_irnum, intr_1_regout, main_1_p4, main_1_p6, main_1_p7,
       main_1_p9, main_1_p10, mem_wb_1_a0dout, mem_wb_1_aludout, mem_wb_1_cp00dout, mem_wb_1_cp01dout,
       mem_wb_1_dmdout, mem_wb_1_irdout, mem_wb_1_pcadddout, mem_wb_1_sext16to32dout, multiplexer_1_out,
       multiplexer_2_out, multiplexer_3_out, multiplexer_4_out, multiplexer_8_out, multiplexer_9_out,
       multiplexer_10_out, multiplexer_11_out, multiplexer_12_out, multiplexer_13_out, multiplexer_14_out,
       multiplexer_15_out, multiplexer_16_out, multiplexer_17_out, multiplexer_18_out, multiplexer_19_out,
       multiplexer_20_out, multiplexer_21_out, multiplexer_22_out, PC_q, ram_1_data, register_1_q,
       register_2_q, rom_1_data;

  Multiplexer #(.width(32), .enable("false")) multiplexer_1 (
    .in0(multiplexer_3_out), .in1(multiplexer_18_out), .out(multiplexer_1_out), .sel(branch_1_pcsrc));
  Hex_Digit_Display hex_digit_display_1 (.value(Disp_q_6), .dp(1'b0));
  Multiplexer #(.width(32), .enable("false")) multiplexer_2 (
    .in0(adder_2_out), .in1(register_1_q), .out(multiplexer_2_out), .sel(datahzd_1_stop));
  Register #(.width(32)) PC (.D(multiplexer_1_out), .en(datahzd_1_stop), .Q(PC_q), .clk(Clk));  // open: clr
  BHT bht_1 (
    .write_valid(branch_1_tobht[7]), .we_valid(branch_1_tobht[6]), .we_pc(branch_1_tobht[1]),
    .write_pc(id_ex_1_pcdout), .we_branch(branch_1_tobht[0]), .cur_pc(PC_q), .we_predict(branch_1_tobht[3]),
    .write_branch(multiplexer_18_out), .we_lru(branch_1_tobht[2]), .write_predict(branch_1_tobht_2),
    .Hit(bht_1_hit[0]), .BranchAddr(bht_1_branchaddr), .InsertNum(bht_1_insertnum), .predict(bht_1_predict),
    .write_address(branch_1_tobht_3), .HitNum(bht_1_hitnum), .Clk(Clk));
  Hex_Digit_Display hex_digit_display_2 (.value(Disp_q_4), .dp(1'b0));
  Hex_Digit_Display hex_digit_display_3 (.value(Disp_q_5), .dp(1'b0));
  Clock clock_1 (.out(ComClk));
  Register #(.width(32)) register_1 (.D(multiplexer_2_out), .Q(register_1_q), .clk(Clk));  // open: en, clr
  Adder #(.width(32)) adder_1 (.a(32'h1), .b(PC_q), .out(adder_1_out));  // open: cin, cout
  Multiplexer #(.width(32), .enable("false")) multiplexer_3 (
    .in0(adder_1_out), .in1(bht_1_branchaddr), .out(multiplexer_3_out), .sel(and_1_out));
  and and_1 (and_1_out, bht_1_hit[0], bht_1_predict[1]);
  Hex_Digit_Display hex_digit_display_4 (.value(Disp_q_3), .dp(1'b0));
  Hex_Digit_Display hex_digit_display_5 (.value(Disp_q_2), .dp(1'b0));
  Register #(.width(32), .trigger("high")) Disp (
    .D(mem_wb_1_a0dout), .en(1'b1), .Q({Disp_q_6, Disp_q_5, Disp_q_4, Disp_q_3, Disp_q_2, Disp_q}),
    .clk(mem_wb_1_dispdout), .clr(1'b0));
  Adder #(.width(32)) adder_2 (.a(32'h1), .b(register_1_q), .out(adder_2_out));  // open: cin, cout
  // Probe on register_1_q
  Hex_Digit_Display hex_digit_display_6 (.value(Disp_q[11:8]), .dp(1'b0));
  Hex_Digit_Display hex_digit_display_7 (.value(Disp_q[7:4]), .dp(1'b0));
  Hex_Digit_Display hex_digit_display_8 (.value(Disp_q[3:0]), .dp(1'b0));
  ROM #(.addrWidth(10), .dataWidth(32)) rom_1 (.addr(PC_q[9:0]), .data(rom_1_data), .sel(1'b1));
  IF_ID if_id_1 (
    .PCDin(PC_q), .IRDin(rom_1_data), .PCDout(if_id_1_pcdout), .IRDout(if_id_1_irdout), .WE(datahzd_1_stop),
    .Clk(Clk), .Rst(branch_1_pcsrc), .PC_1Din(adder_1_out), .PC_1Dout(if_id_1_pc_1dout),
    .BHTItemDin({bht_1_insertnum, bht_1_hitnum, bht_1_predict, bht_1_hit[0]}),
    .BHTItemDout(if_id_1_bhtitemdout));
  Counter #(.width(32), .max('hffffffff)) counter_1 (.Q(counter_1_q), .clk(Clk));  // open: load, D, count, carry, clr
  DataHzd datahzd_1 (
    .EX_WReg(id_ex_1_wregdout), .MEM_WReg(ex_mem_1_wregdout), .AllIns(control_1_allins),
    .EX_WE(id_ex_1_rfwedout), .Rs(insanalyse_1_rs), .Rt(insanalyse_1_rt), .Stop(datahzd_1_stop),
    .Nop(datahzd_1_nop), .MEM_WE(ex_mem_1_rfwedout), .RDTR1Src(datahzd_1_rdtr1src),
    .RDTR2Src(datahzd_1_rdtr2src), .load(id_ex_1_loaddout));
  InsAnalyse insanalyse_1 (
    .Ins(if_id_1_irdout), .OP(insanalyse_1_op), .Rs(insanalyse_1_rs), .Rt(insanalyse_1_rt),
    .Rd(insanalyse_1_rd), .Shamt(insanalyse_1_shamt), .funct(insanalyse_1_funct),
    .Immediate16(insanalyse_1_immediate16), .Immediate26(insanalyse_1_immediate26));
  Multiplexer #(.width(32), .enable("false")) multiplexer_4 (
    .in0({32{1'b0}}), .in1(32'h1), .out(multiplexer_4_out), .sel(Halt));
  // Probe on if_id_1_irdout
  not not_1 (not_1_out, control_1_rfr1src);
  // Probe on adder_3_out
  Adder #(.width(32)) adder_3 (.a(multiplexer_4_out), .b(counter_1_q), .out(adder_3_out));  // open: cin, cout
  Control control_1 (
    .PCAddSrc(control_1_pcaddsrc), .RFR1Src(control_1_rfr1src), .RFRWSrc(control_1_rfrwsrc),
    .RFDinSrc(control_1_rfdinsrc), .RFWE(control_1_rfwe), .ALUYSrc(control_1_aluysrc),
    .ALUOP(control_1_aluop), .DMWE(control_1_dmwe), .Syscall(control_1_syscall),
    .ALUYSrc2(control_1_aluysrc2), .BrIns(control_1_brins), .AllIns(control_1_allins), .load(control_1_load),
    .OP(insanalyse_1_op), .funct(insanalyse_1_funct), .Rs(insanalyse_1_rs), .Rd(insanalyse_1_rd),
    .INTCtl(control_1_intctl));
  Multiplexer #(.width(5), .enable("false")) multiplexer_5 (
    .in0(insanalyse_1_rs), .in1(insanalyse_1_rt), .out(multiplexer_5_out), .sel(control_1_rfr1src));
  Multiplexer #(.width(5), .enable("false")) multiplexer_6 (
    .in0(insanalyse_1_rs), .in1(insanalyse_1_rt), .out(multiplexer_6_out), .sel(not_1_out));
  Multiplexer #(.select(2), .width(5), .enable("false")) multiplexer_7 (
    .in0(insanalyse_1_rt), .in1(insanalyse_1_rd), .in2({5{1'b1}}), .out(multiplexer_7_out),
    .sel(control_1_rfrwsrc));  // open: in3
  // regfile_5_stage_cpu_main main_1: pin names not known; wires that end beside it: multiplexer_5_out, multiplexer_6_out, main_1_p3, main_1_p4, main_1_p5, main_1_p6, main_1_p7, Clk, main_1_p9, main_1_p10
  assign bit_extender_1_out = {{27{1'b0}}, insanalyse_1_shamt};  // Bit_Extender bit_extender_1
  assign bit_extender_2_out = {{16{insanalyse_1_immediate16[15]}}, insanalyse_1_immediate16};  // Bit_Extender bit_extender_2
  assign bit_extender_3_out = {{16{1'b0}}, insanalyse_1_immediate16};  // Bit_Extender bit_extender_3
  assign bit_extender_4_out = {{6{1'b0}}, insanalyse_1_immediate26};  // Bit_Extender bit_extender_4
  Button Interupt0 (.out(Interupt0_out[0]));
  LED led_1 (.in(intr_1_irwt[0]));
  or or_1 (or_1_out, datahzd_1_nop, branch_1_pcsrc);
  ID_EX id_ex_1 (
    .PCDin(if_id_1_pcdout), .IRDin(if_id_1_irdout), .ALUOPDin(control_1_aluop), .PCDout(id_ex_1_pcdout),
    .IRDout(id_ex_1_irdout), .ALUOPDout(id_ex_1_aluopdout), .ALUYSrcDin(control_1_aluysrc),
    .ALUYSrcDout(id_ex_1_aluysrcdout), .ALUYSrc2Din(control_1_aluysrc2), .ALUYSrc2Dout(id_ex_1_aluysrc2dout),
    .Ext5to32Din(bit_extender_1_out), .Ext5to32Dout(id_ex_1_ext5to32dout),
    .SExt16to32Din(bit_extender_2_out), .SExt16to32Dout(id_ex_1_sext16to32dout),
    .Ext16to32Din(bit_extender_3_out), .Ext16to32Dout(id_ex_1_ext16to32dout), .RFR1Din(main_1_p9),
    .RFR1Dout(id_ex_1_rfr1dout), .RFR2Din(main_1_p10), .RFR2Dout(id_ex_1_rfr2dout),
    .PC_1Din(if_id_1_pc_1dout), .PC_1Dout(id_ex_1_pc_1dout), .DMWEDin(control_1_dmwe),
    .DMWEDout(id_ex_1_dmwedout), .PCAddSrcDin(control_1_pcaddsrc), .PCAddSrcDout(id_ex_1_pcaddsrcdout),
    .RFWEDin(control_1_rfwe), .RFWEDout(id_ex_1_rfwedout), .RFDinSrcDin(control_1_rfdinsrc),
    .RFDinSrcDout(id_ex_1_rfdinsrcdout), .SExt26to32Din(bit_extender_4_out),
    .SExt26to32Dout(id_ex_1_sext26to32dout), .BrInsDin(control_1_brins), .BrInsDout(id_ex_1_brinsdout),
    .WRegDin(multiplexer_7_out), .WRegDout(id_ex_1_wregdout), .SyscallDin(control_1_syscall),
    .SyscallDout(id_ex_1_syscalldout), .WE(1'b1), .Clk(Clk), .Rst(or_1_out), .a0Din(main_1_p7),
    .a0Dout(id_ex_1_a0dout), .RDTR1SrcDin(datahzd_1_rdtr1src), .RDTR1SrcDout(id_ex_1_rdtr1srcdout),
    .RDTR2SrcDin(datahzd_1_rdtr2src), .RDTR2SrcDout(id_ex_1_rdtr2srcdout), .loadDin(control_1_load),
    .loadDout(id_ex_1_loaddout), .v0Din(main_1_p6), .v0Dout(id_ex_1_v0dout), .INTCtlDin(control_1_intctl),
    .INTCtlDout(id_ex_1_intctldout), .CP01Din(EPC_q), .CP01Dout(id_ex_1_cp01dout), .CP00Din(intr_1_regout),
    .CP00Dout(id_ex_1_cp00dout), .BHTItemDin(if_id_1_bhtitemdout), .BHTItemDout(id_ex_1_bhtitemdout));
  Button Interupt1 (.out(Interupt0_out[1]));
  LED led_2 (.in(intr_1_irwt[1]));
  Multiplexer #(.width(32), .enable("false")) multiplexer_8 (
    .in0(id_ex_1_pcdout), .in1(main_1_p4), .out(multiplexer_8_out), .sel(mem_wb_1_intctldout[0]));
  Multiplexer #(.select(2), .width(32), .enable("false")) multiplexer_9 (
    .in0(id_ex_1_v0dout), .in1(main_1_p4), .in2(multiplexer_20_out), .in3(multiplexer_20_out),
    .out(multiplexer_9_out), .sel(id_ex_1_rdtr1srcdout));
  Multiplexer #(.select(2), .width(32), .enable("false")) multiplexer_10 (
    .in0(id_ex_1_rfr1dout), .in1(main_1_p4), .in2(multiplexer_20_out), .in3(multiplexer_20_out),
    .out(multiplexer_10_out), .sel(id_ex_1_rdtr1srcdout));
  Button Interupt3 (.out(Interupt0_out[3]));
  Button Interupt2 (.out(Interupt0_out[2]));
  LED led_3 (.in(intr_1_irwt[2]));
  LED led_4 (.in(intr_1_irwt[3]));
  Register #(.width(32)) EPC (.D(multiplexer_8_out), .en(or_2_out), .Q(EPC_q), .clk(Clk));  // open: clr
  or or_2 (or_2_out, mem_wb_1_intctldout[1], and_2_out);
  Multiplexer #(.width(32), .enable("false")) multiplexer_11 (
    .in0(32'h1), .in1(main_1_p4), .out(multiplexer_11_out), .sel(mem_wb_1_intctldout[2]));
  Multiplexer #(.select(2), .width(32), .enable("false")) multiplexer_12 (
    .in0(id_ex_1_a0dout), .in1(main_1_p4), .in2(multiplexer_20_out), .in3(multiplexer_20_out),
    .out(multiplexer_12_out), .sel(id_ex_1_rdtr2srcdout));
  Multiplexer #(.select(2), .width(32), .enable("false")) multiplexer_13 (
    .in0(id_ex_1_rfr2dout), .in1(main_1_p4), .in2(multiplexer_20_out), .in3(multiplexer_20_out),
    .out(multiplexer_13_out), .sel(id_ex_1_rdtr2srcdout));
  and and_2 (and_2_out, intr_1_intr, intr_1_res);
  Comparator #(.width(32), .mode("unsigned")) comparator_1 (
    .a(multiplexer_9_out), .b(32'ha), .eq(comparator_1_eq));  // open: gt, lt
  Multiplexer #(.select(2), .width(32), .enable("false")) multiplexer_14 (
    .in0(multiplexer_13_out), .in1(id_ex_1_ext5to32dout), .in2(id_ex_1_sext16to32dout),
    .in3(id_ex_1_ext16to32dout), .out(multiplexer_14_out), .sel(id_ex_1_aluysrcdout));
  Multiplexer #(.width(32), .enable("false")) multiplexer_15 (
    .in0({32{1'b0}}), .in1(id_ex_1_sext16to32dout), .out(multiplexer_15_out), .sel(id_ex_1_pcaddsrcdout));
  INTR intr_1 (
    .Clk(Clk), .Rst(Rst), .RegIn(multiplexer_11_out), .IEW(mem_wb_1_intctldout[4]),
    .INMW(mem_wb_1_intctldout[3]), .IRSRC(Interupt0_out), .IRNUM(intr_1_irnum), .INTR(intr_1_intr),
    .RegOut(intr_1_regout), .IRWT(intr_1_irwt), .IR(id_ex_1_pcdout), .PC(id_ex_1_irdout), .Res(intr_1_res));
  and and_3 (and_3_out, id_ex_1_syscalldout, comparator_1_eq);
  and and_4 (and_4_out, id_ex_1_syscalldout, ~comparator_1_eq);  // AND_Gate
  ALU alu_1 (
    .AluOP(id_ex_1_aluopdout), .X(multiplexer_10_out), .Equal(alu_1_equal), .Result(alu_1_result),
    .Y(multiplexer_16_out));  // open: Signed_Overflow, Result_2, UnSigned_Overflow
  Multiplexer #(.width(32), .disabled(0), .enable("false")) multiplexer_16 (
    .in0(multiplexer_14_out), .in1({32{1'b0}}), .out(multiplexer_16_out), .sel(id_ex_1_aluysrc2dout));
  Adder #(.width(32)) adder_4 (
    .a(multiplexer_15_out), .b(id_ex_1_pc_1dout), .out(adder_4_out), .cin(1'b0));  // open: cout
  // Probe on id_ex_1_irdout
  Adder #(.width(32)) adder_5 (.a(32'h1), .b(intr_1_irnum), .out(adder_5_out));  // open: cin, cout
  Branch branch_1 (
    .Equal(alu_1_equal), .Judge(alu_1_result[0]), .BrIns(id_ex_1_brinsdout), .BrPCSrc(branch_1_brpcsrc),
    .PCSrc(branch_1_pcsrc), .INTR(and_2_out), .RePCSrc2(branch_1_repcsrc2), .PostClr(branch_1_postclr),
    .BHTItem(id_ex_1_bhtitemdout), .PredictYes(comparator_2_eq),
    .ToBHT({branch_1_tobht_3, branch_1_tobht[7:6], branch_1_tobht_2, branch_1_tobht[3:0]}));
  Multiplexer #(.select(2), .width(32), .enable("false")) multiplexer_17 (
    .in0(multiplexer_10_out), .in1(id_ex_1_pc_1dout), .in2(adder_4_out), .in3(id_ex_1_sext26to32dout),
    .out(multiplexer_17_out), .sel(branch_1_brpcsrc));
  Comparator #(.width(32), .mode("unsigned")) comparator_2 (
    .a(if_id_1_pcdout), .b(multiplexer_18_out), .eq(comparator_2_eq));  // open: gt, lt
  Multiplexer #(.select(2), .width(32), .enable("false")) multiplexer_18 (
    .in0(multiplexer_17_out), .in1(id_ex_1_cp01dout), .in2(adder_5_out), .in3(adder_5_out),
    .out(multiplexer_18_out), .sel(branch_1_repcsrc2));
  not not_2 (not_2_out, branch_1_pcsrc);
  EX_MEM ex_mem_1 (
    .PCDin(id_ex_1_pcdout), .IRDin(id_ex_1_irdout), .DMWEDin(id_ex_1_dmwedout), .RFWEDin(id_ex_1_rfwedout),
    .RFDinSrcDin(id_ex_1_rfdinsrcdout), .PCDout(ex_mem_1_pcdout), .IRDout(ex_mem_1_irdout),
    .DMWEDout(ex_mem_1_dmwedout), .RFWEDout(ex_mem_1_rfwedout), .RFDinSrcDout(ex_mem_1_rfdinsrcdout),
    .ALUDin(alu_1_result), .ALUDout(ex_mem_1_aludout), .RFR2Din(multiplexer_13_out),
    .RFR2Dout(ex_mem_1_rfr2dout), .PCAddDin(adder_4_out), .PCAddDout(ex_mem_1_pcadddout),
    .WRegDin(id_ex_1_wregdout), .WRegDout(ex_mem_1_wregdout), .HaltDin(and_3_out),
    .HaltDout(ex_mem_1_haltdout), .DispDin(and_4_out), .DispDout(ex_mem_1_dispdout), .WE(1'b1), .Clk(Clk),
    .Rst(branch_1_postclr), .a0Din(multiplexer_12_out), .a0Dout(ex_mem_1_a0dout), .CP01Din(id_ex_1_cp01dout),
    .CP01Dout(ex_mem_1_cp01dout), .CP00Din(id_ex_1_cp00dout), .CP00Dout(ex_mem_1_cp00dout),
    .INTCtlDin(id_ex_1_intctldout), .INTCtlDout(ex_mem_1_intctldout));
  Multiplexer #(.width(32), .enable("false")) multiplexer_19 (
    .in0(adder_6_out), .in1(register_2_q), .out(multiplexer_19_out), .sel(not_2_out));
  Multiplexer #(.select(2), .width(32), .enable("false")) multiplexer_20 (
    .in0(ex_mem_1_pcadddout), .in2(ex_mem_1_aludout), .out(multiplexer_20_out), .sel(ex_mem_1_rfdinsrcdout));  // open: in1, in3
  // Probe on register_2_q
  Register #(.width(32)) register_2 (.D(multiplexer_19_out), .Q(register_2_q), .clk(Clk));  // open: en, clr
  RAM #(.addrWidth(10), .dataWidth(32), .bus("separate")) ram_1 (
    .addr(ex_mem_1_aludout[9:0]), .din(ex_mem_1_rfr2dout), .data(ram_1_data), .str(ex_mem_1_dmwedout),
    .sel(1'b1), .clk(Clk), .ld(1'b1), .clr(1'b0));
  // Probe on ex_mem_1_irdout
  Adder #(.width(32)) adder_6 (.a(32'h1), .b(register_2_q), .out(adder_6_out));  // open: cin, cout
  assign bit_extender_5_out = {{16{ram_1_data[15]}}, ram_1_data[15:0]};  // Bit_Extender bit_extender_5
  // Probe on mem_wb_1_irdout
  MEM_WB mem_wb_1 (
    .PCDin(ex_mem_1_pcdout), .IRDin(ex_mem_1_irdout), .RFWEDin(ex_mem_1_rfwedout),
    .RFDinSrcDin(ex_mem_1_rfdinsrcdout), .IRDout(mem_wb_1_irdout), .RFWEDout(main_1_p5),
    .RFDinSrcDout(mem_wb_1_rfdinsrcdout), .ALUDin(ex_mem_1_aludout), .ALUDout(mem_wb_1_aludout),
    .DMDin(ram_1_data), .DMDout(mem_wb_1_dmdout), .PCAddDin(ex_mem_1_pcadddout),
    .PCAddDout(mem_wb_1_pcadddout), .SExt16to32Din(bit_extender_5_out),
    .SExt16to32Dout(mem_wb_1_sext16to32dout), .WRegDin(ex_mem_1_wregdout), .WRegDout(main_1_p3),
    .HaltDin(ex_mem_1_haltdout), .HaltDout(Halt), .DispDin(ex_mem_1_dispdout), .DispDout(mem_wb_1_dispdout),
    .WE(1'b1), .Clk(Clk), .Rst(Rst), .a0Din(ex_mem_1_a0dout), .a0Dout(mem_wb_1_a0dout),
    .CP01Din(ex_mem_1_cp01dout), .CP01Dout(mem_wb_1_cp01dout), .CP00Din(ex_mem_1_cp00dout),
    .CP00Dout(mem_wb_1_cp00dout), .INTCtlDin(ex_mem_1_intctldout), .INTCtlDout(mem_wb_1_intctldout));  // open: PCDout
  Multiplexer #(.width(32), .enable("false")) multiplexer_21 (
    .in0(mem_wb_1_cp00dout), .in1(mem_wb_1_cp01dout), .out(multiplexer_21_out), .sel(mem_wb_1_intctldout[6]));
  Multiplexer #(.select(2), .width(32), .enable("false")) multiplexer_22 (
    .in0(mem_wb_1_pcadddout), .in1(mem_wb_1_dmdout), .in2(mem_wb_1_aludout), .in3(mem_wb_1_sext16to32dout),
    .out(multiplexer_22_out), .sel(mem_wb_1_rfdinsrcdout));
  and and_5 (Clk, ~Halt, ComClk);  // AND_Gate
  Multiplexer #(.width(32), .enable("false")) multiplexer_23 (
    .in0(multiplexer_22_out), .in1(multiplexer_21_out), .out(main_1_p4), .sel(mem_wb_1_intctldout[5]));

  // Notes on the sheet:
  //   contents of rom_1 (hex, n*v repeats v):
  //   20110001 8000c05 20110001 20120002 20130003 8000c09 20110001 20120002 20130003 8000c0d 20110001
  //   20120002 20130003 8000c11 20110001 20120002 20130003 c000cb8 20100001 20110001 118fc0 112020
  //   20020022 c 118882 12200001 8000c15 112020 20020022 c 20110001 118880 112020 20020022 c 12200001
  //   8000c1f 20110001 118fc0 112020 20020022 c 1188c3 112020 20020022 c 118903 112020 20020022 c 118903
  //   112020 20020022 c 118903 112020 20020022 c 118903 112020 20020022 c 118903 112020 20020022 c 118903
  //   112020 20020022 c 118903 112020 20020022 c 20100001 109fc0 139fc3 8021 2012000c 24160003 26100001
  //   3210000f 20080008 20090001 139900 2709825 132020 20020022 c 1094022 1500fff9 22100001 2018000f
  //   2188024 108700 20080008 20090001 139902 2709825 132021 20020022 c 1094022 1500fff9 108702 2c9b022
  //   12c00001 8000c50 4020 1084027 84400 3508ffff 82021 20020022 c 2010ffff 20110000 ae300000 22100001
  //   22310004 ae300000 22100001 22310004 ae300000 22100001 22310004 ae300000 22100001 22310004 ae300000
  //   22100001 22310004 ae300000 22100001 22310004 ae300000 22100001 22310004 ae300000 22100001 22310004
  //   ae300000 22100001 22310004 ae300000 22100001 22310004 ae300000 22100001 22310004 ae300000 22100001
  //   22310004 ae300000 22100001 22310004 ae300000 22100001 22310004 ae300000 22100001 22310004 ae300000
  //   22100001 22310004 22100001 8020 2011003c 8e130000 8e340000 274402a 11000002 ae330000 ae140000
  //   2231fffc 1611fff8 102020 20020022 c 22100004 2011003c 1611fff2 2002000a c 20100000 22100001 102020
  //   20020022 c 22100002 102020 20020022 c 22100003 102020 20020022 c 22100004 102020 20020022 c 22100005
  //   102020 20020022 c 22100006 102020 20020022 c 22100007 102020 20020022 c 22100008 102020 20020022
  //   20020022 c 3e00008
endmodule

module InsAnalyse (
  input  [31:0] Ins,
  output [5:0] OP,
  output [4:0] Rs,
  output [4:0] Rt,
  output [4:0] Rd,
  output [4:0] Shamt,
  output [5:0] funct,
  output [15:0] Immediate16,
  output [25:0] Immediate26
);


  assign funct = Ins[5:0];
  assign Immediate16 = Ins[15:0];
  assign Immediate26 = Ins[25:0];
  assign OP = Ins[31:26];
  assign Rd = Ins[15:11];
  assign Rs = Ins[25:21];
  assign Rt = Ins[20:16];
  assign Shamt = Ins[10:6];
endmodule

module Control (
  input  [4:0] Rs,
  input  [4:0] Rd,
  input  [5:0] OP,
  input  [5:0] funct,
  output [6:0] INTCtl,
  output [31:0] AllIns,
  output [6:0] BrIns,
  output load,
  output PCAddSrc,
  output RFR1Src,
  output [1:0] RFRWSrc,
  output [1:0] RFDinSrc,
  output RFWE,
  output [1:0] ALUYSrc,
  output ALUYSrc2,
  output [3:0] ALUOP,
  output DMWE,
  output Syscall
);

  wire decoder_1_out0, decoder_1_out1, decoder_2_out0, decoder_2_out16, decoder_4_out0, decoder_6_out0,
       decoder_6_out1, mtc0;

  Decoder #(.enable("false")) decoder_1 (.out0(decoder_1_out0), .out1(decoder_1_out1), .sel(OP[5]));
  or or_1 (PCAddSrc, AllIns[6], AllIns[5], AllIns[9]);
  nor nor_1 (RFDinSrc[1], AllIns[11], AllIns[7]);
  or or_2 (RFDinSrc[0], AllIns[11], AllIns[10]);
  or or_3 (ALUYSrc2, AllIns[9], mtc0);
  Decoder #(.select(5), .disabled(0)) decoder_2 (
    .out0(decoder_2_out0), .out1(AllIns[9]), .out2(AllIns[8]), .out3(AllIns[7]), .out4(AllIns[6]),
    .out5(AllIns[5]), .out8(AllIns[4]), .out9(AllIns[3]), .out10(AllIns[2]), .out12(AllIns[1]),
    .out13(AllIns[0]), .out16(decoder_2_out16), .sel(OP[4:0]), .en(decoder_1_out0));  // open: out6, out7, out11, out14, out15, out17, out18, out19, out20, out21, out22, out23, out24, out25, out26, out27, out28, out29, out30, out31
  Decoder #(.select(5), .disabled(0)) decoder_3 (
    .out1(AllIns[10]), .out3(AllIns[11]), .out11(AllIns[12]), .sel(OP[4:0]), .en(decoder_1_out1));  // open: out0, out2, out4, out5, out6, out7, out8, out9, out10, out12, out13, out14, out15, out16, out17, out18, out19, out20, out21, out22, out23, out24, out25, out26, out27, out28, out29, out30, out31
  or or_4 (RFR1Src, AllIns[19], AllIns[17], AllIns[18], AllIns[16], AllIns[15], mtc0);
  or or_5 (ALUYSrc[1], AllIns[4], AllIns[3], AllIns[1], AllIns[0], AllIns[11], AllIns[12], AllIns[2], AllIns[10]);
  or or_6 (ALUYSrc[0], AllIns[1], AllIns[19], AllIns[17], AllIns[18], AllIns[0]);
  or or_7 (ALUOP[3], AllIns[24], AllIns[0], AllIns[25], AllIns[26], AllIns[2], AllIns[27], AllIns[9]);
  nor nor_2 (RFWE, AllIns[12], AllIns[6], AllIns[5], AllIns[8], AllIns[14], AllIns[13], AllIns[9], mtc0, AllIns[31]);
  or or_8 (ALUOP[1], AllIns[23], AllIns[1], AllIns[18], AllIns[22], AllIns[25], AllIns[6], AllIns[5], AllIns[26], AllIns[2], AllIns[15], AllIns[9]);
  or or_9 (RFRWSrc[0], AllIns[20], AllIns[21], AllIns[23], AllIns[19], AllIns[17], AllIns[18], AllIns[22], AllIns[24], AllIns[25], AllIns[26], AllIns[27], AllIns[16], AllIns[15]);
  or or_10 (ALUOP[2], AllIns[20], AllIns[4], AllIns[3], AllIns[21], AllIns[23], AllIns[1], AllIns[22], AllIns[11], AllIns[12], AllIns[6], AllIns[5], AllIns[27], AllIns[10]);
  or or_11 (ALUOP[0], AllIns[20], AllIns[4], AllIns[3], AllIns[21], AllIns[23], AllIns[1], AllIns[17], AllIns[11], AllIns[12], AllIns[26], AllIns[2], AllIns[10], AllIns[9]);
  Decoder #(.disabled(0)) decoder_4 (.out0(decoder_4_out0), .out1(AllIns[31]), .sel(funct[4]), .en(decoder_2_out16));
  Decoder #(.disabled(0)) decoder_5 (.out0(AllIns[30]), .out1(mtc0), .sel(Rs[2]), .en(decoder_4_out0));
  Decoder #(.disabled(0)) decoder_6 (.out0(decoder_6_out0), .out1(decoder_6_out1), .sel(funct[5]), .en(decoder_2_out0));
  Decoder #(.disabled(0)) decoder_7 (.out0(AllIns[28]), .out1(AllIns[29]), .sel(Rd[0]), .en(mtc0));
  Decoder #(.select(5), .disabled(0)) decoder_8 (
    .out0(AllIns[19]), .out2(AllIns[18]), .out3(AllIns[17]), .out4(AllIns[16]), .out6(AllIns[15]),
    .out8(AllIns[14]), .out12(AllIns[13]), .sel(funct[4:0]), .en(decoder_6_out0));  // open: out1, out5, out7, out9, out10, out11, out13, out14, out15, out16, out17, out18, out19, out20, out21, out22, out23, out24, out25, out26, out27, out28, out29, out30, out31
  Decoder #(.select(5), .disabled(0)) decoder_9 (
    .out0(AllIns[20]), .out1(AllIns[21]), .out2(AllIns[22]), .out4(AllIns[23]), .out5(AllIns[24]),
    .out7(AllIns[25]), .out10(AllIns[26]), .out11(AllIns[27]), .sel(funct[4:0]), .en(decoder_6_out1));  // open: out3, out6, out8, out9, out12, out13, out14, out15, out16, out17, out18, out19, out20, out21, out22, out23, out24, out25, out26, out27, out28, out29, out30, out31
  or or_12 (load, AllIns[10], AllIns[11]);
  or or_13 (INTCtl[4], AllIns[28], AllIns[31]);

  assign BrIns = {AllIns[31], AllIns[14], AllIns[7], AllIns[8], AllIns[9], AllIns[5], AllIns[6]};
  assign DMWE = AllIns[12];
  assign {INTCtl[6:5], INTCtl[3:0]} = {Rd[0], AllIns[30], {2{AllIns[28]}}, {2{AllIns[29]}}};
  assign RFRWSrc[1] = AllIns[7];
  assign Syscall = AllIns[13];

  // Other names for the same wires on the sheet: ori = AllIns[0]; andi = AllIns[1]; slti = AllIns[2];
  //   addiu = AllIns[3]; addi = AllIns[4]; bne = AllIns[5]; beq = AllIns[6]; jal = AllIns[7]; j = AllIns[8];
  //   bgez = AllIns[9]; lh = AllIns[10]; lw = AllIns[11]; sw = AllIns[12]; jr = AllIns[14]; srlv = AllIns[15];
  //   sllv = AllIns[16]; sra = AllIns[17]; srl = AllIns[18]; sll = AllIns[19]; add = AllIns[20]; addu = AllIns[21];
  //   sub = AllIns[22]; and = AllIns[23]; or = AllIns[24]; nor = AllIns[25]; slt = AllIns[26]; sltu = AllIns[27];
  //   eret = AllIns[31]; EPCEn = AllIns[29]; EPCSrc = AllIns[29]; mtc01 = AllIns[29]; IEIMSrc = AllIns[28];
  //   INMW = AllIns[28]; mtc00 = AllIns[28]; IEW = INTCtl[4]; mfc0 = AllIns[30]; Rd_t = Rd[0]; Rs_t = Rs[2]
endmodule

module Branch (
  input  Equal,
  input  Judge,
  input  INTR,
  input  PredictYes,
  input  [6:0] BrIns,
  input  [8:0] BHTItem,
  output [1:0] RePCSrc2,
  output PostClr,
  output [10:0] ToBHT,
  output [1:0] BrPCSrc,
  output PCSrc
);

  wire and_1_out, and_2_out, and_3_out, and_4_out, and_5_out, and_6_out, and_7_out, and_8_out, and_9_out,
       HitAndYes, HitButWrong, not_1_out, not_2_out, not_3_out, or_4_out;
  wire [1:0] multiplexer_2_out, multiplexer_3_out, multiplexer_4_out;

  not not_1 (not_1_out, Judge);
  not not_2 (not_2_out, Equal);
  and and_1 (and_1_out, BrIns[0], Equal);
  and and_2 (and_2_out, BrIns[1], not_3_out);
  not not_3 (not_3_out, Equal);
  and and_3 (and_3_out, BrIns[0], Equal);
  and and_4 (and_4_out, BrIns[1], not_2_out);
  and and_5 (and_5_out, BrIns[2], not_1_out);
  and and_6 (and_6_out, BrIns[2], not_1_out);
  or or_1 (BrPCSrc[1], and_3_out, and_4_out, BrIns[3], BrIns[4], and_5_out);
  nor nor_1 (BrPCSrc[0], and_6_out, and_1_out, and_2_out, BrIns[5]);
  or or_2 (ToBHT[3], ToBHT[7], HitAndYes, HitButWrong);
  or or_3 (ToBHT[2], HitAndYes, ToBHT[7]);
  and and_7 (and_7_out, BrIns[0], Equal);
  and and_8 (and_8_out, BrIns[1], ~Equal);  // AND_Gate
  and and_9 (and_9_out, BrIns[2], ~Judge);  // AND_Gate
  Multiplexer #(.width(3), .enable("false")) multiplexer_1 (
    .in0(BHTItem[8:6]), .in1(BHTItem[5:3]), .out(ToBHT[10:8]), .sel(BHTItem[0]));
  Multiplexer #(.select(2), .width(2), .enable("false")) multiplexer_2 (
    .in0(2'b00), .in1(2'b00), .in2(2'b01), .in3(2'b10), .out(multiplexer_2_out), .sel(BHTItem[2:1]));
  Multiplexer #(.select(2), .width(2), .enable("false")) multiplexer_3 (
    .in0(2'b01), .in1(2'b10), .in2(2'b11), .in3(2'b11), .out(multiplexer_3_out), .sel(BHTItem[2:1]));
  Multiplexer #(.width(2), .enable("false")) multiplexer_4 (
    .in0(multiplexer_2_out), .in1(multiplexer_3_out), .out(multiplexer_4_out), .sel(PredictYes));
  and and_10 (HitButWrong, BHTItem[0], ~PredictYes);  // AND_Gate
  Multiplexer #(.width(2), .enable("false")) multiplexer_5 (
    .in0(2'b10), .in1(multiplexer_4_out), .out(ToBHT[5:4]), .sel(BHTItem[0]));
  or or_4 (or_4_out, and_7_out, and_8_out, and_9_out, BrIns[3], BrIns[4], BrIns[5], BrIns[6], INTR);
  and and_11 (ToBHT[7], ~BHTItem[0], or_4_out);  // AND_Gate
  and and_12 (HitAndYes, BHTItem[0], PredictYes);
  or or_5 (PCSrc, ToBHT[7], HitButWrong);

  assign PostClr = INTR;
  assign RePCSrc2 = {INTR, BrIns[6]};
  assign {ToBHT[6], ToBHT[1:0]} = {3{ToBHT[7]}};

  // Other names for the same wires on the sheet: Hit = BHTItem[0]; PredictIn[1:0] = BHTItem[2:1];
  //   HitNum[2:0] = BHTItem[5:3]; InsertNum[2:0] = BHTItem[8:6]; beq = BrIns[0]; bne = BrIns[1]; bgez = BrIns[2];
  //   j = BrIns[3]; jal = BrIns[4]; jr = BrIns[5]; eret = BrIns[6]; we_lru = ToBHT[2]; we_predict = ToBHT[3];
  //   write_predict[1:0] = ToBHT[5:4]; NotHitButBr = ToBHT[7]; we_branch = ToBHT[7]; we_pc = ToBHT[7];
  //   we_valid = ToBHT[7]; write_valid = ToBHT[7]; write_address[2:0] = ToBHT[10:8]
endmodule

module IF_ID (
  input  [8:0] BHTItemDin,
  input  [31:0] PC_1Din,
  input  [31:0] PCDin,
  input  [31:0] IRDin,
  input  WE,
  input  Clk,
  input  Rst,
  output [8:0] BHTItemDout,
  output [31:0] PC_1Dout,
  output [31:0] PCDout,
  output [31:0] IRDout
);

  wire d_ff_1_q;

  Register #(.width(9)) BHTItem (.D(BHTItemDin), .en(WE), .Q(BHTItemDout), .clk(Clk), .clr(d_ff_1_q));
  Register #(.width(32)) PC_1 (.D(PC_1Din), .en(WE), .Q(PC_1Dout), .clk(Clk), .clr(d_ff_1_q));
  Register #(.width(32)) PC (.D(PCDin), .en(WE), .Q(PCDout), .clk(Clk), .clr(d_ff_1_q));
  Register #(.width(32)) IR (.D(IRDin), .en(WE), .Q(IRDout), .clk(Clk), .clr(d_ff_1_q));
  D_Flip_Flop d_ff_1 (.clk(Clk), .D(Rst), .Q(d_ff_1_q), .reset(d_ff_1_q));  // open: Qn, preset, en
endmodule

module ID_EX (
  input  [8:0] BHTItemDin,
  input  [31:0] CP01Din,
  input  [31:0] CP00Din,
  input  [6:0] INTCtlDin,
  input  loadDin,
  input  [1:0] RDTR1SrcDin,
  input  [1:0] RDTR2SrcDin,
  input  [31:0] a0Din,
  input  [31:0] v0Din,
  input  SyscallDin,
  input  [31:0] PC_1Din,
  input  [31:0] PCDin,
  input  [31:0] IRDin,
  input  [3:0] ALUOPDin,
  input  [1:0] ALUYSrcDin,
  input  ALUYSrc2Din,
  input  [31:0] RFR1Din,
  input  [31:0] RFR2Din,
  input  [31:0] Ext5to32Din,
  input  [31:0] SExt16to32Din,
  input  [31:0] Ext16to32Din,
  input  [31:0] SExt26to32Din,
  input  DMWEDin,
  input  PCAddSrcDin,
  input  RFWEDin,
  input  [1:0] RFDinSrcDin,
  input  [6:0] BrInsDin,
  input  [4:0] WRegDin,
  input  WE,
  input  Clk,
  input  Rst,
  output [8:0] BHTItemDout,
  output [31:0] CP01Dout,
  output [31:0] CP00Dout,
  output [6:0] INTCtlDout,
  output loadDout,
  output [1:0] RDTR1SrcDout,
  output [1:0] RDTR2SrcDout,
  output [31:0] a0Dout,
  output [31:0] v0Dout,
  output SyscallDout,
  output [31:0] PC_1Dout,
  output [31:0] PCDout,
  output [31:0] IRDout,
  output [3:0] ALUOPDout,
  output [1:0] ALUYSrcDout,
  output ALUYSrc2Dout,
  output [31:0] RFR1Dout,
  output [31:0] RFR2Dout,
  output [31:0] Ext5to32Dout,
  output [31:0] SExt16to32Dout,
  output [31:0] Ext16to32Dout,
  output [31:0] SExt26to32Dout,
  output DMWEDout,
  output PCAddSrcDout,
  output RFWEDout,
  output [1:0] RFDinSrcDout,
  output [6:0] BrInsDout,
  output [4:0] WRegDout
);

  wire d_ff_1_q;

  Register #(.width(9)) BHTItem (.D(BHTItemDin), .en(WE), .Q(BHTItemDout), .clk(Clk), .clr(d_ff_1_q));
  Register #(.width(32)) CP01 (.D(CP01Din), .en(WE), .Q(CP01Dout), .clk(Clk), .clr(d_ff_1_q));
  Register #(.width(32)) CP00 (.D(CP00Din), .en(WE), .Q(CP00Dout), .clk(Clk), .clr(d_ff_1_q));
  Register #(.width(7)) INTCtl (.D(INTCtlDin), .en(WE), .Q(INTCtlDout), .clk(Clk), .clr(d_ff_1_q));
  Register #(.width(1)) load (.D(loadDin), .en(WE), .Q(loadDout), .clk(Clk), .clr(d_ff_1_q));
  Register #(.width(2)) RDTR1Src (.D(RDTR1SrcDin), .en(WE), .Q(RDTR1SrcDout), .clk(Clk), .clr(d_ff_1_q));
  Register #(.width(2)) RDTR2Src (.D(RDTR2SrcDin), .en(WE), .Q(RDTR2SrcDout), .clk(Clk), .clr(d_ff_1_q));
  Register #(.width(32)) a0 (.D(a0Din), .en(WE), .Q(a0Dout), .clk(Clk), .clr(d_ff_1_q));
  Register #(.width(32)) v0 (.D(v0Din), .en(WE), .Q(v0Dout), .clk(Clk), .clr(d_ff_1_q));
  Register #(.width(1)) Syscall (.D(SyscallDin), .en(WE), .Q(SyscallDout), .clk(Clk), .clr(d_ff_1_q));
  Register #(.width(32)) PC_1 (.D(PC_1Din), .en(WE), .Q(PC_1Dout), .clk(Clk), .clr(d_ff_1_q));
  Register #(.width(32)) PC (.D(PCDin), .en(WE), .Q(PCDout), .clk(Clk), .clr(d_ff_1_q));
  Register #(.width(32)) IR (.D(IRDin), .en(WE), .Q(IRDout), .clk(Clk), .clr(d_ff_1_q));
  Register #(.width(4)) ALUOP (.D(ALUOPDin), .en(WE), .Q(ALUOPDout), .clk(Clk), .clr(d_ff_1_q));
  Register #(.width(2)) ALUYSrc (.D(ALUYSrcDin), .en(WE), .Q(ALUYSrcDout), .clk(Clk), .clr(d_ff_1_q));
  Register #(.width(1)) ALUYSrc2 (.D(ALUYSrc2Din), .en(WE), .Q(ALUYSrc2Dout), .clk(Clk), .clr(d_ff_1_q));
  Register #(.width(32)) RFR1 (.D(RFR1Din), .en(WE), .Q(RFR1Dout), .clk(Clk), .clr(d_ff_1_q));
  Register #(.width(32)) RFR2 (.D(RFR2Din), .en(WE), .Q(RFR2Dout), .clk(Clk), .clr(d_ff_1_q));
  Register #(.width(32)) Ext5to32 (.D(Ext5to32Din), .en(WE), .Q(Ext5to32Dout), .clk(Clk), .clr(d_ff_1_q));
  Register #(.width(32)) SExt16to32 (.D(SExt16to32Din), .en(WE), .Q(SExt16to32Dout), .clk(Clk), .clr(d_ff_1_q));
  Register #(.width(32)) Ext16to32 (.D(Ext16to32Din), .en(WE), .Q(Ext16to32Dout), .clk(Clk), .clr(d_ff_1_q));
  Register #(.width(32)) SExt26to32 (.D(SExt26to32Din), .en(WE), .Q(SExt26to32Dout), .clk(Clk), .clr(d_ff_1_q));
  Register #(.width(1)) DMWE (.D(DMWEDin), .en(WE), .Q(DMWEDout), .clk(Clk), .clr(d_ff_1_q));
  Register #(.width(1)) PCAddSrc (.D(PCAddSrcDin), .en(WE), .Q(PCAddSrcDout), .clk(Clk), .clr(d_ff_1_q));
  Register #(.width(1)) RFWE (.D(RFWEDin), .en(WE), .Q(RFWEDout), .clk(Clk), .clr(d_ff_1_q));
  Register #(.width(2)) RFDinSrc (.D(RFDinSrcDin), .en(WE), .Q(RFDinSrcDout), .clk(Clk), .clr(d_ff_1_q));
  Register #(.width(7)) BrIns (.D(BrInsDin), .en(WE), .Q(BrInsDout), .clk(Clk), .clr(d_ff_1_q));
  Register #(.width(5)) WReg (.D(WRegDin), .en(WE), .Q(WRegDout), .clk(Clk), .clr(d_ff_1_q));
  D_Flip_Flop d_ff_1 (.clk(Clk), .D(Rst), .Q(d_ff_1_q), .reset(d_ff_1_q));  // open: Qn, preset, en
endmodule

module EX_MEM (
  input  [31:0] CP01Din,
  input  [31:0] CP00Din,
  input  [6:0] INTCtlDin,
  input  [31:0] a0Din,
  input  DispDin,
  input  HaltDin,
  input  [31:0] PCDin,
  input  [31:0] IRDin,
  input  DMWEDin,
  input  RFWEDin,
  input  [1:0] RFDinSrcDin,
  input  [31:0] ALUDin,
  input  [31:0] RFR2Din,
  input  [31:0] PCAddDin,
  input  [4:0] WRegDin,
  input  WE,
  input  Clk,
  input  Rst,
  output [31:0] CP01Dout,
  output [31:0] CP00Dout,
  output [6:0] INTCtlDout,
  output [31:0] a0Dout,
  output DispDout,
  output HaltDout,
  output [31:0] PCDout,
  output [31:0] IRDout,
  output DMWEDout,
  output RFWEDout,
  output [1:0] RFDinSrcDout,
  output [31:0] ALUDout,
  output [31:0] RFR2Dout,
  output [31:0] PCAddDout,
  output [4:0] WRegDout
);

  wire d_ff_1_q;

  Register #(.width(32)) CP01 (.D(CP01Din), .en(WE), .Q(CP01Dout), .clk(Clk), .clr(d_ff_1_q));
  Register #(.width(32)) CP00 (.D(CP00Din), .en(WE), .Q(CP00Dout), .clk(Clk), .clr(d_ff_1_q));
  Register #(.width(7)) INTCtl (.D(INTCtlDin), .en(WE), .Q(INTCtlDout), .clk(Clk), .clr(d_ff_1_q));
  Register #(.width(32)) a0 (.D(a0Din), .en(WE), .Q(a0Dout), .clk(Clk), .clr(d_ff_1_q));
  Register #(.width(1)) Disp (.D(DispDin), .en(WE), .Q(DispDout), .clk(Clk), .clr(d_ff_1_q));
  Register #(.width(1)) Halt (.D(HaltDin), .en(WE), .Q(HaltDout), .clk(Clk), .clr(d_ff_1_q));
  Register #(.width(32)) PC (.D(PCDin), .en(WE), .Q(PCDout), .clk(Clk), .clr(d_ff_1_q));
  Register #(.width(32)) IR (.D(IRDin), .en(WE), .Q(IRDout), .clk(Clk), .clr(d_ff_1_q));
  Register #(.width(1)) DMWE (.D(DMWEDin), .en(WE), .Q(DMWEDout), .clk(Clk), .clr(d_ff_1_q));
  Register #(.width(1)) RFWE (.D(RFWEDin), .en(WE), .Q(RFWEDout), .clk(Clk), .clr(d_ff_1_q));
  Register #(.width(2)) RFDinSrc (.D(RFDinSrcDin), .en(WE), .Q(RFDinSrcDout), .clk(Clk), .clr(d_ff_1_q));
  Register #(.width(32)) ALU (.D(ALUDin), .en(WE), .Q(ALUDout), .clk(Clk), .clr(d_ff_1_q));
  Register #(.width(32)) RFR2 (.D(RFR2Din), .en(WE), .Q(RFR2Dout), .clk(Clk), .clr(d_ff_1_q));
  Register #(.width(32)) PCAdd (.D(PCAddDin), .en(WE), .Q(PCAddDout), .clk(Clk), .clr(d_ff_1_q));
  Register #(.width(5)) WReg (.D(WRegDin), .en(WE), .Q(WRegDout), .clk(Clk), .clr(d_ff_1_q));
  D_Flip_Flop d_ff_1 (.clk(Clk), .D(Rst), .Q(d_ff_1_q), .reset(d_ff_1_q));  // open: Qn, preset, en
endmodule

module MEM_WB (
  input  [31:0] CP01Din,
  input  [31:0] CP00Din,
  input  [6:0] INTCtlDin,
  input  [31:0] a0Din,
  input  DispDin,
  input  HaltDin,
  input  [31:0] PCDin,
  input  [31:0] IRDin,
  input  RFWEDin,
  input  [1:0] RFDinSrcDin,
  input  [31:0] ALUDin,
  input  [31:0] DMDin,
  input  [31:0] SExt16to32Din,
  input  [31:0] PCAddDin,
  input  [4:0] WRegDin,
  input  WE,
  input  Clk,
  input  Rst,
  output [31:0] CP01Dout,
  output [31:0] CP00Dout,
  output [6:0] INTCtlDout,
  output [31:0] a0Dout,
  output DispDout,
  output HaltDout,
  output [31:0] PCDout,
  output [31:0] IRDout,
  output RFWEDout,
  output [1:0] RFDinSrcDout,
  output [31:0] ALUDout,
  output [31:0] DMDout,
  output [31:0] SExt16to32Dout,
  output [31:0] PCAddDout,
  output [4:0] WRegDout
);

  wire d_ff_1_q;

  Register #(.width(32)) CP01 (.D(CP01Din), .en(WE), .Q(CP01Dout), .clk(Clk), .clr(d_ff_1_q));
  Register #(.width(32)) CP00 (.D(CP00Din), .en(WE), .Q(CP00Dout), .clk(Clk), .clr(d_ff_1_q));
  Register #(.width(7)) INTCtl (.D(INTCtlDin), .en(WE), .Q(INTCtlDout), .clk(Clk), .clr(d_ff_1_q));
  Register #(.width(32)) a0 (.D(a0Din), .en(WE), .Q(a0Dout), .clk(Clk), .clr(d_ff_1_q));
  Register #(.width(1)) Disp (.D(DispDin), .en(WE), .Q(DispDout), .clk(Clk), .clr(d_ff_1_q));
  Register #(.width(1)) Halt (.D(HaltDin), .en(WE), .Q(HaltDout), .clk(Clk), .clr(d_ff_1_q));
  Register #(.width(32)) PC (.D(PCDin), .en(WE), .Q(PCDout), .clk(Clk), .clr(d_ff_1_q));
  Register #(.width(32)) IR (.D(IRDin), .en(WE), .Q(IRDout), .clk(Clk), .clr(d_ff_1_q));
  Register #(.width(1)) RFWE (.D(RFWEDin), .en(WE), .Q(RFWEDout), .clk(Clk), .clr(d_ff_1_q));
  Register #(.width(2)) RFDinSrc (.D(RFDinSrcDin), .en(WE), .Q(RFDinSrcDout), .clk(Clk), .clr(d_ff_1_q));
  Register #(.width(32)) ALU (.D(ALUDin), .en(WE), .Q(ALUDout), .clk(Clk), .clr(d_ff_1_q));
  Register #(.width(32)) DM (.D(DMDin), .en(WE), .Q(DMDout), .clk(Clk), .clr(d_ff_1_q));
  Register #(.width(32)) SExt16to32 (.D(SExt16to32Din), .en(WE), .Q(SExt16to32Dout), .clk(Clk), .clr(d_ff_1_q));
  Register #(.width(32)) PCAdd (.D(PCAddDin), .en(WE), .Q(PCAddDout), .clk(Clk), .clr(d_ff_1_q));
  Register #(.width(5)) WReg (.D(WRegDin), .en(WE), .Q(WRegDout), .clk(Clk), .clr(d_ff_1_q));
  D_Flip_Flop d_ff_1 (.clk(Clk), .D(Rst), .Q(d_ff_1_q), .reset(d_ff_1_q));  // open: Qn, preset, en
endmodule

module DataHzd (
  input  [4:0] EX_WReg,
  input  EX_WE,
  input  [4:0] MEM_WReg,
  input  [4:0] Rs,
  input  MEM_WE,
  input  [4:0] Rt,
  input  [31:0] AllIns,
  input  load,
  output Nop,
  output Stop,
  output [1:0] RDTR1Src,
  output [1:0] RDTR2Src
);

  wire and_1_out, and_6_out, and_7_out, and_8_out, and_9_out, and_10_out, and_11_out, and_12_out, and_13_out,
       and_14_out, and_15_out, and_16_out, and_18_out, and_19_out, and_20_out, and_21_out, and_22_out,
       and_23_out, and_24_out, and_25_out, comparator_1_eq, comparator_2_eq, comparator_3_eq,
       comparator_4_eq, EXRsEqu, EXRtEqu, MEMRsEqu, MEMRtEqu, or_3_out, or_4_out, or_5_out, or_6_out,
       or_7_out, or_8_out, or_9_out, or_10_out, or_11_out, or_12_out, or_13_out, or_14_out, or_15_out,
       or_16_out, or_17_out, or_20_out, or_21_out, or_22_out, or_23_out, or_24_out, or_25_out, or_26_out,
       or_27_out, RsZero, RtZero;
  wire [4:0] EX_WReg_t, MEM_WReg_t, Rs_t, Rt_t;

  Multiplexer #(.width(5), .enable("false")) multiplexer_1 (
    .in0({5{1'b0}}), .in1(EX_WReg), .out(EX_WReg_t), .sel(EX_WE));
  Multiplexer #(.width(5), .enable("false")) multiplexer_2 (
    .in0({5{1'b0}}), .in1(MEM_WReg), .out(MEM_WReg_t), .sel(MEM_WE));
  or or_1 (RsZero, Rs_t[0], Rs_t[1], Rs_t[2], Rs_t[3], Rs_t[4]);
  or or_2 (RtZero, Rt_t[0], Rt_t[1], Rt_t[2], Rt_t[3], Rt_t[4]);
  Comparator #(.width(5), .mode("unsigned")) comparator_1 (
    .a(EX_WReg_t), .b(Rs_t), .eq(comparator_1_eq));  // open: gt, lt
  Comparator #(.width(5), .mode("unsigned")) comparator_2 (
    .a(EX_WReg_t), .b(Rt_t), .eq(comparator_2_eq));  // open: gt, lt
  Comparator #(.width(5), .mode("unsigned")) comparator_3 (
    .a(MEM_WReg_t), .b(Rs_t), .eq(comparator_3_eq));  // open: gt, lt
  Comparator #(.width(5), .mode("unsigned")) comparator_4 (
    .a(MEM_WReg_t), .b(Rt_t), .eq(comparator_4_eq));  // open: gt, lt
  or or_3 (or_3_out, AllIns[5], AllIns[6], AllIns[12]);
  or or_4 (or_4_out, AllIns[17], AllIns[18], AllIns[19]);
  or or_5 (or_5_out, AllIns[17], AllIns[18], AllIns[19]);
  or or_6 (or_6_out, AllIns[0], AllIns[1], AllIns[2], AllIns[3], AllIns[4], AllIns[14], AllIns[9], AllIns[10], AllIns[11]);
  or or_7 (or_7_out, AllIns[15], AllIns[16]);
  or or_8 (or_8_out, AllIns[5], AllIns[6], AllIns[12]);
  or or_9 (or_9_out, AllIns[15], AllIns[16]);
  or or_10 (or_10_out, AllIns[5], AllIns[6], AllIns[12]);
  or or_11 (or_11_out, AllIns[15], AllIns[16], AllIns[20], AllIns[21], AllIns[22], AllIns[23], AllIns[24], AllIns[25], AllIns[26], AllIns[27], AllIns[13]);
  or or_12 (or_12_out, EXRsEqu, EXRtEqu);
  or or_13 (or_13_out, AllIns[0], AllIns[1], AllIns[2], AllIns[3], AllIns[4], AllIns[14], AllIns[9], AllIns[10], AllIns[11]);
  and and_1 (and_1_out, or_5_out, EXRtEqu);
  or or_14 (or_14_out, AllIns[20], AllIns[21], AllIns[22], AllIns[23], AllIns[24], AllIns[25], AllIns[26], AllIns[27], AllIns[13]);
  or or_15 (or_15_out, AllIns[20], AllIns[21], AllIns[22], AllIns[23], AllIns[24], AllIns[25], AllIns[26], AllIns[27], AllIns[13]);
  and and_2 (EXRsEqu, RsZero, comparator_1_eq);
  and and_3 (EXRtEqu, RtZero, comparator_2_eq);
  and and_4 (MEMRsEqu, RsZero, comparator_3_eq);
  and and_5 (MEMRtEqu, RtZero, comparator_4_eq);
  or or_16 (or_16_out, EXRsEqu, EXRtEqu);
  and and_6 (and_6_out, or_4_out, EXRtEqu);
  and and_7 (and_7_out, or_13_out, EXRsEqu);
  and and_8 (and_8_out, or_6_out, EXRsEqu);
  and and_9 (and_9_out, or_7_out, EXRtEqu);
  and and_10 (and_10_out, or_8_out, EXRsEqu);
  and and_11 (and_11_out, or_9_out, EXRsEqu);
  and and_12 (and_12_out, or_10_out, EXRtEqu);
  and and_13 (and_13_out, or_11_out, or_16_out);
  and and_14 (and_14_out, or_3_out, or_12_out);
  and and_15 (and_15_out, or_14_out, EXRsEqu);
  and and_16 (and_16_out, or_15_out, EXRtEqu);
  Multiplexer #(.width(5), .enable("false")) multiplexer_3 (.in0(Rs), .in1(5'b00010), .out(Rs_t), .sel(AllIns[13]));
  Multiplexer #(.width(5), .enable("false")) multiplexer_4 (.in0(Rt), .in1(5'b00100), .out(Rt_t), .sel(AllIns[13]));
  or or_17 (or_17_out, and_13_out, and_14_out, and_6_out, and_7_out);
  or or_18 (RDTR1Src[1], and_1_out, and_8_out, and_15_out, and_9_out, and_10_out);
  or or_19 (RDTR2Src[1], and_16_out, and_11_out, and_12_out);
  and and_17 (Nop, or_17_out, load);
  not not_1 (Stop, Nop);
  or or_20 (or_20_out, AllIns[17], AllIns[18], AllIns[19]);
  or or_21 (or_21_out, AllIns[0], AllIns[1], AllIns[2], AllIns[3], AllIns[4], AllIns[14], AllIns[9], AllIns[10], AllIns[11]);
  or or_22 (or_22_out, AllIns[15], AllIns[16]);
  or or_23 (or_23_out, AllIns[5], AllIns[6], AllIns[12]);
  or or_24 (or_24_out, AllIns[15], AllIns[16]);
  or or_25 (or_25_out, AllIns[5], AllIns[6], AllIns[12]);
  and and_18 (and_18_out, or_20_out, MEMRtEqu);
  or or_26 (or_26_out, AllIns[20], AllIns[21], AllIns[22], AllIns[23], AllIns[24], AllIns[25], AllIns[26], AllIns[27], AllIns[13]);
  and and_19 (and_19_out, or_22_out, MEMRtEqu);
  and and_20 (and_20_out, or_23_out, MEMRsEqu);
  or or_27 (or_27_out, AllIns[20], AllIns[21], AllIns[22], AllIns[23], AllIns[24], AllIns[25], AllIns[26], AllIns[27], AllIns[13]);
  and and_21 (and_21_out, or_24_out, MEMRsEqu);
  and and_22 (and_22_out, or_25_out, MEMRtEqu);
  and and_23 (and_23_out, or_21_out, MEMRsEqu);
  and and_24 (and_24_out, or_26_out, MEMRsEqu);
  and and_25 (and_25_out, or_27_out, MEMRtEqu);
  or or_28 (RDTR2Src[0], and_25_out, and_21_out, and_22_out);
  or or_29 (RDTR1Src[0], and_18_out, and_23_out, and_24_out, and_19_out, and_20_out);

  // Other names for the same wires on the sheet: ori = AllIns[0]; andi = AllIns[1]; slti = AllIns[2];
  //   addiu = AllIns[3]; addi = AllIns[4]; bne = AllIns[5]; beq = AllIns[6]; jal = AllIns[7]; j = AllIns[8];
  //   bgez = AllIns[9]; lh = AllIns[10]; lw = AllIns[11]; sw = AllIns[12]; syscall = AllIns[13]; jr = AllIns[14];
  //   srlv = AllIns[15]; sllv = AllIns[16]; sra = AllIns[17]; srl = AllIns[18]; sll = AllIns[19]; add = AllIns[20];
  //   addu = AllIns[21]; sub = AllIns[22]; and = AllIns[23]; or = AllIns[24]; nor = AllIns[25]; slt = AllIns[26];
  //   sltu = AllIns[27]; mtc00 = AllIns[28]; mtc01 = AllIns[29]; mfc0 = AllIns[30]; eret = AllIns[31];
  //   MEMR1Equ = RDTR1Src[0]; EXR1Equ = RDTR1Src[1]; MEMR2Equ = RDTR2Src[0]; EXR2Equ = RDTR2Src[1]
endmodule

module INTR (
  input  Clk,
  input  Rst,
  input  [31:0] IR,
  input  IEW,
  input  [31:0] RegIn,
  input  INMW,
  input  [31:0] PC,
  input  [3:0] IRSRC,
  output [31:0] IRNUM,
  output INTR,
  output Res,
  output [31:0] RegOut,
  output [3:0] IRWT
);

  wire and_1_out, and_2_out, and_3_out, and_4_out, and_5_out, and_6_out, and_7_out, and_8_out, and_9_out,
       and_10_out, and_12_out, comparator_1_eq, comparator_2_eq, d_ff_1_q, d_ff_2_q, d_ff_3_q, d_ff_4_q,
       d_ff_5_q, d_ff_6_q, d_ff_7_q, d_ff_8_q, decoder_1_out0, decoder_1_out1, decoder_1_out2,
       decoder_1_out3, IE, IEW_t, INM0, INM1, INM2, INM3, not_1_out, not_2_out, not_3_out, not_4_out,
       priority_encoder_1_en_out, priority_encoder_1_gs;
  wire [31:5] multiplexer_1_out;

  Decoder #(.select(2), .disabled(0)) decoder_1 (
    .out0(decoder_1_out0), .out1(decoder_1_out1), .out2(decoder_1_out2), .out3(decoder_1_out3),
    .sel(IRNUM[1:0]), .en(and_10_out));
  and and_1 (and_1_out, INTR, Res);
  or or_1 (IEW_t, and_1_out, IEW);
  D_Flip_Flop d_ff_1 (.clk(IRSRC[0]), .D(1'b1), .Q(d_ff_1_q), .reset(decoder_1_out0));  // open: Qn, preset, en
  D_Flip_Flop d_ff_2 (.clk(IRSRC[1]), .D(1'b1), .Q(d_ff_2_q), .reset(decoder_1_out1));  // open: Qn, preset, en
  D_Flip_Flop d_ff_3 (.clk(IRSRC[2]), .D(1'b1), .Q(d_ff_3_q), .reset(decoder_1_out2));  // open: Qn, preset, en
  D_Flip_Flop d_ff_4 (.clk(IRSRC[3]), .D(1'b1), .Q(d_ff_4_q), .reset(decoder_1_out3));  // open: Qn, preset, en
  or or_2 (IRWT[0], d_ff_1_q, decoder_1_out0);
  or or_3 (IRWT[1], d_ff_2_q, decoder_1_out1);
  or or_4 (IRWT[2], d_ff_3_q, decoder_1_out2);
  or or_5 (IRWT[3], d_ff_4_q, decoder_1_out3);
  Comparator #(.width(32), .mode("unsigned")) comparator_1 (
    .a(IR), .b({32{1'b0}}), .eq(comparator_1_eq));  // open: gt, lt
  Comparator #(.width(32), .mode("unsigned")) comparator_2 (
    .a(PC), .b({32{1'b0}}), .eq(comparator_2_eq));  // open: gt, lt
  and and_2 (and_2_out, d_ff_1_q, ~Rst);  // AND_Gate
  and and_3 (and_3_out, d_ff_2_q, ~Rst);  // AND_Gate
  and and_4 (and_4_out, d_ff_3_q, ~Rst);  // AND_Gate
  and and_5 (and_5_out, d_ff_4_q, ~Rst);  // AND_Gate
  Register #(.width(1)) register_1 (.D(INM0), .en(INMW), .Q(RegOut[1]), .clk(Clk), .clr(Rst));
  Register #(.width(1)) register_2 (.D(INM1), .en(INMW), .Q(RegOut[2]), .clk(Clk), .clr(Rst));
  Register #(.width(1)) register_3 (.D(INM2), .en(INMW), .Q(RegOut[3]), .clk(Clk), .clr(Rst));
  Register #(.width(1)) register_4 (.D(INM3), .en(INMW), .Q(RegOut[4]), .clk(Clk), .clr(Rst));
  nand nand_1 (Res, comparator_1_eq, comparator_2_eq);
  D_Flip_Flop d_ff_5 (.clk(Clk), .D(and_2_out), .Q(d_ff_5_q));  // open: Qn, preset, en, reset
  D_Flip_Flop d_ff_6 (.clk(Clk), .D(and_3_out), .Q(d_ff_6_q));  // open: Qn, preset, en, reset
  D_Flip_Flop d_ff_7 (.clk(Clk), .D(and_4_out), .Q(d_ff_7_q));  // open: Qn, preset, en, reset
  D_Flip_Flop d_ff_8 (.clk(Clk), .D(and_5_out), .Q(d_ff_8_q));  // open: Qn, preset, en, reset
  not not_1 (not_1_out, RegOut[1]);
  not not_2 (not_2_out, RegOut[2]);
  not not_3 (not_3_out, RegOut[3]);
  not not_4 (not_4_out, RegOut[4]);
  and and_6 (and_6_out, d_ff_5_q, not_1_out);
  and and_7 (and_7_out, d_ff_6_q, not_2_out);
  and and_8 (and_8_out, d_ff_7_q, not_3_out);
  and and_9 (and_9_out, d_ff_8_q, not_4_out);
  and and_10 (and_10_out, ~priority_encoder_1_en_out, RegOut[0], Res);  // AND_Gate
  Priority_Encoder #(.select(2), .disabled(0)) priority_encoder_1 (
    .in0(and_6_out), .in1(and_7_out), .in2(and_8_out), .in3(and_9_out), .out(IRNUM[1:0]),
    .gs(priority_encoder_1_gs), .en_out(priority_encoder_1_en_out), .en_in(1'b1));
  Register #(.width(1)) register_5 (.D(IE), .en(IEW_t), .Q(RegOut[0]), .clk(Clk), .clr(Rst));
  and and_11 (INTR, priority_encoder_1_gs, RegOut[0]);
  and and_12 (and_12_out, Res, INTR);
  Multiplexer #(.width(32), .enable("false")) multiplexer_1 (
    .in0(RegIn), .in1(32'h1e), .out({multiplexer_1_out, INM3, INM2, INM1, INM0, IE}), .sel(and_12_out));

  assign IRNUM[31:2] = {30{1'b0}};
  assign RegOut[31:5] = {27{1'b0}};

  // Other names for the same wires on the sheet: IRNUM_t[1:0] = IRNUM[1:0]; IR0 = IRSRC[0]; IR1 = IRSRC[1];
  //   IR2 = IRSRC[2]; IR3 = IRSRC[3]; IEOut = RegOut[0]; INM0Out = RegOut[1]; INM1Out = RegOut[2];
  //   INM2Out = RegOut[3]; INM3Out = RegOut[4]
endmodule

module BHT (
  input  Clk,
  input  write_valid,
  input  we_valid,
  input  we_pc,
  input  [31:0] write_pc,
  input  we_branch,
  input  [31:0] cur_pc,
  input  we_predict,
  input  [31:0] write_branch,
  input  we_lru,
  input  [1:0] write_predict,
  input  [2:0] write_address,
  output Hit,
  output [2:0] HitNum,
  output [31:0] BranchAddr,
  output [2:0] InsertNum,
  output [1:0] predict
);

  wire and_1_out, and_2_out, and_3_out, and_4_out, and_5_out, and_6_out, and_7_out, and_8_out, and_9_out,
       and_10_out, and_11_out, and_12_out, and_13_out, and_14_out, and_15_out, and_16_out, and_17_out,
       and_18_out, and_19_out, and_20_out, and_21_out, and_22_out, and_23_out, and_24_out, and_25_out,
       and_26_out, and_27_out, and_28_out, and_29_out, and_30_out, and_31_out, and_32_out, and_33_out,
       and_34_out, and_35_out, and_36_out, and_37_out, and_38_out, and_39_out, and_40_out, and_41_out,
       and_42_out, and_43_out, and_44_out, and_45_out, and_46_out, and_47_out, and_48_out, comparator_1_lt,
       comparator_2_lt, comparator_3_lt, comparator_4_lt, comparator_5_lt, comparator_6_lt, comparator_8_eq,
       comparator_9_eq, comparator_10_eq, comparator_11_eq, comparator_12_eq, comparator_13_eq,
       comparator_14_eq, comparator_15_eq, decoder_1_out0, decoder_1_out1, decoder_1_out2, decoder_1_out3,
       decoder_1_out4, decoder_1_out5, decoder_1_out6, decoder_1_out7, multiplexer_6_out, multiplexer_8_out,
       register_1_q, register_2_q, register_3_q, register_4_q, register_5_q, register_6_q, register_7_q,
       register_8_q, we_lru_t;
  wire [1:0] predict0, predict1, predict2, predict3, predict4, predict5, predict6, predict7, undriven_3;
  wire [2:0] priority_encoder_1_out;
  wire [12:0] lru0, lru1, lru2, lru3, lru4, lru5, lru6, lru7, multiplexer_1_out, multiplexer_2_out,
       multiplexer_3_out, multiplexer_4_out, multiplexer_5_out, multiplexer_7_out;
  wire [31:0] register_9_q, register_10_q, register_11_q, register_12_q, register_13_q, register_14_q,
       register_15_q, register_16_q, register_17_q, register_18_q, register_19_q, register_20_q,
       register_21_q, register_22_q, register_23_q, register_24_q, undriven, undriven_2;

  Decoder #(.select(3), .disabled(0), .enable("false")) decoder_1 (
    .out0(decoder_1_out0), .out1(decoder_1_out1), .out2(decoder_1_out2), .out3(decoder_1_out3),
    .out4(decoder_1_out4), .out5(decoder_1_out5), .out6(decoder_1_out6), .out7(decoder_1_out7),
    .sel(write_address));
  and and_1 (and_1_out, we_valid, decoder_1_out0);
  and and_2 (and_2_out, we_valid, decoder_1_out1);
  and and_3 (and_3_out, we_valid, decoder_1_out2);
  and and_4 (and_4_out, we_valid, decoder_1_out3);
  and and_5 (and_5_out, we_valid, decoder_1_out4);
  and and_6 (and_6_out, we_valid, decoder_1_out5);
  and and_7 (and_7_out, we_valid, decoder_1_out6);
  and and_8 (and_8_out, we_valid, decoder_1_out7);
  Comparator #(.width(13), .mode("unsigned")) comparator_1 (.a(lru0), .b(lru1), .lt(comparator_1_lt));  // open: gt, eq
  Comparator #(.width(13), .mode("unsigned")) comparator_2 (.a(lru2), .b(lru3), .lt(comparator_2_lt));  // open: gt, eq
  Comparator #(.width(13), .mode("unsigned")) comparator_3 (.a(lru4), .b(lru5), .lt(comparator_3_lt));  // open: gt, eq
  Comparator #(.width(13), .mode("unsigned")) comparator_4 (.a(lru6), .b(lru7), .lt(comparator_4_lt));  // open: gt, eq
  and and_9 (and_9_out, we_pc, decoder_1_out0);
  and and_10 (and_10_out, we_branch, decoder_1_out0);
  and and_11 (and_11_out, we_pc, decoder_1_out1);
  and and_12 (and_12_out, we_branch, decoder_1_out1);
  and and_13 (and_13_out, we_pc, decoder_1_out2);
  and and_14 (and_14_out, we_branch, decoder_1_out2);
  and and_15 (and_15_out, we_pc, decoder_1_out3);
  and and_16 (and_16_out, we_branch, decoder_1_out3);
  and and_17 (and_17_out, we_pc, decoder_1_out4);
  and and_18 (and_18_out, we_branch, decoder_1_out4);
  and and_19 (and_19_out, we_pc, decoder_1_out5);
  and and_20 (and_20_out, we_branch, decoder_1_out5);
  and and_21 (and_21_out, we_pc, decoder_1_out6);
  and and_22 (and_22_out, we_branch, decoder_1_out6);
  and and_23 (and_23_out, we_pc, decoder_1_out7);
  and and_24 (and_24_out, we_branch, decoder_1_out7);
  Multiplexer #(.width(13), .enable("false")) multiplexer_1 (
    .in0(lru0), .in1(lru1), .out(multiplexer_1_out), .sel(comparator_1_lt));
  Multiplexer #(.width(13), .enable("false")) multiplexer_2 (
    .in0(lru2), .in1(lru3), .out(multiplexer_2_out), .sel(comparator_2_lt));
  Multiplexer #(.width(13), .enable("false")) multiplexer_3 (
    .in0(lru4), .in1(lru5), .out(multiplexer_3_out), .sel(comparator_3_lt));
  Multiplexer #(.width(13), .enable("false")) multiplexer_4 (
    .in0(lru6), .in1(lru7), .out(multiplexer_4_out), .sel(comparator_4_lt));
  and and_25 (and_25_out, we_predict, decoder_1_out0);
  and and_26 (and_26_out, we_predict, decoder_1_out1);
  and and_27 (and_27_out, we_predict, decoder_1_out2);
  and and_28 (and_28_out, we_predict, decoder_1_out3);
  and and_29 (and_29_out, we_predict, decoder_1_out4);
  and and_30 (and_30_out, we_predict, decoder_1_out5);
  and and_31 (and_31_out, we_predict, decoder_1_out6);
  and and_32 (and_32_out, we_predict, decoder_1_out7);
  and and_33 (and_33_out, we_lru_t, decoder_1_out0);
  and and_34 (and_34_out, we_lru_t, decoder_1_out1);
  and and_35 (and_35_out, we_lru_t, decoder_1_out2);
  and and_36 (and_36_out, we_lru_t, decoder_1_out3);
  and and_37 (and_37_out, we_lru_t, decoder_1_out4);
  and and_38 (and_38_out, we_lru_t, decoder_1_out5);
  and and_39 (and_39_out, we_lru_t, decoder_1_out6);
  and and_40 (and_40_out, we_lru_t, decoder_1_out7);
  Comparator #(.width(13), .mode("unsigned")) comparator_5 (
    .a(multiplexer_1_out), .b(multiplexer_2_out), .lt(comparator_5_lt));  // open: gt, eq
  Comparator #(.width(13), .mode("unsigned")) comparator_6 (
    .a(multiplexer_3_out), .b(multiplexer_4_out), .lt(comparator_6_lt));  // open: gt, eq
  D_Flip_Flop d_ff_1 (.clk(Clk), .D(we_lru), .Q(we_lru_t), .reset(we_lru_t));  // open: Qn, preset, en
  Multiplexer #(.width(13), .enable("false")) multiplexer_5 (
    .in0(multiplexer_1_out), .in1(multiplexer_2_out), .out(multiplexer_5_out), .sel(comparator_5_lt));
  Multiplexer #(.enable("false")) multiplexer_6 (
    .in0(comparator_1_lt), .in1(comparator_2_lt), .out(multiplexer_6_out), .sel(comparator_5_lt));
  Multiplexer #(.width(13), .enable("false")) multiplexer_7 (
    .in0(multiplexer_3_out), .in1(multiplexer_4_out), .out(multiplexer_7_out), .sel(comparator_6_lt));
  Multiplexer #(.enable("false")) multiplexer_8 (
    .in0(comparator_3_lt), .in1(comparator_4_lt), .out(multiplexer_8_out), .sel(comparator_6_lt));
  Register #(.width(1)) register_1 (.D(write_valid), .en(and_1_out), .Q(register_1_q), .clk(Clk), .clr(1'b0));
  Register #(.width(1)) register_2 (.D(write_valid), .en(and_2_out), .Q(register_2_q), .clk(Clk), .clr(1'b0));
  Register #(.width(1)) register_3 (.D(write_valid), .en(and_3_out), .Q(register_3_q), .clk(Clk), .clr(1'b0));
  Register #(.width(1)) register_4 (.D(write_valid), .en(and_4_out), .Q(register_4_q), .clk(Clk), .clr(1'b0));
  Register #(.width(1)) register_5 (.D(write_valid), .en(and_5_out), .Q(register_5_q), .clk(Clk), .clr(1'b0));
  Register #(.width(1)) register_6 (.D(write_valid), .en(and_6_out), .Q(register_6_q), .clk(Clk), .clr(1'b0));
  Register #(.width(1)) register_7 (.D(write_valid), .en(and_7_out), .Q(register_7_q), .clk(Clk), .clr(1'b0));
  Register #(.width(1)) register_8 (.D(write_valid), .en(and_8_out), .Q(register_8_q), .clk(Clk), .clr(1'b0));
  Comparator #(.width(13), .mode("unsigned")) comparator_7 (
    .a(multiplexer_5_out), .b(multiplexer_7_out), .lt(InsertNum[2]));  // open: gt, eq
  Register #(.width(32)) register_9 (.D(write_pc), .en(and_9_out), .Q(register_9_q), .clk(Clk), .clr(1'b0));
  Register #(.width(32)) register_10 (.D(write_pc), .en(and_11_out), .Q(register_10_q), .clk(Clk), .clr(1'b0));
  Register #(.width(32)) register_11 (.D(write_pc), .en(and_13_out), .Q(register_11_q), .clk(Clk), .clr(1'b0));
  Register #(.width(32)) register_12 (.D(write_pc), .en(and_15_out), .Q(register_12_q), .clk(Clk), .clr(1'b0));
  Register #(.width(32)) register_13 (.D(write_pc), .en(and_17_out), .Q(register_13_q), .clk(Clk), .clr(1'b0));
  Register #(.width(32)) register_14 (.D(write_pc), .en(and_19_out), .Q(register_14_q), .clk(Clk), .clr(1'b0));
  Register #(.width(32)) register_15 (.D(undriven), .en(and_21_out), .Q(register_15_q), .clk(Clk), .clr(1'b0));
  Register #(.width(32)) register_16 (.D(undriven), .en(and_23_out), .Q(register_16_q), .clk(Clk), .clr(1'b0));
  Multiplexer #(.enable("false")) multiplexer_9 (
    .in0(comparator_5_lt), .in1(comparator_6_lt), .out(InsertNum[1]), .sel(InsertNum[2]));
  Multiplexer #(.enable("false")) multiplexer_10 (
    .in0(multiplexer_6_out), .in1(multiplexer_8_out), .out(InsertNum[0]), .sel(InsertNum[2]));
  Register #(.width(32)) register_17 (.D(write_branch), .en(and_10_out), .Q(register_17_q), .clk(Clk), .clr(1'b0));
  Register #(.width(32)) register_18 (.D(write_branch), .en(and_12_out), .Q(register_18_q), .clk(Clk), .clr(1'b0));
  Register #(.width(32)) register_19 (.D(write_branch), .en(and_14_out), .Q(register_19_q), .clk(Clk), .clr(1'b0));
  Register #(.width(32)) register_20 (.D(write_branch), .en(and_16_out), .Q(register_20_q), .clk(Clk), .clr(1'b0));
  Register #(.width(32)) register_21 (.D(write_branch), .en(and_18_out), .Q(register_21_q), .clk(Clk), .clr(1'b0));
  Register #(.width(32)) register_22 (.D(write_branch), .en(and_20_out), .Q(register_22_q), .clk(Clk), .clr(1'b0));
  Register #(.width(32)) register_23 (.D(undriven_2), .en(and_22_out), .Q(register_23_q), .clk(Clk), .clr(1'b0));
  Register #(.width(32)) register_24 (.D(undriven_2), .en(and_24_out), .Q(register_24_q), .clk(Clk), .clr(1'b0));
  Register #(.width(2)) register_25 (.D(write_predict), .en(and_25_out), .Q(predict0), .clk(Clk), .clr(1'b0));
  Register #(.width(2)) register_26 (.D(write_predict), .en(and_26_out), .Q(predict1), .clk(Clk), .clr(1'b0));
  Register #(.width(2)) register_27 (.D(write_predict), .en(and_27_out), .Q(predict2), .clk(Clk), .clr(1'b0));
  Register #(.width(2)) register_28 (.D(write_predict), .en(and_28_out), .Q(predict3), .clk(Clk), .clr(1'b0));
  Register #(.width(2)) register_29 (.D(write_predict), .en(and_29_out), .Q(predict4), .clk(Clk), .clr(1'b0));
  Register #(.width(2)) register_30 (.D(write_predict), .en(and_30_out), .Q(predict5), .clk(Clk), .clr(1'b0));
  Register #(.width(2)) register_31 (.D(undriven_3), .en(and_31_out), .Q(predict6), .clk(Clk), .clr(1'b0));
  Register #(.width(2)) register_32 (.D(undriven_3), .en(and_32_out), .Q(predict7), .clk(Clk), .clr(1'b0));
  Counter #(.width(13), .max('h1fff)) counter_1 (.Q(lru0), .clk(Clk), .clr(and_33_out));  // open: load, D, count, carry
  Counter #(.width(13), .max('h1fff)) counter_2 (.Q(lru1), .clk(Clk), .clr(and_34_out));  // open: load, D, count, carry
  Counter #(.width(13), .max('h1fff)) counter_3 (.Q(lru2), .clk(Clk), .clr(and_35_out));  // open: load, D, count, carry
  Counter #(.width(13), .max('h1fff)) counter_4 (.Q(lru3), .clk(Clk), .clr(and_36_out));  // open: load, D, count, carry
  Counter #(.width(13), .max('h1fff)) counter_5 (.Q(lru4), .clk(Clk), .clr(and_37_out));  // open: load, D, count, carry
  Counter #(.width(13), .max('h1fff)) counter_6 (.Q(lru5), .clk(Clk), .clr(and_38_out));  // open: load, D, count, carry
  Counter #(.width(13), .max('h1fff)) counter_7 (.Q(lru6), .clk(Clk), .clr(and_39_out));  // open: load, D, count, carry
  Counter #(.width(13), .max('h1fff)) counter_8 (.Q(lru7), .clk(Clk), .clr(and_40_out));  // open: load, D, count, carry
  Comparator #(.width(32), .mode("unsigned")) comparator_8 (
    .a(cur_pc), .b(register_9_q), .eq(comparator_8_eq));  // open: gt, lt
  Comparator #(.width(32), .mode("unsigned")) comparator_9 (
    .a(cur_pc), .b(register_10_q), .eq(comparator_9_eq));  // open: gt, lt
  Comparator #(.width(32), .mode("unsigned")) comparator_10 (
    .a(cur_pc), .b(register_11_q), .eq(comparator_10_eq));  // open: gt, lt
  Comparator #(.width(32), .mode("unsigned")) comparator_11 (
    .a(cur_pc), .b(register_12_q), .eq(comparator_11_eq));  // open: gt, lt
  Comparator #(.width(32), .mode("unsigned")) comparator_12 (
    .a(cur_pc), .b(register_13_q), .eq(comparator_12_eq));  // open: gt, lt
  Comparator #(.width(32), .mode("unsigned")) comparator_13 (
    .a(cur_pc), .b(register_14_q), .eq(comparator_13_eq));  // open: gt, lt
  Comparator #(.width(32), .mode("unsigned")) comparator_14 (
    .a(cur_pc), .b(register_15_q), .eq(comparator_14_eq));  // open: gt, lt
  Comparator #(.width(32), .mode("unsigned")) comparator_15 (
    .a(cur_pc), .b(register_16_q), .eq(comparator_15_eq));  // open: gt, lt
  and and_41 (and_41_out, register_1_q, comparator_8_eq);
  and and_42 (and_42_out, register_2_q, comparator_9_eq);
  and and_43 (and_43_out, register_3_q, comparator_10_eq);
  and and_44 (and_44_out, register_4_q, comparator_11_eq);
  and and_45 (and_45_out, register_5_q, comparator_12_eq);
  and and_46 (and_46_out, register_6_q, comparator_13_eq);
  and and_47 (and_47_out, register_7_q, comparator_14_eq);
  and and_48 (and_48_out, register_8_q, comparator_15_eq);
  Priority_Encoder priority_encoder_1 (
    .in0(and_41_out), .in1(and_42_out), .in2(and_43_out), .in3(and_44_out), .in4(and_45_out),
    .in5(and_46_out), .in6(and_47_out), .in7(and_48_out), .out(priority_encoder_1_out), .gs(Hit));  // open: en_in, en_out
  Multiplexer #(.select(3), .width(2), .disabled(0)) multiplexer_11 (
    .in0(predict0), .in1(predict1), .in2(predict2), .in3(predict3), .in4(predict4), .in5(predict5),
    .in6(predict6), .in7(predict7), .out(predict), .sel(priority_encoder_1_out), .en(Hit));
  Multiplexer #(.width(3), .disabled(0), .enable("false")) multiplexer_12 (
    .in0(3'b000), .in1(priority_encoder_1_out), .out(HitNum), .sel(Hit));
  Multiplexer #(.select(3), .width(32), .disabled(0)) multiplexer_13 (
    .in0(register_17_q), .in1(register_18_q), .in2(register_19_q), .in3(register_20_q), .in4(register_21_q),
    .in5(register_22_q), .in6(register_23_q), .in7(register_24_q), .out(BranchAddr),
    .sel(priority_encoder_1_out), .en(Hit));
endmodule
