// Logisim project alu-cpu.circ as structural Verilog: 5 circuits, main circuit ALU
module ALU (
  input  [31:0] X,
  input  [31:0] Y,
  input  [3:0] AluOP,
  output Signed_Overflow,
  output UnSigned_Overflow,
  output Equal,
  output [31:0] Result,
  output [31:0] Result_2
);

  wire adder32bitall_1_out_5, and_2_out, and_3_out, and_4_out, and_5_out, comparator_1_lt, comparator_2_lt,
       or_3_out, xor_1_out, xor_3_out;
  wire [31:0] multiplexer_1_out, not_1_out, or_2_out, R2OP3, R2OP4, ROP0, ROP1, ROP2, ROP3, ROP4, ROP7, ROP8,
       ROP9, ROP10, ROP11, ROP12, ROP56;

  // Probe on X
  // Probe on X
  // Probe on Y
  // Probe on Y
  Shifter #(.width(32)) shifter_1 (.in(X), .\dist (Y[4:0]), .out(ROP0));
  Shifter #(.width(32), .shift("ar")) shifter_2 (.in(X), .\dist (Y[4:0]), .out(ROP1));
  Shifter #(.width(32), .shift("lr")) shifter_3 (.in(X), .\dist (Y[4:0]), .out(ROP2));
  Multiplier #(.width(32)) multiplier_1 (.a(X), .b(Y), .out(ROP3), .cin({32{1'b0}}), .cout(R2OP3));
  Divider #(.width(32)) divider_1 (.a(X), .b(Y), .out(ROP4), .upper({32{1'b0}}), .rem(R2OP4));
  assign ROP7 = X & Y;  // AND_Gate and_1, 32 bits wide
  Multiplexer #(.width(32), .enable("false")) multiplexer_1 (
    .in0(Y), .in1(not_1_out), .out(multiplexer_1_out), .sel(and_2_out));
  assign not_1_out = ~Y;  // NOT_Gate not_1, 32 bits wide
  and and_2 (and_2_out, ~AluOP[0], AluOP[1], AluOP[2], ~AluOP[3]);  // AND_Gate
  xor xor_1 (xor_1_out, AluOP[0], AluOP[1]);
  // Probe on AluOP
  // Probe on Result
  // Probe on Result
  Adder32bitAll adder32bitall_1 (
    .out_5(adder32bitall_1_out_5), .out_4(ROP56), .in_2(X), .in_3(multiplexer_1_out), .in_1(and_2_out));
  and and_3 (and_3_out, xor_1_out, AluOP[2], ~AluOP[3]);  // AND_Gate
  assign ROP8 = X | Y;  // OR_Gate or_1, 32 bits wide
  assign ROP9 = X ^ Y;  // XOR_Gate xor_2, 32 bits wide
  assign or_2_out = X | Y;  // OR_Gate or_2, 32 bits wide
  Comparator #(.width(32)) comparator_1 (.a(X), .b(Y), .eq(Equal), .lt(comparator_1_lt));  // open: gt
  Comparator #(.width(32), .mode("unsigned")) comparator_2 (.a(X), .b(Y), .lt(comparator_2_lt));  // open: gt, eq
  xor xor_3 (xor_3_out, and_2_out, adder32bitall_1_out_5);
  // Probe on Result_2
  assign ROP10 = ~or_2_out;  // NOT_Gate not_2, 32 bits wide
  assign ROP11 = {{31{1'b0}}, comparator_1_lt};  // Bit_Extender bit_extender_1
  assign ROP12 = {{31{1'b0}}, comparator_2_lt};  // Bit_Extender bit_extender_2
  and and_4 (and_4_out, X[31], multiplexer_1_out[31], ~ROP56[31]);  // AND_Gate
  and and_5 (and_5_out, ~X[31], ~multiplexer_1_out[31], ROP56[31]);  // AND_Gate
  or or_3 (or_3_out, and_4_out, and_5_out);
  and and_6 (UnSigned_Overflow, xor_3_out, and_3_out);
  and and_7 (Signed_Overflow, or_3_out, and_3_out);
  Multiplexer #(.select(4), .width(32), .enable("false")) multiplexer_2 (
    .in0(ROP0), .in1(ROP1), .in2(ROP2), .in3(ROP3), .in4(ROP4), .in5(ROP56), .in6(ROP56), .in7(ROP7),
    .in8(ROP8), .in9(ROP9), .in10(ROP10), .in11(ROP11), .in12(ROP12), .in13({32{1'b0}}), .in14({32{1'b0}}),
    .in15({32{1'b0}}), .out(Result), .sel(AluOP));
  Multiplexer #(.select(4), .width(32), .enable("false")) multiplexer_3 (
    .in0({32{1'b0}}), .in1({32{1'b0}}), .in2({32{1'b0}}), .in3(R2OP3), .in4(R2OP4), .in5({32{1'b0}}),
    .in6({32{1'b0}}), .in7({32{1'b0}}), .in8({32{1'b0}}), .in9({32{1'b0}}), .in10({32{1'b0}}),
    .in11({32{1'b0}}), .in12({32{1'b0}}), .in13({32{1'b0}}), .in14({32{1'b0}}), .in15({32{1'b0}}),
    .out(Result_2), .sel(AluOP));

  // Other names for the same wires on the sheet: OF = Signed_Overflow; Result2[31:0] = Result_2; S[3:0] = AluOP;
  //   UOF = UnSigned_Overflow

  // Notes on the sheet:
  //   不要改变此引脚区域内容，也不要改变ALU封装形式
  //   输入引脚
  //   请在下方利用上方输入输出引脚的隧道信号构建ALU电路，ctrl+d复制选择部件
  //   华中科技大学计算机学院 计算机组成原理，鸣谢加州大学伯克利CS61C课程
  //   输出引脚
  //   探测区域
endmodule

module carrier (
  input  C0,
  input  G4,
  input  P4,
  input  G3,
  input  P3,
  input  G2,
  input  P2,
  input  G1,
  input  P1,
  output G,
  output P,
  output C4,
  output C3,
  output C2,
  output C1
);

  wire and_2_out, and_3_out, and_4_out, and_5_out, and_6_out, and_7_out, and_8_out, and_9_out, and_10_out,
       and_11_out;

  or or_1 (G, G4, and_2_out, and_3_out, and_4_out);
  and and_1 (P, P4, P3, P2, P1);
  and and_2 (and_2_out, P4, G3);
  or or_2 (C4, G4, and_2_out, and_3_out, and_4_out, and_5_out);
  and and_3 (and_3_out, P4, P3, G2);
  and and_4 (and_4_out, P4, P3, P2, G1);
  and and_5 (and_5_out, P4, P3, P2, P1, C0);
  or or_3 (C3, G3, and_6_out, and_7_out, and_8_out);
  and and_6 (and_6_out, P3, G2);
  and and_7 (and_7_out, P3, P2, G1);
  and and_8 (and_8_out, P3, P2, P1, C0);
  or or_4 (C2, G2, and_9_out, and_10_out);
  and and_9 (and_9_out, P2, G1);
  and and_10 (and_10_out, P2, P1, C0);
  or or_5 (C1, G1, and_11_out);
  and and_11 (and_11_out, P1, C0);
endmodule

module adder (
  input  C0,
  input  X4,
  input  X3,
  input  X2,
  input  X1,
  input  Y4,
  input  Y3,
  input  Y2,
  input  Y1,
  output G,
  output P,
  output C4,
  output S4,
  output S3,
  output S2,
  output S1
);

  wire and_2_out, and_3_out, and_4_out, and_5_out, and_6_out, and_7_out, and_8_out, and_9_out, and_10_out,
       and_11_out, and_12_out, and_13_out, and_14_out, and_15_out, or_3_out, or_4_out, or_5_out, xor_1_out,
       xor_3_out, xor_5_out, xor_7_out;

  or or_1 (G, and_2_out, and_3_out, and_4_out, and_5_out);
  and and_1 (P, xor_1_out, xor_3_out, xor_5_out, xor_7_out);
  // Probe on and_2_out
  and and_2 (and_2_out, X4, Y4);
  and and_3 (and_3_out, xor_1_out, and_7_out);
  // Probe on C4
  or or_2 (C4, and_2_out, and_3_out, and_4_out, and_5_out, and_6_out);
  and and_4 (and_4_out, xor_1_out, xor_3_out, and_12_out);
  and and_5 (and_5_out, xor_1_out, xor_3_out, xor_5_out, and_14_out);
  and and_6 (and_6_out, xor_1_out, xor_3_out, xor_5_out, xor_7_out, C0);
  // Probe on xor_1_out
  xor xor_1 (xor_1_out, X4, Y4);
  xor xor_2 (S4, xor_1_out, or_3_out);
  and and_7 (and_7_out, X3, Y3);
  // Probe on or_3_out
  or or_3 (or_3_out, and_7_out, and_8_out, and_9_out, and_10_out);
  and and_8 (and_8_out, xor_3_out, and_12_out);
  and and_9 (and_9_out, xor_3_out, xor_5_out, and_14_out);
  // Probe on and_7_out
  and and_10 (and_10_out, xor_3_out, xor_5_out, xor_7_out, C0);
  // Probe on xor_3_out
  xor xor_3 (xor_3_out, X3, Y3);
  xor xor_4 (S3, xor_3_out, or_4_out);
  or or_4 (or_4_out, and_12_out, and_11_out, and_13_out);
  and and_11 (and_11_out, xor_5_out, and_14_out);
  // Probe on and_12_out
  and and_12 (and_12_out, X2, Y2);
  // Probe on or_4_out
  and and_13 (and_13_out, xor_5_out, xor_7_out, C0);
  // Probe on xor_5_out
  xor xor_5 (xor_5_out, X2, Y2);
  xor xor_6 (S2, xor_5_out, or_5_out);
  or or_5 (or_5_out, and_14_out, and_15_out);
  // Probe on and_14_out
  and and_14 (and_14_out, X1, Y1);
  // Probe on or_5_out
  and and_15 (and_15_out, xor_7_out, C0);
  // Probe on xor_7_out
  xor xor_7 (xor_7_out, X1, Y1);
  xor xor_8 (S1, xor_7_out, C0);
endmodule

module Adder32bit (
  input  in_1,
  input  [31:0] in_2,
  input  [31:0] in_3,
  output [31:0] out_4,
  output out_5
);

  wire adder_1_g, adder_1_p, adder_2_g, adder_2_p, adder_3_g, adder_3_p, adder_4_g, adder_4_p, adder_5_c4,
       adder_5_g, adder_5_p, adder_6_g, adder_6_p, adder_7_g, adder_7_p, adder_8_g, adder_8_p, carrier_1_c1,
       carrier_1_c2, carrier_1_c3, carrier_2_c1, carrier_2_c2, carrier_2_c3;

  adder adder_1 (
    .G(adder_1_g), .P(adder_1_p), .C4(out_5), .S4(out_4[31]), .S3(out_4[30]), .S2(out_4[29]), .S1(out_4[28]),
    .X4(in_2[31]), .X3(in_2[30]), .X2(in_2[29]), .X1(in_2[28]), .Y4(in_3[31]), .Y3(in_3[30]), .Y2(in_3[29]),
    .Y1(in_3[28]), .C0(carrier_1_c3));
  adder adder_2 (
    .G(adder_2_g), .P(adder_2_p), .S4(out_4[27]), .S3(out_4[26]), .S2(out_4[25]), .S1(out_4[24]),
    .X4(in_2[27]), .X3(in_2[26]), .X2(in_2[25]), .X1(in_2[24]), .Y4(in_3[27]), .Y3(in_3[26]), .Y2(in_3[25]),
    .Y1(in_3[24]), .C0(carrier_1_c2));  // open: C4
  carrier carrier_1 (
    .C3(carrier_1_c3), .C2(carrier_1_c2), .C1(carrier_1_c1), .G4(adder_1_g), .P4(adder_1_p), .G3(adder_2_g),
    .P3(adder_2_p), .G2(adder_3_g), .P2(adder_3_p), .G1(adder_4_g), .P1(adder_4_p), .C0(adder_5_c4));  // open: G, P, C4
  adder adder_3 (
    .G(adder_3_g), .P(adder_3_p), .S4(out_4[23]), .S3(out_4[22]), .S2(out_4[21]), .S1(out_4[20]),
    .X4(in_2[23]), .X3(in_2[22]), .X2(in_2[21]), .X1(in_2[20]), .Y4(in_3[23]), .Y3(in_3[22]), .Y2(in_3[21]),
    .Y1(in_3[20]), .C0(carrier_1_c1));  // open: C4
  adder adder_4 (
    .G(adder_4_g), .P(adder_4_p), .S4(out_4[19]), .S3(out_4[18]), .S2(out_4[17]), .S1(out_4[16]),
    .X4(in_2[19]), .X3(in_2[18]), .X2(in_2[17]), .X1(in_2[16]), .Y4(in_3[19]), .Y3(in_3[18]), .Y2(in_3[17]),
    .Y1(in_3[16]), .C0(adder_5_c4));  // open: C4
  adder adder_5 (
    .G(adder_5_g), .P(adder_5_p), .C4(adder_5_c4), .S4(out_4[15]), .S3(out_4[14]), .S2(out_4[13]),
    .S1(out_4[12]), .X4(in_2[15]), .X3(in_2[14]), .X2(in_2[13]), .X1(in_2[12]), .Y4(in_3[15]), .Y3(in_3[14]),
    .Y2(in_3[13]), .Y1(in_3[12]), .C0(carrier_2_c3));
  adder adder_6 (
    .G(adder_6_g), .P(adder_6_p), .S4(out_4[11]), .S3(out_4[10]), .S2(out_4[9]), .S1(out_4[8]),
    .X4(in_2[11]), .X3(in_2[10]), .X2(in_2[9]), .X1(in_2[8]), .Y4(in_3[11]), .Y3(in_3[10]), .Y2(in_3[9]),
    .Y1(in_3[8]), .C0(carrier_2_c2));  // open: C4
  carrier carrier_2 (
    .C3(carrier_2_c3), .C2(carrier_2_c2), .C1(carrier_2_c1), .G4(adder_5_g), .P4(adder_5_p), .G3(adder_6_g),
    .P3(adder_6_p), .G2(adder_7_g), .P2(adder_7_p), .G1(adder_8_g), .P1(adder_8_p), .C0(in_1));  // open: G, P, C4
  adder adder_7 (
    .G(adder_7_g), .P(adder_7_p), .S4(out_4[7]), .S3(out_4[6]), .S2(out_4[5]), .S1(out_4[4]), .X4(in_2[7]),
    .X3(in_2[6]), .X2(in_2[5]), .X1(in_2[4]), .Y4(in_3[7]), .Y3(in_3[6]), .Y2(in_3[5]), .Y1(in_3[4]),
    .C0(carrier_2_c1));  // open: C4
  adder adder_8 (
    .G(adder_8_g), .P(adder_8_p), .S4(out_4[3]), .S3(out_4[2]), .S2(out_4[1]), .S1(out_4[0]), .X4(in_2[3]),
    .X3(in_2[2]), .X2(in_2[1]), .X1(in_2[0]), .Y4(in_3[3]), .Y3(in_3[2]), .Y2(in_3[1]), .Y1(in_3[0]),
    .C0(in_1));  // open: C4
endmodule

module Adder32bitAll (
  input  in_1,
  input  [31:0] in_2,
  input  [31:0] in_3,
  output [31:0] out_4,
  output out_5
);

  wire adder_1_g, adder_1_p, adder_2_g, adder_2_p, adder_3_g, adder_3_p, adder_4_g, adder_4_p, adder_5_c4,
       adder_5_g, adder_5_p, adder_6_g, adder_6_p, adder_7_g, adder_7_p, adder_8_g, adder_8_p, carrier_1_c1,
       carrier_1_c2, carrier_1_c3, carrier_2_c1, carrier_3_c1, carrier_3_c2, carrier_3_c3, carrier_3_g,
       carrier_3_p;

  adder adder_1 (
    .G(adder_1_g), .P(adder_1_p), .C4(out_5), .S4(out_4[31]), .S3(out_4[30]), .S2(out_4[29]), .S1(out_4[28]),
    .X4(in_2[31]), .X3(in_2[30]), .X2(in_2[29]), .X1(in_2[28]), .Y4(in_3[31]), .Y3(in_3[30]), .Y2(in_3[29]),
    .Y1(in_3[28]), .C0(carrier_1_c3));
  adder adder_2 (
    .G(adder_2_g), .P(adder_2_p), .S4(out_4[27]), .S3(out_4[26]), .S2(out_4[25]), .S1(out_4[24]),
    .X4(in_2[27]), .X3(in_2[26]), .X2(in_2[25]), .X1(in_2[24]), .Y4(in_3[27]), .Y3(in_3[26]), .Y2(in_3[25]),
    .Y1(in_3[24]), .C0(carrier_1_c2));  // open: C4
  carrier carrier_1 (
    .C3(carrier_1_c3), .C2(carrier_1_c2), .C1(carrier_1_c1), .G4(adder_1_g), .P4(adder_1_p), .G3(adder_2_g),
    .P3(adder_2_p), .G2(adder_3_g), .P2(adder_3_p), .G1(adder_4_g), .P1(adder_4_p), .C0(carrier_2_c1));  // open: G, P, C4
  adder adder_3 (
    .G(adder_3_g), .P(adder_3_p), .S4(out_4[23]), .S3(out_4[22]), .S2(out_4[21]), .S1(out_4[20]),
    .X4(in_2[23]), .X3(in_2[22]), .X2(in_2[21]), .X1(in_2[20]), .Y4(in_3[23]), .Y3(in_3[22]), .Y2(in_3[21]),
    .Y1(in_3[20]), .C0(carrier_1_c1));  // open: C4
  adder adder_4 (
    .G(adder_4_g), .P(adder_4_p), .S4(out_4[19]), .S3(out_4[18]), .S2(out_4[17]), .S1(out_4[16]),
    .X4(in_2[19]), .X3(in_2[18]), .X2(in_2[17]), .X1(in_2[16]), .Y4(in_3[19]), .Y3(in_3[18]), .Y2(in_3[17]),
    .Y1(in_3[16]), .C0(carrier_2_c1));  // open: C4
  carrier carrier_2 (
    .C1(carrier_2_c1), .G1(carrier_3_g), .P1(carrier_3_p), .C0(adder_5_c4));  // open: G, P, C4, C3, C2, G4, P4, G3, P3, G2, P2
  adder adder_5 (
    .G(adder_5_g), .P(adder_5_p), .C4(adder_5_c4), .S4(out_4[15]), .S3(out_4[14]), .S2(out_4[13]),
    .S1(out_4[12]), .X4(in_2[15]), .X3(in_2[14]), .X2(in_2[13]), .X1(in_2[12]), .Y4(in_3[15]), .Y3(in_3[14]),
    .Y2(in_3[13]), .Y1(in_3[12]), .C0(carrier_3_c3));
  adder adder_6 (
    .G(adder_6_g), .P(adder_6_p), .S4(out_4[11]), .S3(out_4[10]), .S2(out_4[9]), .S1(out_4[8]),
    .X4(in_2[11]), .X3(in_2[10]), .X2(in_2[9]), .X1(in_2[8]), .Y4(in_3[11]), .Y3(in_3[10]), .Y2(in_3[9]),
    .Y1(in_3[8]), .C0(carrier_3_c2));  // open: C4
  carrier carrier_3 (
    .G(carrier_3_g), .P(carrier_3_p), .C3(carrier_3_c3), .C2(carrier_3_c2), .C1(carrier_3_c1),
    .G4(adder_5_g), .P4(adder_5_p), .G3(adder_6_g), .P3(adder_6_p), .G2(adder_7_g), .P2(adder_7_p),
    .G1(adder_8_g), .P1(adder_8_p), .C0(in_1));  // open: C4
  adder adder_7 (
    .G(adder_7_g), .P(adder_7_p), .S4(out_4[7]), .S3(out_4[6]), .S2(out_4[5]), .S1(out_4[4]), .X4(in_2[7]),
    .X3(in_2[6]), .X2(in_2[5]), .X1(in_2[4]), .Y4(in_3[7]), .Y3(in_3[6]), .Y2(in_3[5]), .Y1(in_3[4]),
    .C0(carrier_3_c1));  // open: C4
  adder adder_8 (
    .G(adder_8_g), .P(adder_8_p), .S4(out_4[3]), .S3(out_4[2]), .S2(out_4[1]), .S1(out_4[0]), .X4(in_2[3]),
    .X3(in_2[2]), .X2(in_2[1]), .X1(in_2[0]), .Y4(in_3[3]), .Y3(in_3[2]), .Y2(in_3[1]), .Y1(in_3[0]),
    .C0(in_1));  // open: C4
endmodule
