// Logisim project ir-cpu.circ as structural Verilog: 4 circuits, main circuit main
module main (
);

  wire alu_1_equal, Clk, clock_1_out, control_1_aluysrc2, control_1_disp, control_1_dmaddsrc, control_1_dmwe,
       control_1_epcen, control_1_epcsrc, control_1_halt, control_1_iew, control_1_inmw, control_1_pcaddsrc,
       control_1_pcen, control_1_rfr1src, control_1_rfwe, ir_1_ir, not_1_out;
  wire [1:0] control_1_aluysrc, control_1_out_12, control_1_pcsrc, control_1_pcsrc2, control_1_rfdinsrc,
       control_1_rfrwsrc, ir_1_irnum;
  wire [2:2] control_1_rfdinsrc_2;
  wire [3:0] control_1_aluop, Disp_q, Disp_q_2, Disp_q_3, Disp_q_4, Disp_q_5, Disp_q_6, Disp_q_7, Disp_q_8,
       Interupt0_out, ir_1_irwt;
  wire [4:0] insanalyse_1_rd, insanalyse_1_rs, insanalyse_1_rt, insanalyse_1_shamt, multiplexer_5_out,
       multiplexer_6_out, multiplexer_7_out;
  wire [5:0] insanalyse_1_funct, insanalyse_1_op;
  wire [9:0] control_1_irnum_2, multiplexer_13_out;
  wire [15:0] insanalyse_1_immediate16, ram_1_data;
  wire [25:0] insanalyse_1_immediate26;
  wire [31:0] adder_1_out, adder_2_out, alu_1_result, bit_extender_1_out, bit_extender_2_out,
       bit_extender_3_out, bit_extender_4_out, bit_extender_5_out, counter_1_q, EPC_q, ir_1_regout,
       main_1_a0_value, main_1_reg1, main_1_reg2_2, main_1_v0_value, multiplexer_1_out, multiplexer_2_out,
       multiplexer_3_out, multiplexer_4_out, multiplexer_8_out, multiplexer_9_out, multiplexer_10_out,
       multiplexer_11_out, multiplexer_12_out, multiplexer_14_out, PC_q, rom_1_data;
  wire [31:16] ram_1_data_2;

  Multiplexer #(.select(2), .width(32), .enable("false")) multiplexer_1 (
    .in0(main_1_reg1), .in1(adder_1_out), .in2(adder_2_out), .in3(bit_extender_1_out),
    .out(multiplexer_1_out), .sel(control_1_pcsrc));
  assign bit_extender_1_out = {{6{1'b0}}, insanalyse_1_immediate26};  // Bit_Extender bit_extender_1
  Multiplexer #(.select(2), .width(32), .enable("false")) multiplexer_2 (
    .in0(multiplexer_1_out), .in1(EPC_q), .in2({ram_1_data_2, ram_1_data}), .in3({ram_1_data_2, ram_1_data}),
    .out(multiplexer_2_out), .sel(control_1_pcsrc2));
  Register #(.width(32)) PC (.D(multiplexer_2_out), .en(control_1_pcen), .Q(PC_q), .clk(Clk), .clr(1'b0));
  Adder #(.width(32)) adder_1 (.a(32'h1), .b(PC_q), .out(adder_1_out), .cin(1'b0));  // open: cout
  Multiplexer #(.width(32), .enable("false")) multiplexer_3 (
    .in0(PC_q), .in1(main_1_reg1), .out(multiplexer_3_out), .sel(control_1_epcsrc));
  Register #(.width(32)) EPC (.D(multiplexer_3_out), .en(control_1_epcen), .Q(EPC_q), .clk(Clk), .clr(1'b0));
  Hex_Digit_Display hex_digit_display_1 (.value(Disp_q_8), .dp(1'b0));
  Hex_Digit_Display hex_digit_display_2 (.value(Disp_q_7), .dp(1'b0));
  Button Interupt0 (.out(Interupt0_out[0]));
  LED led_1 (.in(ir_1_irwt[0]));
  Hex_Digit_Display hex_digit_display_3 (.value(Disp_q_5), .dp(1'b0));
  Hex_Digit_Display hex_digit_display_4 (.value(Disp_q_6), .dp(1'b0));
  Button Interupt1 (.out(Interupt0_out[1]));
  LED led_2 (.in(ir_1_irwt[1]));
  Hex_Digit_Display hex_digit_display_5 (.value(Disp_q_4), .dp(1'b0));
  Hex_Digit_Display hex_digit_display_6 (.value(Disp_q_3), .dp(1'b0));
  Button Interupt2 (.out(Interupt0_out[2]));
  LED led_3 (.in(ir_1_irwt[2]));
  Multiplexer #(.select(2), .width(32), .enable("false")) multiplexer_4 (
    .in0(main_1_reg1), .in1({32{1'b0}}), .in2(32'h1), .in3(32'h1), .out(multiplexer_4_out),
    .sel(control_1_out_12));
  Hex_Digit_Display hex_digit_display_7 (.value(Disp_q), .dp(1'b0));
  Hex_Digit_Display hex_digit_display_8 (.value(Disp_q_2), .dp(1'b0));
  ROM #(.addrWidth(10), .dataWidth(32)) rom_1 (.addr(PC_q[9:0]), .data(rom_1_data), .sel(1'b1));
  Button Interupt3 (.out(Interupt0_out[3]));
  LED led_4 (.in(ir_1_irwt[3]));
  // Probe on counter_1_q
  Counter #(.width(32), .max('hffffffff)) counter_1 (.Q(counter_1_q), .clk(Clk));  // open: load, D, count, carry, clr
  IR ir_1 (
    .Rst(1'b0), .IEW(control_1_iew), .INMW(control_1_inmw), .IRSRC(Interupt0_out), .IRNUM(ir_1_irnum),
    .IR(ir_1_ir), .IRWT(ir_1_irwt), .Clk(Clk), .RegIn(multiplexer_4_out), .RegOut(ir_1_regout));
  Register #(.width(32), .trigger("high")) Disp (
    .D(main_1_a0_value), .en(1'b1),
    .Q({Disp_q_8, Disp_q_7, Disp_q_6, Disp_q_5, Disp_q_4, Disp_q_3, Disp_q_2, Disp_q}), .clk(control_1_disp),
    .clr(1'b0));
  InsAnalyse insanalyse_1 (
    .Ins(rom_1_data), .OP(insanalyse_1_op), .Rs(insanalyse_1_rs), .Rt(insanalyse_1_rt), .Rd(insanalyse_1_rd),
    .Shamt(insanalyse_1_shamt), .funct(insanalyse_1_funct), .Immediate16(insanalyse_1_immediate16),
    .Immediate26(insanalyse_1_immediate26));
  not not_1 (not_1_out, control_1_rfr1src);
  Clock clock_1 (.out(clock_1_out));
  Control control_1 (
    .Equal(alu_1_equal), .v0(main_1_v0_value), .OP(insanalyse_1_op), .funct(insanalyse_1_funct),
    .PCSrc(control_1_pcsrc), .PCAddSrc(control_1_pcaddsrc), .PCEn(control_1_pcen),
    .RFR1Src(control_1_rfr1src), .RFRWSrc(control_1_rfrwsrc),
    .RFDinSrc({control_1_rfdinsrc_2[2], control_1_rfdinsrc}), .RFWE(control_1_rfwe),
    .ALUYSrc(control_1_aluysrc), .ALUOP(control_1_aluop), .Halt(control_1_halt), .Disp(control_1_disp),
    .Judge(alu_1_result[0]), .ALUYSrc2(control_1_aluysrc2), .IR(ir_1_ir), .IRNUM(ir_1_irnum),
    .IRNUM_2(control_1_irnum_2), .DMAddSrc(control_1_dmaddsrc), .PCSrc2(control_1_pcsrc2),
    .Rs(insanalyse_1_rs), .IEW(control_1_iew), .INMW(control_1_inmw), .EPCEn(control_1_epcen),
    .DMWE(control_1_dmwe), .out_12(control_1_out_12), .Rd(insanalyse_1_rd), .EPCSrc(control_1_epcsrc));
  Multiplexer #(.width(5), .enable("false")) multiplexer_5 (
    .in0(insanalyse_1_rs), .in1(insanalyse_1_rt), .out(multiplexer_5_out), .sel(control_1_rfr1src));
  Multiplexer #(.width(5), .enable("false")) multiplexer_6 (
    .in0(insanalyse_1_rs), .in1(insanalyse_1_rt), .out(multiplexer_6_out), .sel(not_1_out));
  Multiplexer #(.select(2), .width(5), .enable("false")) multiplexer_7 (
    .in0(insanalyse_1_rt), .in1(insanalyse_1_rd), .in2({5{1'b1}}), .out(multiplexer_7_out),
    .sel(control_1_rfrwsrc));  // open: in3
  Multiplexer #(.select(2), .width(32), .enable("false")) multiplexer_8 (
    .in0(adder_2_out), .in1({ram_1_data_2, ram_1_data}), .in2(alu_1_result), .in3(bit_extender_5_out),
    .out(multiplexer_8_out), .sel(control_1_rfdinsrc));
  Multiplexer #(.width(32), .enable("false")) multiplexer_9 (
    .in0(ir_1_regout), .in1(EPC_q), .out(multiplexer_9_out), .sel(insanalyse_1_rd[0]));
  and and_1 (Clk, ~control_1_halt, clock_1_out);  // AND_Gate
  Multiplexer #(.width(32), .enable("false")) multiplexer_10 (
    .in0(multiplexer_8_out), .in1(multiplexer_9_out), .out(multiplexer_10_out), .sel(control_1_rfdinsrc_2[2]));
  regfile_cpu_main main_1 (
    .Reg1_num(multiplexer_5_out), .Reg2(multiplexer_6_out), .Write_Reg_num(multiplexer_7_out),
    .Din(multiplexer_10_out), .Write_Enable(control_1_rfwe), .Clock(Clk), .Reg1(main_1_reg1),
    .Reg2_2(main_1_reg2_2), .v0_Value(main_1_v0_value), .a0_Value(main_1_a0_value));  // open: s0_Value, s1_Value, s2_Value, ra_Value
  assign bit_extender_2_out = {{27{1'b0}}, insanalyse_1_shamt};  // Bit_Extender bit_extender_2
  assign bit_extender_3_out = {{16{insanalyse_1_immediate16[15]}}, insanalyse_1_immediate16};  // Bit_Extender bit_extender_3
  assign bit_extender_4_out = {{16{1'b0}}, insanalyse_1_immediate16};  // Bit_Extender bit_extender_4
  Multiplexer #(.select(2), .width(32), .enable("false")) multiplexer_11 (
    .in0(main_1_reg2_2), .in1(bit_extender_2_out), .in2(bit_extender_3_out), .in3(bit_extender_4_out),
    .out(multiplexer_11_out), .sel(control_1_aluysrc));
  Multiplexer #(.width(32), .disabled(0), .enable("false")) multiplexer_12 (
    .in0(multiplexer_11_out), .in1({32{1'b0}}), .out(multiplexer_12_out), .sel(control_1_aluysrc2));
  ALU alu_1 (
    .AluOP(control_1_aluop), .X(main_1_reg1), .Equal(alu_1_equal), .Result(alu_1_result),
    .Y(multiplexer_12_out));  // open: Signed_Overflow, Result_2, UnSigned_Overflow
  Multiplexer #(.width(10), .enable("false")) multiplexer_13 (
    .in0(control_1_irnum_2), .in1(alu_1_result[9:0]), .out(multiplexer_13_out), .sel(control_1_dmaddsrc));
  Multiplexer #(.width(32), .enable("false")) multiplexer_14 (
    .in0({32{1'b0}}), .in1(bit_extender_3_out), .out(multiplexer_14_out), .sel(control_1_pcaddsrc));
  RAM #(.addrWidth(10), .dataWidth(32), .bus("separate")) ram_1 (
    .addr(multiplexer_13_out), .din(main_1_reg2_2), .data({ram_1_data_2, ram_1_data}), .str(control_1_dmwe),
    .sel(1'b1), .clk(Clk), .ld(1'b1), .clr(1'b0));
  Adder #(.width(32)) adder_2 (.a(adder_1_out), .b(multiplexer_14_out), .out(adder_2_out), .cin(1'b0));  // open: cout
  assign bit_extender_5_out = {{16{ram_1_data[15]}}, ram_1_data};  // Bit_Extender bit_extender_5

  // Notes on the sheet:
  //   contents of rom_1 (hex, n*v repeats v):
  //   81000cd 8100005 8100037 8100069 810009b 27bdffff afa40000 27bdffff afa20000 27bdffff afb00000
  //   27bdffff afb10000 27bdffff 40114000 afb10000 27bdffff 40114800 afb10000 20100002 40904000 40104000
  //   36100001 40904000 20020001 20040000 c 2010000f 2004000f c 20110007 108100 2042020 c 2231ffff
  //   1620fffb 20100002 40904000 8fb10000 40914800 27bd0001 8fb10000 118842 118840 40914000 27bd0001
  //   8fb10000 27bd0001 8fb00000 27bd0001 8fa20000 27bd0001 8fa40000 27bd0001 42000018 27bdffff afa40000
  //   27bdffff afa20000 27bdffff afb00000 27bdffff afb10000 27bdffff 40114000 afb10000 27bdffff 40114800
  //   afb10000 20100006 40904000 40104000 36100001 40904000 20020001 20040000 c 20100001 20040001 c
  //   20110007 108100 2042020 c 2231ffff 1620fffb 20100006 40904000 8fb10000 40914800 27bd0001 8fb10000
  //   118842 118840 40914000 27bd0001 8fb10000 27bd0001 8fb00000 27bd0001 8fa20000 27bd0001 8fa40000
  //   27bd0001 42000018 27bdffff afa40000 27bdffff afa20000 27bdffff afb00000 27bdffff afb10000 27bdffff
  //   40114000 afb10000 27bdffff 40114800 afb10000 2010000e 40904000 40104000 36100001 40904000 20020001
  //   20040000 c 20100002 20040002 c 20110007 108100 2042020 c 2231ffff 1620fffb 2010000e 40904000
  //   8fb10000 40914800 27bd0001 8fb10000 118842 118840 40914000 27bd0001 8fb10000 27bd0001 8fb00000
  //   27bd0001 8fa20000 27bd0001 8fa40000 27bd0001 42000018 27bdffff afa40000 27bdffff afa20000 27bdffff
  //   afb00000 27bdffff afb10000 27bdffff 40114000 afb10000 27bdffff 40114800 afb10000 2010001e 40904000
  //   40104000 36100001 40904000 20020001 20040000 c 20100003 20040003 c 20110007 108100 2042020 c
  //   2231ffff 1620fffb 2010001e 40904000 8fb10000 40914800 27bd0001 8fb10000 118842 118840 40914000
  //   27bd0001 8fb10000 27bd0001 8fb00000 27bd0001 8fa20000 27bd0001 8fa40000 27bd0001 42000018 201d03ff
  //   20110004 afb10000 20110003 23bdffff afb10000 20110002 23bdffff afb10000 20110001 23bdffff afb10000
  //   20110001 40914000 81000dc 20110001 81000e1 20110001 20120002 20130003 81000e5 20110001 20120002
  //   20130003 81000e9 20110001 20120002 20130003 81000ed 20110001 20120002 20130003 c100194 20100001
  //   20110001 118fc0 112020 20020022 c 118882 12200001 81000f1 112020 20020022 c 20110001 118880 112020
  //   20020022 c 12200001 81000fb 20110001 118fc0 112020 20020022 c 1188c3 112020 20020022 c 118903 112020
  //   20020022 c 118903 112020 20020022 c 118903 112020 20020022 c 118903 112020 20020022 c 118903 112020
  //   20020022 c 118903 112020 20020022 c 118903 112020 20020022 c 20100001 109fc0 139fc3 8021 2012000c
  //   24160003 26100001 3210000f 20080008 20090001 139900 2709825 132020 20020022 c 1094022 1500fff9
  //   22100001 2018000f 2188024 108700 20080008 20090001 139902 2709825 132021 20020022 c 1094022 1500fff9
  //   108702 2c9b022 12c00001 810012c 4020 1084027 84400 3508ffff 82021 20020022 c 2010ffff 20110000
  //   ae300000 22100001 22310004 ae300000 22100001 22310004 ae300000 22100001 22310004 ae300000 22100001
  //   22310004 ae300000 22100001 22310004 ae300000 22100001 22310004 ae300000 22100001 22310004 ae300000
  //   22100001 22310004 ae300000 22100001 22310004 ae300000 22100001 22310004 ae300000 22100001 22310004
  //   ae300000 22100001 22310004 ae300000 22100001 22310004 ae300000 22100001 22310004 ae300000 22100001
  //   22310004 ae300000 22100001 22310004 22100001 8020 2011003c 8e130000 8e340000 274402a 11000002
  //   ae330000 ae140000 2231fffc 1611fff8 102020 20020022 c 22100004 2011003c 1611fff2 2002000a c 20100000
  //   22100001 102020 20020022 c 22100002 102020 20020022 c 22100003 102020 20020022 c 22100004 102020
  //   20020022 c 22100005 102020 20020022 c 22100006 102020 20020022 c 22100007 102020 20020022 c 22100008
  //   102020 20020022 20020022 c 3e00008
endmodule

module InsAnalyse (
  input  [31:0] Ins,
  output [5:0] OP,
  output [4:0] Rs,
  output [4:0] Rt,
  output [4:0] Rd,
  output [4:0] Shamt,
  output [5:0] funct,
  output [15:0] Immediate16,
  output [25:0] Immediate26
);


  assign funct = Ins[5:0];
  assign Immediate16 = Ins[15:0];
  assign Immediate26 = Ins[25:0];
  assign OP = Ins[31:26];
  assign Rd = Ins[15:11];
  assign Rs = Ins[25:21];
  assign Rt = Ins[20:16];
  assign Shamt = Ins[10:6];
endmodule

module Control (
  input  Equal,
  input  Judge,
  input  IR,
  input  [1:0] IRNUM,
  input  [4:0] Rs,
  input  [4:0] Rd,
  input  [31:0] v0,
  input  [5:0] OP,
  input  [5:0] funct,
  output DMAddSrc,
  output [9:0] IRNUM_2,
  output [1:0] out_12,
  output [1:0] PCSrc2,
  output EPCEn,
  output EPCSrc,
  output [1:0] PCSrc,
  output PCAddSrc,
  output PCEn,
  output RFR1Src,
  output [1:0] RFRWSrc,
  output [2:0] RFDinSrc,
  output RFWE,
  output [1:0] ALUYSrc,
  output ALUYSrc2,
  output [3:0] ALUOP,
  output DMWE,
  output IEW,
  output INMW,
  output Halt,
  output Disp
);

  wire add, addi, addiu, addu, \and , and_4_out, and_5_out, and_6_out, and_7_out, and_8_out, and_9_out, andi,
       beq, bne, decoder_1_out0, decoder_1_out16, decoder_2_out0, decoder_2_out1, decoder_5_out0,
       decoder_6_out0, decoder_6_out1, j, jr, lh, lw, mtc0, \nor , nor_2_out, not_1_out, not_2_out,
       not_3_out, \or , ori, sll, sllv, slt, slti, sltu, sra, srl, srlv, sub, sw, syscall, v0_10;
  wire [7:0] or_8_out;
  wire [31:0] subtractor_1_out;

  Decoder #(.select(5), .disabled(0)) decoder_1 (
    .out0(decoder_1_out0), .out1(ALUYSrc2), .out2(j), .out3(RFRWSrc[1]), .out4(beq), .out5(bne), .out8(addi),
    .out9(addiu), .out10(slti), .out12(andi), .out13(ori), .out16(decoder_1_out16), .sel(OP[4:0]),
    .en(decoder_2_out0));  // open: out6, out7, out11, out14, out15, out17, out18, out19, out20, out21, out22, out23, out24, out25, out26, out27, out28, out29, out30, out31
  Decoder #(.enable("false")) decoder_2 (.out0(decoder_2_out0), .out1(decoder_2_out1), .sel(OP[5]));
  Decoder #(.select(5), .disabled(0)) decoder_3 (
    .out1(lh), .out3(lw), .out11(sw), .sel(OP[4:0]), .en(decoder_2_out1));  // open: out0, out2, out4, out5, out6, out7, out8, out9, out10, out12, out13, out14, out15, out16, out17, out18, out19, out20, out21, out22, out23, out24, out25, out26, out27, out28, out29, out30, out31
  not not_1 (not_1_out, Judge);
  or or_1 (PCAddSrc, beq, bne, ALUYSrc2);
  nor nor_1 (RFDinSrc[1], lw, RFRWSrc[1]);
  or or_2 (RFDinSrc[0], lw, lh);
  and and_1 (DMWE, sw, ~IR);  // AND_Gate
  or or_3 (IEW, INMW, IR, out_12[1]);
  and and_2 (Halt, syscall, v0_10);
  and and_3 (Disp, syscall, ~v0_10);  // AND_Gate
  Subtractor #(.width(32)) subtractor_1 (.a(v0), .b(32'ha), .out(subtractor_1_out));  // open: bin, bout
  not not_2 (not_2_out, Equal);
  and and_4 (and_4_out, beq, Equal);
  and and_5 (and_5_out, bne, not_3_out);
  not not_3 (not_3_out, Equal);
  or or_4 (RFR1Src, sll, sra, srl, sllv, srlv, mtc0);
  or or_5 (ALUYSrc[1], addi, addiu, andi, ori, lw, sw, slti, lh);
  or or_6 (ALUYSrc[0], andi, sll, sra, srl, ori);
  or or_7 (ALUOP[3], \or , ori, \nor , slt, slti, sltu, ALUYSrc2);
  assign or_8_out = subtractor_1_out[7:0] | subtractor_1_out[15:8] | subtractor_1_out[23:16] | subtractor_1_out[31:24];  // OR_Gate or_8, 8 bits wide
  and and_6 (and_6_out, beq, Equal);
  and and_7 (and_7_out, bne, not_2_out);
  and and_8 (and_8_out, ALUYSrc2, not_1_out);
  and and_9 (and_9_out, ALUYSrc2, not_1_out);
  nor nor_2 (nor_2_out, sw, beq, bne, j, jr, syscall, ALUYSrc2, mtc0, out_12[1]);
  or or_9 (ALUOP[1], \and , andi, srl, sub, \nor , beq, bne, slt, slti, srlv, ALUYSrc2);
  or or_10 (PCSrc[1], and_6_out, and_7_out, j, RFRWSrc[1], and_8_out);
  nor nor_3 (PCSrc[0], and_9_out, and_4_out, and_5_out, jr);
  or or_11 (RFRWSrc[0], add, addu, \and , sll, sra, srl, sub, \or , \nor , slt, sltu, sllv, srlv);
  and and_10 (RFWE, nor_2_out, ~IR);  // AND_Gate
  or or_12 (ALUOP[2], add, addi, addiu, addu, \and , andi, sub, lw, sw, beq, bne, sltu, lh);
  or or_13 (ALUOP[0], add, addi, addiu, addu, \and , andi, sra, lw, sw, slt, slti, lh, ALUYSrc2);
  nor nor_4 (v0_10, or_8_out[0], or_8_out[1], or_8_out[2], or_8_out[3], or_8_out[4], or_8_out[5], or_8_out[6], or_8_out[7]);
  Decoder #(.disabled(0)) decoder_4 (.out0(RFDinSrc[2]), .out1(mtc0), .sel(Rs[2]), .en(decoder_5_out0));
  Decoder #(.disabled(0)) decoder_5 (.out0(decoder_5_out0), .out1(out_12[1]), .sel(funct[4]), .en(decoder_1_out16));
  Decoder #(.disabled(0)) decoder_6 (.out0(decoder_6_out0), .out1(decoder_6_out1), .sel(funct[5]), .en(decoder_1_out0));
  not not_4 (DMAddSrc, IR);
  Decoder #(.disabled(0)) decoder_7 (.out0(INMW), .out1(EPCSrc), .sel(Rd[0]), .en(mtc0));
  Decoder #(.select(5), .disabled(0)) decoder_8 (
    .out0(sll), .out2(srl), .out3(sra), .out4(sllv), .out6(srlv), .out8(jr), .out12(syscall),
    .sel(funct[4:0]), .en(decoder_6_out0));  // open: out1, out5, out7, out9, out10, out11, out13, out14, out15, out16, out17, out18, out19, out20, out21, out22, out23, out24, out25, out26, out27, out28, out29, out30, out31
  Decoder #(.select(5), .disabled(0)) decoder_9 (
    .out0(add), .out1(addu), .out2(sub), .out4(\and ), .out5(\or ), .out7(\nor ), .out10(slt), .out11(sltu),
    .sel(funct[4:0]), .en(decoder_6_out1));  // open: out3, out6, out8, out9, out12, out13, out14, out15, out16, out17, out18, out19, out20, out21, out22, out23, out24, out25, out26, out27, out28, out29, out30, out31
  or or_14 (EPCEn, IR, EPCSrc);

  assign IRNUM_2 = {{8{1'b1}}, IRNUM};
  assign out_12[0] = IR;
  assign PCEn = 1'b1;
  assign PCSrc2 = {IR, out_12[1]};

  // Other names for the same wires on the sheet: bgez = ALUYSrc2; mtc00 = INMW; mtc01 = EPCSrc; eret = out_12[1];
  //   Rd_t = Rd[0]; mfc0 = RFDinSrc[2]; jal = RFRWSrc[1]; Rs_t = Rs[2]
endmodule

// INTR
module IR (
  input  Clk,
  input  Rst,
  input  [31:0] RegIn,
  input  IEW,
  input  INMW,
  input  [3:0] IRSRC,
  output [1:0] IRNUM,
  output IR,
  output [31:0] RegOut,
  output [3:0] IRWT
);

  wire and_1_out, and_2_out, and_3_out, and_4_out, and_5_out, and_6_out, and_7_out, and_8_out, and_9_out,
       d_ff_1_q, d_ff_2_q, d_ff_3_q, d_ff_4_q, d_ff_5_q, d_ff_6_q, d_ff_7_q, d_ff_8_q, decoder_1_out0,
       decoder_1_out1, decoder_1_out2, decoder_1_out3, priority_encoder_1_en_out, priority_encoder_1_gs;

  Decoder #(.select(2), .disabled(0)) decoder_1 (
    .out0(decoder_1_out0), .out1(decoder_1_out1), .out2(decoder_1_out2), .out3(decoder_1_out3), .sel(IRNUM),
    .en(and_9_out));
  D_Flip_Flop d_ff_1 (.clk(IRSRC[0]), .D(1'b1), .Q(d_ff_1_q), .reset(decoder_1_out0));  // open: Qn, preset, en
  D_Flip_Flop d_ff_2 (.clk(IRSRC[1]), .D(1'b1), .Q(d_ff_2_q), .reset(decoder_1_out1));  // open: Qn, preset, en
  D_Flip_Flop d_ff_3 (.clk(IRSRC[2]), .D(1'b1), .Q(d_ff_3_q), .reset(decoder_1_out2));  // open: Qn, preset, en
  D_Flip_Flop d_ff_4 (.clk(IRSRC[3]), .D(1'b1), .Q(d_ff_4_q), .reset(decoder_1_out3));  // open: Qn, preset, en
  or or_1 (IRWT[0], d_ff_1_q, decoder_1_out0);
  or or_2 (IRWT[1], d_ff_2_q, decoder_1_out1);
  or or_3 (IRWT[2], d_ff_3_q, decoder_1_out2);
  or or_4 (IRWT[3], d_ff_4_q, decoder_1_out3);
  and and_1 (and_1_out, d_ff_1_q, ~Rst);  // AND_Gate
  and and_2 (and_2_out, d_ff_2_q, ~Rst);  // AND_Gate
  and and_3 (and_3_out, d_ff_3_q, ~Rst);  // AND_Gate
  and and_4 (and_4_out, d_ff_4_q, ~Rst);  // AND_Gate
  Register #(.width(1)) register_1 (.D(RegIn[1]), .en(INMW), .Q(RegOut[1]), .clk(Clk), .clr(Rst));
  Register #(.width(1)) register_2 (.D(RegIn[2]), .en(INMW), .Q(RegOut[2]), .clk(Clk), .clr(Rst));
  Register #(.width(1)) register_3 (.D(RegIn[3]), .en(INMW), .Q(RegOut[3]), .clk(Clk), .clr(Rst));
  Register #(.width(1)) register_4 (.D(RegIn[4]), .en(INMW), .Q(RegOut[4]), .clk(Clk), .clr(Rst));
  D_Flip_Flop d_ff_5 (.clk(Clk), .D(and_1_out), .Q(d_ff_5_q));  // open: Qn, preset, en, reset
  D_Flip_Flop d_ff_6 (.clk(Clk), .D(and_2_out), .Q(d_ff_6_q));  // open: Qn, preset, en, reset
  D_Flip_Flop d_ff_7 (.clk(Clk), .D(and_3_out), .Q(d_ff_7_q));  // open: Qn, preset, en, reset
  D_Flip_Flop d_ff_8 (.clk(Clk), .D(and_4_out), .Q(d_ff_8_q));  // open: Qn, preset, en, reset
  and and_5 (and_5_out, d_ff_5_q, ~RegOut[1]);  // AND_Gate
  and and_6 (and_6_out, d_ff_6_q, ~RegOut[2]);  // AND_Gate
  and and_7 (and_7_out, d_ff_7_q, ~RegOut[3]);  // AND_Gate
  and and_8 (and_8_out, d_ff_8_q, ~RegOut[4]);  // AND_Gate
  and and_9 (and_9_out, ~priority_encoder_1_en_out, RegOut[0]);  // AND_Gate
  Priority_Encoder #(.select(2), .disabled(0)) priority_encoder_1 (
    .in0(and_5_out), .in1(and_6_out), .in2(and_7_out), .in3(and_8_out), .out(IRNUM),
    .gs(priority_encoder_1_gs), .en_out(priority_encoder_1_en_out), .en_in(1'b1));
  Register #(.width(1)) register_5 (.D(RegIn[0]), .en(IEW), .Q(RegOut[0]), .clk(Clk), .clr(Rst));
  and and_10 (IR, priority_encoder_1_gs, RegOut[0]);

  assign RegOut[31:5] = {27{1'b0}};

  // Other names for the same wires on the sheet: IR0 = IRSRC[0]; IR1 = IRSRC[1]; IR2 = IRSRC[2]; IR3 = IRSRC[3];
  //   IE = RegIn[0]; INM0 = RegIn[1]; INM1 = RegIn[2]; INM2 = RegIn[3]; INM3 = RegIn[4]; IEOut = RegOut[0];
  //   INM0Out = RegOut[1]; INM1Out = RegOut[2]; INM2Out = RegOut[3]; INM3Out = RegOut[4]
endmodule
