// Logisim project regfile-5-stage-cpu-bubble.circ as structural Verilog: 2 circuits, main circuit main
module main (
  input  [4:0] Reg1_num,
  input  [4:0] Reg2,
  input  [4:0] Write_Reg_num,
  input  [31:0] Din,
  input  Write_Enable,
  input  Clock,
  output [31:0] Reg1,
  output [31:0] s0_Value,
  output [31:0] s1_Value,
  output [31:0] s2_Value,
  output [31:0] ra_Value,
  output [31:0] v0_Value,
  output [31:0] a0_Value,
  output [31:0] Reg2_2
);

  wire [7:0] decoder_1_out0, decoder_1_out8, decoder_1_out16, decoder_1_out24;
  wire [31:0] r0_q, r1_q, r3_q, r5_q, r6_q, r7_q, r8_q, r9_q, r10_q, r11_q, r12_q, r13_q, r14_q, r15_q,
       r19_q, r20_q, r21_q, r22_q, r23_q, r24_q, r25_q, r26_q, r27_q, r28_q, r29_q, r30_q;

  Decoder #(.select(5), .disabled(0)) decoder_1 (
    .out0(decoder_1_out0[0]), .out1(decoder_1_out0[1]), .out2(decoder_1_out0[2]), .out3(decoder_1_out0[3]),
    .out4(decoder_1_out0[4]), .out5(decoder_1_out0[5]), .out6(decoder_1_out0[6]), .out7(decoder_1_out0[7]),
    .out8(decoder_1_out8[0]), .out9(decoder_1_out8[1]), .out10(decoder_1_out8[2]), .out11(decoder_1_out8[3]),
    .out12(decoder_1_out8[4]), .out13(decoder_1_out8[5]), .out14(decoder_1_out8[6]),
    .out15(decoder_1_out8[7]), .out16(decoder_1_out16[0]), .out17(decoder_1_out16[1]),
    .out18(decoder_1_out16[2]), .out19(decoder_1_out16[3]), .out20(decoder_1_out16[4]),
    .out21(decoder_1_out16[5]), .out22(decoder_1_out16[6]), .out23(decoder_1_out16[7]),
    .out24(decoder_1_out24[0]), .out25(decoder_1_out24[1]), .out26(decoder_1_out24[2]),
    .out27(decoder_1_out24[3]), .out28(decoder_1_out24[4]), .out29(decoder_1_out24[5]),
    .out30(decoder_1_out24[6]), .out31(decoder_1_out24[7]), .sel(Write_Reg_num), .en(Write_Enable));
  Register #(.width(32), .trigger("falling")) r1 (.D(Din), .en(decoder_1_out0[1]), .Q(r1_q), .clk(Clock), .clr(1'b0));
  Register #(.width(32), .trigger("falling")) r0 (.D(Din), .en(decoder_1_out0[0]), .Q(r0_q), .clk(Clock), .clr(1'b1));
  Register #(.width(32), .trigger("falling")) r9 (.D(Din), .en(decoder_1_out8[1]), .Q(r9_q), .clk(Clock), .clr(1'b0));
  Register #(.width(32), .trigger("falling")) r8 (.D(Din), .en(decoder_1_out8[0]), .Q(r8_q), .clk(Clock), .clr(1'b0));
  Register #(.width(32), .trigger("falling")) r16 (
    .D(Din), .en(decoder_1_out16[0]), .Q(s0_Value), .clk(Clock), .clr(1'b0));
  Register #(.width(32), .trigger("falling")) r17 (
    .D(Din), .en(decoder_1_out16[1]), .Q(s1_Value), .clk(Clock), .clr(1'b0));
  Register #(.width(32), .trigger("falling")) r25 (
    .D(Din), .en(decoder_1_out24[1]), .Q(r25_q), .clk(Clock), .clr(1'b0));
  Register #(.width(32), .trigger("falling")) r24 (
    .D(Din), .en(decoder_1_out24[0]), .Q(r24_q), .clk(Clock), .clr(1'b0));
  Register #(.width(32), .trigger("falling")) r2 (
    .D(Din), .en(decoder_1_out0[2]), .Q(v0_Value), .clk(Clock), .clr(1'b0));
  Register #(.width(32), .trigger("falling")) r10 (.D(Din), .en(decoder_1_out8[2]), .Q(r10_q), .clk(Clock), .clr(1'b0));
  Register #(.width(32), .trigger("falling")) r18 (
    .D(Din), .en(decoder_1_out16[2]), .Q(s2_Value), .clk(Clock), .clr(1'b0));
  Register #(.width(32), .trigger("falling")) r26 (
    .D(Din), .en(decoder_1_out24[2]), .Q(r26_q), .clk(Clock), .clr(1'b0));
  Register #(.width(32), .trigger("falling")) r3 (.D(Din), .en(decoder_1_out0[3]), .Q(r3_q), .clk(Clock), .clr(1'b0));
  Register #(.width(32), .trigger("falling")) r11 (.D(Din), .en(decoder_1_out8[3]), .Q(r11_q), .clk(Clock), .clr(1'b0));
  Register #(.width(32), .trigger("falling")) r19 (
    .D(Din), .en(decoder_1_out16[3]), .Q(r19_q), .clk(Clock), .clr(1'b0));
  Register #(.width(32), .trigger("falling")) r27 (
    .D(Din), .en(decoder_1_out24[3]), .Q(r27_q), .clk(Clock), .clr(1'b0));
  Register #(.width(32), .trigger("falling")) r4 (
    .D(Din), .en(decoder_1_out0[4]), .Q(a0_Value), .clk(Clock), .clr(1'b0));
  Register #(.width(32), .trigger("falling")) r12 (.D(Din), .en(decoder_1_out8[4]), .Q(r12_q), .clk(Clock), .clr(1'b0));
  Register #(.width(32), .trigger("falling")) r20 (
    .D(Din), .en(decoder_1_out16[4]), .Q(r20_q), .clk(Clock), .clr(1'b0));
  Register #(.width(32), .trigger("falling")) r28 (
    .D(Din), .en(decoder_1_out24[4]), .Q(r28_q), .clk(Clock), .clr(1'b0));
  Register #(.width(32), .trigger("falling")) r5 (.D(Din), .en(decoder_1_out0[5]), .Q(r5_q), .clk(Clock), .clr(1'b0));
  Register #(.width(32), .trigger("falling")) r13 (.D(Din), .en(decoder_1_out8[5]), .Q(r13_q), .clk(Clock), .clr(1'b0));
  Register #(.width(32), .trigger("falling")) r21 (
    .D(Din), .en(decoder_1_out16[5]), .Q(r21_q), .clk(Clock), .clr(1'b0));
  Register #(.width(32), .trigger("falling")) r29 (
    .D(Din), .en(decoder_1_out24[5]), .Q(r29_q), .clk(Clock), .clr(1'b0));
  Register #(.width(32), .trigger("falling")) r6 (.D(Din), .en(decoder_1_out0[6]), .Q(r6_q), .clk(Clock), .clr(1'b0));
  Register #(.width(32), .trigger("falling")) r14 (.D(Din), .en(decoder_1_out8[6]), .Q(r14_q), .clk(Clock), .clr(1'b0));
  Register #(.width(32), .trigger("falling")) r22 (
    .D(Din), .en(decoder_1_out16[6]), .Q(r22_q), .clk(Clock), .clr(1'b0));
  Register #(.width(32), .trigger("falling")) r30 (
    .D(Din), .en(decoder_1_out24[6]), .Q(r30_q), .clk(Clock), .clr(1'b0));
  Register #(.width(32), .trigger("falling")) r7 (.D(Din), .en(decoder_1_out0[7]), .Q(r7_q), .clk(Clock), .clr(1'b0));
  Register #(.width(32), .trigger("falling")) r15 (.D(Din), .en(decoder_1_out8[7]), .Q(r15_q), .clk(Clock), .clr(1'b0));
  Register #(.width(32), .trigger("falling")) r23 (
    .D(Din), .en(decoder_1_out16[7]), .Q(r23_q), .clk(Clock), .clr(1'b0));
  Register #(.width(32), .trigger("falling")) r31 (
    .D(Din), .en(decoder_1_out24[7]), .Q(ra_Value), .clk(Clock), .clr(1'b0));
  Multiplexer #(.select(5), .width(32), .enable("false")) multiplexer_1 (
    .in0(r0_q), .in1(r1_q), .in2(v0_Value), .in3(r3_q), .in4(a0_Value), .in5(r5_q), .in6(r6_q), .in7(r7_q),
    .in8(r8_q), .in9(r9_q), .in10(r10_q), .in11(r11_q), .in12(r12_q), .in13(r13_q), .in14(r14_q),
    .in15(r15_q), .in16(s0_Value), .in17(s1_Value), .in18(s2_Value), .in19(r19_q), .in20(r20_q),
    .in21(r21_q), .in22(r22_q), .in23(r23_q), .in24(r24_q), .in25(r25_q), .in26(r26_q), .in27(r27_q),
    .in28(r28_q), .in29(r29_q), .in30(r30_q), .in31(ra_Value), .out(Reg1), .sel(Reg1_num));
  Multiplexer #(.select(5), .width(32), .enable("false")) multiplexer_2 (
    .in0(r0_q), .in1(r1_q), .in2(v0_Value), .in3(r3_q), .in4(a0_Value), .in5(r5_q), .in6(r6_q), .in7(r7_q),
    .in8(r8_q), .in9(r9_q), .in10(r10_q), .in11(r11_q), .in12(r12_q), .in13(r13_q), .in14(r14_q),
    .in15(r15_q), .in16(s0_Value), .in17(s1_Value), .in18(s2_Value), .in19(r19_q), .in20(r20_q),
    .in21(r21_q), .in22(r22_q), .in23(r23_q), .in24(r24_q), .in25(r25_q), .in26(r26_q), .in27(r27_q),
    .in28(r28_q), .in29(r29_q), .in30(r30_q), .in31(ra_Value), .out(Reg2_2), .sel(Reg2));

  // Other names for the same wires on the sheet: a0[31:0] = a0_Value; clk = Clock; ra[31:0] = ra_Value;
  //   reg2_num[4:0] = Reg2; reg2_t[31:0] = Reg2_2; s0[31:0] = s0_Value; s1[31:0] = s1_Value; s2[31:0] = s2_Value;
  //   v0[31:0] = v0_Value; WE = Write_Enable; write_data[31:0] = Din

  // Notes on the sheet:
  //   输入引脚
  //   输出引脚
  //   Debug引脚，便于观测寄存器值
  //   请勿修改引脚以及封装，直接使用隧道连接电路
endmodule

module test (
);

  wire undriven;

  main main_1 (.Clock(undriven));  // open: Reg1_num, Reg2, Write_Reg_num, Din, Write_Enable, Reg1, Reg2_2, s0_Value, s1_Value, s2_Value, ra_Value, v0_Value, a0_Value
endmodule
